// Logisim project cpu24_DBP.circ as structural Verilog: 20 circuits, main circuit ◇单周期MIPS
module \单周期MIPS  (
);

  wire and_3_out, and_7_out, Beq, beq_suc, BLTZ, bltz_suc, Bne, bne_suc, CLK, clkne, comparator_2_eq, equal,
       Go, GoCancel__on_fall_q, GoPressed_q, GoUsed_q, JAL, JMP, JR, less, not_1_out, or_1_out, or_2_out,
       or_3_out, RST, SB, SignedExt, SV, syscall, Syscall10, Syscall34, \硬布线控制器_1_alu_src ,
       \硬布线控制器_1_memtoreg , \硬布线控制器_1_memwrite , \硬布线控制器_1_regdst , \硬布线控制器_1_regwrite ;
  wire [1:0] temp_1_sel0;
  wire [3:0] decoder_1_out0, multiplexer_12_out, \硬布线控制器_1_alu_op ;
  wire [4:0] mips_regifile_1_r1, multiplexer_3_out, multiplexer_4_out, multiplexer_5_out, multiplexer_6_out,
       multiplexer_11_out, rom_1_data_3, shifter_2_out;
  wire [15:0] \总周期数 , \无条件分支数 , \条件分支成功数 ;
  wire [25:0] rom_1_data;
  wire [31:0] adder_1_out, adder_2_out, bit_extender_1_out, LedData, mips_ram_1_p7, mips_regifile_1_r2,
       multiplexer_1_out, multiplexer_2_out, multiplexer_7_out, multiplexer_8_out, multiplexer_9_out,
       multiplexer_10_out, multiplexer_13_out, PC_q, shifter_1_out, shifter_3_out;
  wire [31:1] mips_alu_1_result;
  wire [31:5] mips_regifile_1_r1_2;
  wire [31:26] rom_1_data_2;

  Button \u_总复位  (.out(RST));
  Button \u_继续运行  (.out(Go));
  Clock clock_1 (.out(CLK));
  Counter #(.width(16), .max('hffff)) counter_1 (
    .count(not_1_out), .Q(\总周期数 ), .clk(CLK), .clr(RST));  // open: load, D, carry
  not not_1 (not_1_out, clkne);
  Multiplexer #(.select(2), .width(32), .enable("false")) multiplexer_1 (
    .in0({mips_regifile_1_r1_2, mips_regifile_1_r1}), .in1(adder_1_out), .in2(adder_2_out),
    .in3({PC_q[31:28], rom_1_data[25:11], rom_1_data_3, rom_1_data[5:0], 2'b00}), .out(multiplexer_1_out),
    .sel(temp_1_sel0));
  Hex_Digit_Display hex_digit_display_1 (.value(LedData[31:28]));  // open: dp
  Hex_Digit_Display hex_digit_display_2 (.value(LedData[27:24]));  // open: dp
  Register #(.width(32)) PC (.D(multiplexer_1_out), .Q(PC_q), .clk(CLK), .clr(RST));  // open: en
  Multiplexer #(.width(32), .enable("false")) multiplexer_2 (
    .in0(32'h4), .in1({32{1'b0}}), .out(multiplexer_2_out), .sel(clkne));
  and and_1 (clkne, syscall, or_1_out);
  Hex_Digit_Display hex_digit_display_3 (.value(LedData[23:20]));  // open: dp
  Hex_Digit_Display hex_digit_display_4 (.value(LedData[19:16]));  // open: dp
  temp temp_1 (
    .jmp(JMP), .jr(JR), .jal(JAL), .beq(beq_suc), .bne(bne_suc), .bltz(bltz_suc), .sel1(temp_1_sel0[1]),
    .sel0(temp_1_sel0[0]));
  Adder #(.width(32)) adder_1 (.a(PC_q), .b(multiplexer_2_out), .out(adder_1_out));  // open: cin, cout
  Adder #(.width(32)) adder_2 (.a(adder_1_out), .b(shifter_1_out), .out(adder_2_out));  // open: cin, cout
  or or_1 (or_1_out, and_3_out, Syscall10);
  Comparator #(.width(32), .mode("unsigned")) comparator_1 (
    .a(32'ha), .b(mips_regifile_1_r2), .eq(Syscall10));  // open: gt, lt
  Comparator #(.width(32), .mode("unsigned")) comparator_2 (
    .a(32'h22), .b(mips_regifile_1_r2), .eq(comparator_2_eq));  // open: gt, lt
  and and_2 (Syscall34, comparator_2_eq, syscall);
  Hex_Digit_Display hex_digit_display_5 (.value(LedData[11:8]));  // open: dp
  Hex_Digit_Display hex_digit_display_6 (.value(LedData[15:12]));  // open: dp
  ROM #(.addrWidth(10), .dataWidth(32)) rom_1 (
    .addr(PC_q[11:2]), .data({rom_1_data_2, rom_1_data[25:11], rom_1_data_3, rom_1_data[5:0]}));  // open: sel
  and and_3 (and_3_out, ~comparator_2_eq, ~GoPressed_q);  // AND_Gate
  Register #(.width(32)) register_1 (
    .D({mips_regifile_1_r1_2, mips_regifile_1_r1}), .en(Syscall34), .Q(LedData), .clk(CLK), .clr(RST));
  Hex_Digit_Display hex_digit_display_7 (.value(LedData[3:0]));  // open: dp
  Hex_Digit_Display hex_digit_display_8 (.value(LedData[7:4]));  // open: dp
  and and_4 (beq_suc, Beq, equal);
  and and_5 (bne_suc, Bne, ~equal);  // AND_Gate
  and and_6 (bltz_suc, BLTZ, less);
  Shifter #(.width(32)) shifter_1 (.in(bit_extender_1_out), .\dist (5'b00010), .out(shifter_1_out));
  D_Flip_Flop GoPressed (.clk(Go), .D(1'b1), .Q(GoPressed_q), .reset(GoCancel__on_fall_q));  // open: Qn, preset, en
  // Probe on \总周期数 
  // Probe on \无条件分支数 
  // Probe on \条件分支成功数 
  D_Flip_Flop GoUsed (.clk(CLK), .D(GoPressed_q), .Q(GoUsed_q), .reset(GoCancel__on_fall_q));  // open: Qn, preset, en
  \硬布线控制器  \u_硬布线控制器_1  (
    .Func(rom_1_data[5:0]), .OP(rom_1_data_2), .ALU_OP(\硬布线控制器_1_alu_op ), .MemToReg(\硬布线控制器_1_memtoreg ),
    .MemWrite(\硬布线控制器_1_memwrite ), .ALU_SRC(\硬布线控制器_1_alu_src ), .RegWrite(\硬布线控制器_1_regwrite ),
    .SysCALL(syscall), .SignedExt(SignedExt), .RegDst(\硬布线控制器_1_regdst ), .JR(JR), .JMP(JMP), .Beq(Beq),
    .JAL(JAL), .Bne(Bne), .BLTZ(BLTZ), .SB(SB), .SV(SV));
  Multiplexer #(.width(5), .enable("false")) multiplexer_3 (
    .in0(rom_1_data[25:21]), .in1(5'b00100), .out(multiplexer_3_out), .sel(Syscall34));
  Multiplexer #(.width(5), .enable("false")) multiplexer_4 (
    .in0(rom_1_data[20:16]), .in1(5'b00010), .out(multiplexer_4_out), .sel(syscall));
  Multiplexer #(.width(5), .enable("false")) multiplexer_5 (
    .in0(rom_1_data[20:16]), .in1(rom_1_data[15:11]), .out(multiplexer_5_out), .sel(\硬布线控制器_1_regdst ));
  Multiplexer #(.width(5), .enable("false")) multiplexer_6 (
    .in0(multiplexer_5_out), .in1({5{1'b1}}), .out(multiplexer_6_out), .sel(JAL));
  and and_7 (and_7_out, SignedExt, rom_1_data[15]);
  Multiplexer #(.width(32), .enable("false")) multiplexer_7 (
    .in0(multiplexer_13_out), .in1(adder_1_out), .out(multiplexer_7_out), .sel(JAL));
  assign bit_extender_1_out = {{16{and_7_out}}, {rom_1_data[15:11], rom_1_data_3, rom_1_data[5:0]}};  // Bit_Extender bit_extender_1
  D_Flip_Flop #(.trigger("falling")) GoCancel__on_fall (
    .clk(CLK), .D(GoUsed_q), .Q(GoCancel__on_fall_q), .reset(RST));  // open: Qn, preset, en
  or or_2 (or_2_out, JAL, JR, JMP);
  MIPS_Regifile mips_regifile_1 (
    .Din(multiplexer_7_out), .Clk(CLK), .R1({mips_regifile_1_r1_2, mips_regifile_1_r1}),
    .R2(mips_regifile_1_r2), .WE(\硬布线控制器_1_regwrite ), .W_num(multiplexer_6_out), .R1_num(multiplexer_3_out),
    .R2_num(multiplexer_4_out));
  Shifter #(.width(5)) shifter_2 (.in({3'b000, mips_alu_1_result[1], less}), .\dist (3'b011), .out(shifter_2_out));
  Counter #(.width(16), .max('hffff)) counter_2 (
    .count(or_2_out), .Q(\无条件分支数 ), .clk(CLK), .clr(RST));  // open: load, D, carry
  Multiplexer #(.width(32), .enable("false")) multiplexer_8 (
    .in0(multiplexer_9_out), .in1({32{1'b0}}), .out(multiplexer_8_out), .sel(BLTZ));
  Multiplexer #(.width(32), .enable("false")) multiplexer_9 (
    .in0(mips_regifile_1_r2), .in1(bit_extender_1_out), .out(multiplexer_9_out), .sel(\硬布线控制器_1_alu_src ));
  Multiplexer #(.width(32), .enable("false")) multiplexer_10 (
    .in0(mips_regifile_1_r2), .in1(shifter_3_out), .out(multiplexer_10_out), .sel(SB));
  Shifter #(.width(32)) shifter_3 (.in(mips_regifile_1_r2), .\dist (shifter_2_out), .out(shifter_3_out));
  MIPS_ALU mips_alu_1 (
    .X({mips_regifile_1_r1_2, mips_regifile_1_r1}), .Y(multiplexer_8_out), .AluOP(\硬布线控制器_1_alu_op ),
    .Equal(equal), .Result({mips_alu_1_result, less}), .shamt(multiplexer_11_out));  // open: Result_2
  Multiplexer #(.width(5), .enable("false")) multiplexer_11 (
    .in0(rom_1_data_3), .in1(mips_regifile_1_r1), .out(multiplexer_11_out), .sel(SV));
  Decoder #(.select(2)) decoder_1 (
    .out0(decoder_1_out0[0]), .out1(decoder_1_out0[1]), .out2(decoder_1_out0[2]), .out3(decoder_1_out0[3]),
    .sel({mips_alu_1_result[1], less}));  // open: en
  or or_3 (or_3_out, bne_suc, bltz_suc, beq_suc);
  Multiplexer #(.width(4), .enable("false")) multiplexer_12 (
    .in0(4'b1111), .in1(decoder_1_out0), .out(multiplexer_12_out), .sel(SB));
  Counter #(.width(16), .max('hffff)) counter_3 (
    .count(or_3_out), .Q(\条件分支成功数 ), .clk(CLK), .clr(RST));  // open: load, D, carry
  // MIPS_RAM mips_ram_1: pin names not known; wires that end beside it: mips_alu_1_result[21:2], multiplexer_10_out, \硬布线控制器_1_memwrite , multiplexer_12_out, CLK, RST, mips_ram_1_p7
  Multiplexer #(.width(32), .enable("false")) multiplexer_13 (
    .in0({mips_alu_1_result, less}), .in1(mips_ram_1_p7), .out(multiplexer_13_out), .sel(\硬布线控制器_1_memtoreg ));

  // Notes on the sheet:
  //   数码管输出应该用寄存器锁存，否则显示数据只能一闪而过
  //   10#10 (exit)
  //   10#34 (print hex)
  //   可以通过项目增加Logisim库的方式将前几次实验完成的电路作为子电路引入到本电路中使用
  //   指令存储器
  //   contents of rom_1 (hex, n*v repeats v):
  //   20110001 8000c05 20110001 20120002 20130003 8000c09 20110001 20120002 20130003 8000c0d 20110001
  //   20120002 20130003 8000c11 20110001 20120002 20130003 c000cfa 20100001 20110001 118fc0 112020
  //   20020022 c 118882 12200001 8000c15 112020 20020022 c 20110001 118880 112020 20020022 c 12200001
  //   8000c1f 20110001 118fc0 112020 20020022 c 1188c3 112020 20020022 c 118903 112020 20020022 c 118903
  //   112020 20020022 c 118903 112020 20020022 c 118903 112020 20020022 c 118903 112020 20020022 c 118903
  //   112020 20020022 c 118903 112020 20020022 c 20100001 109fc0 139fc3 8021 2012000c 24160003 26100001
  //   3210000f 20080008 20090001 139900 2709825 132020 20020022 c 1094022 1500fff9 22100001 2018000f
  //   2188024 108700 20080008 20090001 139902 2709825 132021 20020022 c 1094022 1500fff9 108702 2c9b022
  //   12c00001 8000c50 4020 1084027 84400 3508ffff 82021 20020022 c 2010ffff 20110000 ae300000 22100001
  //   22310004 ae300000 22100001 22310004 ae300000 22100001 22310004 ae300000 22100001 22310004 ae300000
  //   22100001 22310004 ae300000 22100001 22310004 ae300000 22100001 22310004 ae300000 22100001 22310004
  //   ae300000 22100001 22310004 ae300000 22100001 22310004 ae300000 22100001 22310004 ae300000 22100001
  //   22310004 ae300000 22100001 22310004 ae300000 22100001 22310004 ae300000 22100001 22310004 ae300000
  //   22100001 22310004 22100001 8020 2011003c 8e130000 8e340000 274402a 11000002 ae330000 ae140000
  //   2231fffc 1611fff8 102020 20020022 c 22100004 2011003c 1611fff2 20020032 c 20080001 20090003 20110876
  //   118d00 112020 20020022 c 200b0008 1118806 1318806 112020 20020022 c 216bffff 1560fff9 20020032 c
  //   20080001 20090003 20110876 118d00 112020 20020022 c 200b0008 1118807 1318807 112020 20020022 c
  //   216bffff 1560fff9 20020032 c 20090000 200b0020 20110000 20120001 a1310000 112020 20020022 c 2328820
  //   21290001 216bffff 1560fff8 200b0008 20090000 8d310000 112020 20020022 c 21290004 216bffff 1560fff9
  //   20020032 c 2011fff1 112020 20020022 c 22310001 620fffb 20020032 c 8000c00 20100000 22100001 102020
  //   20020022 c 22100002 102020 20020022 c 22100003 102020 20020022 c 22100004 102020 20020022 c 22100005
  //   102020 20020022 c 22100006 102020 20020022 c 22100007 102020 20020022 c 22100008 102020 20020022
  //   20020022 c 3e00008
  //   Syscall34
  //   数码管输出
  //   OP
  //   Func
  //   rs
  //   指令字
  //   rt
  //   rd
  //   总复位信号应将除ROM以外所有存储组件全部清零
  //   JMP
  //   JR
  //   OP
  //   Func
  //   Beq
  //   Bne
  //   MemToReg
  //   MemWrite
  //   AluOP
  //   AluSrcB
  //   RegWrite
  //   JAL
  //   RegDst
  //   Syscall
endmodule

// 单周期硬布线控制器
module \硬布线控制器  (
  input  [5:0] OP,
  input  [5:0] Func,
  output [3:0] ALU_OP,
  output MemToReg,
  output MemWrite,
  output ALU_SRC,
  output RegWrite,
  output SysCALL,
  output SignedExt,
  output RegDst,
  output Beq,
  output Bne,
  output JR,
  output JMP,
  output JAL,
  output BLTZ,
  output SB,
  output SV
);

  wire comparator_3_eq, comparator_4_eq, comparator_5_eq, or_1_out;

  \运算控制器  \u_运算控制器_1  (
    .OP0(OP[0]), .OP1(OP[1]), .OP2(OP[2]), .OP3(OP[3]), .OP4(OP[4]), .OP5(OP[5]), .F0(Func[0]), .F1(Func[1]),
    .F2(Func[2]), .F3(Func[3]), .F4(Func[4]), .F5(Func[5]), .S0(ALU_OP[0]), .S1(ALU_OP[1]), .S2(ALU_OP[2]),
    .S3(ALU_OP[3]));
  \控制信号生成  \u_控制信号生成_1  (
    .OP0(OP[0]), .OP1(OP[1]), .OP2(OP[2]), .OP3(OP[3]), .OP4(OP[4]), .OP5(OP[5]), .F0(Func[0]), .F1(Func[1]),
    .F2(Func[2]), .F3(Func[3]), .F4(Func[4]), .F5(Func[5]), .MemToReg(MemToReg), .MemWrite(MemWrite),
    .ALU_SRC(ALU_SRC), .RegWrite(RegWrite), .SysCALL(SysCALL), .SignedExt(SignedExt), .RegDst(RegDst),
    .BEQ(Beq), .BNE(Bne), .JR(JR), .JMP(JMP), .JAL(JAL));
  Comparator #(.width(6)) comparator_1 (.a(OP), .b(6'b000001), .eq(BLTZ));  // open: gt, lt
  Comparator #(.width(6)) comparator_2 (.a(OP), .b(6'b101000), .eq(SB));  // open: gt, lt
  Comparator #(.width(6)) comparator_3 (.a(OP), .b({6{1'b0}}), .eq(comparator_3_eq));  // open: gt, lt
  Comparator #(.width(6)) comparator_4 (.a(Func), .b(6'b000110), .eq(comparator_4_eq));  // open: gt, lt
  Comparator #(.width(6)) comparator_5 (.a(Func), .b(6'b000111), .eq(comparator_5_eq));  // open: gt, lt
  or or_1 (or_1_out, comparator_4_eq, comparator_5_eq);
  and and_1 (SV, comparator_3_eq, or_1_out);

  // Other names for the same wires on the sheet: OP_CODE[5:0] = OP

  // Notes on the sheet:
  //   运算器控制器，根据指令生成运算器功能选择信号
  //   控制信号生成，产生数据通路需要的其他控制信号
endmodule

// 运算器控制器
module \运算控制器  (
  input  OP0,
  input  OP1,
  input  OP2,
  input  OP3,
  input  OP4,
  input  OP5,
  input  F0,
  input  F1,
  input  F2,
  input  F3,
  input  F4,
  input  F5,
  output S0,
  output S1,
  output S2,
  output S3
);

  wire and_1_out, and_2_out, and_3_out, and_4_out, and_5_out, and_6_out, and_7_out, and_8_out, and_9_out,
       and_10_out, and_11_out, and_12_out, and_13_out, and_14_out, and_15_out, and_16_out, and_17_out,
       and_18_out, and_19_out, and_20_out, and_21_out, and_22_out, and_23_out, and_24_out, and_25_out,
       and_26_out, and_27_out, and_28_out, and_29_out, and_30_out, and_31_out, and_32_out, and_33_out,
       and_34_out, and_35_out, and_36_out, and_37_out, and_38_out, and_39_out, and_40_out, and_41_out,
       not_1_out, not_2_out, not_3_out, not_4_out, not_5_out, not_6_out, not_7_out, not_8_out, not_9_out,
       not_10_out, not_11_out, not_12_out, not_13_out, not_14_out, not_15_out, not_16_out, not_17_out,
       not_18_out, not_19_out, not_20_out, not_21_out, not_22_out, not_23_out, not_24_out, not_25_out,
       not_26_out, not_27_out, not_28_out, not_29_out, not_30_out, not_31_out, not_32_out, not_33_out,
       not_34_out, not_35_out, not_36_out, not_37_out, not_38_out, not_39_out, not_40_out, not_41_out,
       not_42_out, not_43_out, not_44_out, not_45_out, not_46_out, not_47_out, not_48_out, not_49_out,
       not_50_out, not_51_out, not_52_out, not_53_out, not_54_out, not_55_out, not_56_out, not_57_out,
       not_58_out, not_59_out, not_60_out, not_61_out, not_62_out, not_63_out, not_64_out, not_65_out,
       not_66_out, not_67_out, not_68_out, not_69_out, not_70_out, not_71_out, not_72_out, not_73_out,
       not_74_out, not_75_out, not_76_out, not_77_out, not_78_out, not_79_out, not_80_out, not_81_out,
       not_82_out, not_83_out, not_84_out, not_85_out, not_86_out, not_87_out, not_88_out, not_89_out,
       not_90_out, not_91_out, not_92_out, not_93_out, not_94_out, not_95_out, not_96_out, not_97_out,
       not_98_out, not_99_out, not_100_out, not_101_out, not_102_out, not_103_out, not_104_out, not_105_out,
       not_106_out, not_107_out, not_108_out, not_109_out, not_110_out, not_111_out, not_112_out,
       not_113_out, not_114_out, not_115_out, not_116_out, not_117_out, not_118_out, not_119_out,
       not_120_out, not_121_out, not_122_out, not_123_out, not_124_out, not_125_out, not_126_out,
       not_127_out, not_128_out, not_129_out, not_130_out, not_131_out, not_132_out, not_133_out,
       not_134_out, not_135_out, not_136_out, not_137_out, not_138_out, not_139_out, not_140_out,
       not_141_out, not_142_out, not_143_out, not_144_out, not_145_out, not_146_out, not_147_out,
       not_148_out, not_149_out, not_150_out, not_151_out, not_152_out, not_153_out, not_154_out,
       not_155_out, not_156_out, not_157_out, not_158_out, not_159_out, not_160_out, not_161_out,
       not_162_out, not_163_out, not_164_out, not_165_out, not_166_out, not_167_out, not_168_out,
       not_169_out, not_170_out, not_171_out, not_172_out, not_173_out, not_174_out, not_175_out,
       not_176_out, not_177_out, not_178_out, not_179_out, not_180_out, not_181_out, not_182_out,
       not_183_out, not_184_out, not_185_out, not_186_out, not_187_out, not_188_out, not_189_out,
       not_190_out, not_191_out, not_192_out, not_193_out, not_194_out, not_195_out, not_196_out,
       not_197_out, not_198_out, not_199_out, not_200_out, not_201_out, not_202_out, not_203_out,
       not_204_out, not_205_out, not_206_out, not_207_out, not_208_out, not_209_out, not_210_out,
       not_211_out, not_212_out, not_213_out, not_214_out, not_215_out, not_216_out, not_217_out,
       not_218_out, not_219_out, not_220_out, not_221_out, not_222_out, not_223_out, not_224_out,
       not_225_out, not_226_out, not_227_out, not_228_out, not_229_out, not_230_out, not_231_out,
       not_232_out, not_233_out, not_234_out, not_235_out, not_236_out, not_237_out, not_238_out,
       not_239_out, not_240_out, not_241_out, not_242_out, not_243_out, not_244_out, not_245_out,
       not_246_out, not_247_out, not_248_out, not_249_out, not_250_out, not_251_out, not_252_out,
       not_253_out, not_254_out, not_255_out, not_256_out, not_257_out, not_258_out, not_259_out,
       not_260_out, not_261_out, not_262_out, not_263_out, not_264_out, not_265_out, not_266_out,
       not_267_out, not_268_out, not_269_out, not_270_out, not_271_out, not_272_out, not_273_out,
       not_274_out, not_275_out, not_276_out, not_277_out, not_278_out;

  not not_1 (not_1_out, OP5);
  not not_2 (not_2_out, OP4);
  not not_3 (not_3_out, OP3);
  not not_4 (not_4_out, OP2);
  not not_5 (not_5_out, OP1);
  not not_6 (not_6_out, OP0);
  not not_7 (not_7_out, F5);
  not not_8 (not_8_out, F4);
  not not_9 (not_9_out, F3);
  not not_10 (not_10_out, F2);
  not not_11 (not_11_out, OP5);
  not not_12 (not_12_out, OP4);
  not not_13 (not_13_out, OP3);
  not not_14 (not_14_out, OP2);
  not not_15 (not_15_out, OP1);
  not not_16 (not_16_out, OP0);
  not not_17 (not_17_out, F4);
  not not_18 (not_18_out, F3);
  not not_19 (not_19_out, F2);
  not not_20 (not_20_out, F1);
  not not_21 (not_21_out, F0);
  not not_22 (not_22_out, OP5);
  not not_23 (not_23_out, OP4);
  not not_24 (not_24_out, OP3);
  not not_25 (not_25_out, OP2);
  not not_26 (not_26_out, OP1);
  not not_27 (not_27_out, OP0);
  not not_28 (not_28_out, F4);
  not not_29 (not_29_out, F3);
  not not_30 (not_30_out, F2);
  not not_31 (not_31_out, F1);
  not not_32 (not_32_out, OP5);
  not not_33 (not_33_out, OP4);
  not not_34 (not_34_out, OP3);
  not not_35 (not_35_out, OP2);
  not not_36 (not_36_out, OP1);
  not not_37 (not_37_out, OP0);
  not not_38 (not_38_out, F4);
  not not_39 (not_39_out, F3);
  not not_40 (not_40_out, F1);
  not not_41 (not_41_out, F0);
  not not_42 (not_42_out, OP5);
  not not_43 (not_43_out, OP4);
  not not_44 (not_44_out, OP3);
  not not_45 (not_45_out, OP2);
  not not_46 (not_46_out, OP1);
  not not_47 (not_47_out, OP0);
  not not_48 (not_48_out, F4);
  not not_49 (not_49_out, F2);
  not not_50 (not_50_out, F0);
  not not_51 (not_51_out, OP5);
  not not_52 (not_52_out, OP4);
  not not_53 (not_53_out, OP2);
  not not_54 (not_54_out, OP1);
  not not_55 (not_55_out, OP0);
  not not_56 (not_56_out, OP5);
  not not_57 (not_57_out, OP4);
  not not_58 (not_58_out, OP1);
  not not_59 (not_59_out, OP0);
  not not_60 (not_60_out, OP5);
  not not_61 (not_61_out, OP4);
  not not_62 (not_62_out, OP2);
  not not_63 (not_63_out, OP1);
  not not_64 (not_64_out, OP5);
  not not_65 (not_65_out, OP4);
  not not_66 (not_66_out, OP2);
  not not_67 (not_67_out, OP0);
  not not_68 (not_68_out, OP4);
  not not_69 (not_69_out, OP3);
  not not_70 (not_70_out, OP2);
  not not_71 (not_71_out, OP4);
  not not_72 (not_72_out, OP2);
  not not_73 (not_73_out, OP5);
  not not_74 (not_74_out, OP4);
  not not_75 (not_75_out, OP3);
  not not_76 (not_76_out, OP2);
  not not_77 (not_77_out, OP1);
  not not_78 (not_78_out, OP0);
  not not_79 (not_79_out, F5);
  not not_80 (not_80_out, F4);
  not not_81 (not_81_out, F3);
  not not_82 (not_82_out, OP4);
  not not_83 (not_83_out, OP2);
  not not_84 (not_84_out, OP1);
  not not_85 (not_85_out, OP0);
  not not_86 (not_86_out, OP5);
  not not_87 (not_87_out, OP4);
  not not_88 (not_88_out, OP3);
  not not_89 (not_89_out, OP2);
  not not_90 (not_90_out, OP1);
  not not_91 (not_91_out, OP5);
  not not_92 (not_92_out, OP4);
  not not_93 (not_93_out, OP3);
  not not_94 (not_94_out, OP2);
  not not_95 (not_95_out, OP1);
  not not_96 (not_96_out, OP0);
  not not_97 (not_97_out, F5);
  not not_98 (not_98_out, F4);
  not not_99 (not_99_out, F3);
  not not_100 (not_100_out, F2);
  not not_101 (not_101_out, F0);
  not not_102 (not_102_out, OP5);
  not not_103 (not_103_out, OP4);
  not not_104 (not_104_out, OP3);
  not not_105 (not_105_out, OP2);
  not not_106 (not_106_out, OP1);
  not not_107 (not_107_out, OP0);
  not not_108 (not_108_out, F4);
  not not_109 (not_109_out, F3);
  not not_110 (not_110_out, F2);
  not not_111 (not_111_out, F0);
  not not_112 (not_112_out, OP5);
  not not_113 (not_113_out, OP4);
  not not_114 (not_114_out, OP3);
  not not_115 (not_115_out, OP2);
  not not_116 (not_116_out, OP1);
  not not_117 (not_117_out, OP0);
  not not_118 (not_118_out, F4);
  not not_119 (not_119_out, F3);
  not not_120 (not_120_out, F1);
  not not_121 (not_121_out, F0);
  not not_122 (not_122_out, OP5);
  not not_123 (not_123_out, OP4);
  not not_124 (not_124_out, OP3);
  not not_125 (not_125_out, OP2);
  not not_126 (not_126_out, OP1);
  not not_127 (not_127_out, OP0);
  not not_128 (not_128_out, F4);
  not not_129 (not_129_out, F3);
  not not_130 (not_130_out, OP5);
  not not_131 (not_131_out, OP4);
  not not_132 (not_132_out, OP3);
  not not_133 (not_133_out, OP2);
  not not_134 (not_134_out, OP1);
  not not_135 (not_135_out, OP0);
  not not_136 (not_136_out, F4);
  not not_137 (not_137_out, F2);
  not not_138 (not_138_out, F0);
  not not_139 (not_139_out, OP5);
  not not_140 (not_140_out, OP4);
  not not_141 (not_141_out, OP1);
  not not_142 (not_142_out, OP0);
  not not_143 (not_143_out, OP5);
  not not_144 (not_144_out, OP4);
  not not_145 (not_145_out, OP2);
  not not_146 (not_146_out, OP0);
  not not_147 (not_147_out, OP5);
  not not_148 (not_148_out, OP4);
  not not_149 (not_149_out, OP3);
  not not_150 (not_150_out, OP2);
  not not_151 (not_151_out, OP1);
  not not_152 (not_152_out, OP0);
  not not_153 (not_153_out, F5);
  not not_154 (not_154_out, F4);
  not not_155 (not_155_out, F3);
  not not_156 (not_156_out, F0);
  not not_157 (not_157_out, OP5);
  not not_158 (not_158_out, OP4);
  not not_159 (not_159_out, OP3);
  not not_160 (not_160_out, OP2);
  not not_161 (not_161_out, OP1);
  not not_162 (not_162_out, OP5);
  not not_163 (not_163_out, OP4);
  not not_164 (not_164_out, OP3);
  not not_165 (not_165_out, OP2);
  not not_166 (not_166_out, OP1);
  not not_167 (not_167_out, OP0);
  not not_168 (not_168_out, F4);
  not not_169 (not_169_out, F3);
  not not_170 (not_170_out, F2);
  not not_171 (not_171_out, F1);
  not not_172 (not_172_out, F0);
  not not_173 (not_173_out, OP5);
  not not_174 (not_174_out, OP4);
  not not_175 (not_175_out, OP3);
  not not_176 (not_176_out, OP2);
  not not_177 (not_177_out, OP1);
  not not_178 (not_178_out, OP0);
  not not_179 (not_179_out, F4);
  not not_180 (not_180_out, F3);
  not not_181 (not_181_out, F2);
  not not_182 (not_182_out, F1);
  not not_183 (not_183_out, OP5);
  not not_184 (not_184_out, OP4);
  not not_185 (not_185_out, OP3);
  not not_186 (not_186_out, OP2);
  not not_187 (not_187_out, OP1);
  not not_188 (not_188_out, OP0);
  not not_189 (not_189_out, F4);
  not not_190 (not_190_out, F3);
  not not_191 (not_191_out, F2);
  not not_192 (not_192_out, F0);
  not not_193 (not_193_out, OP5);
  not not_194 (not_194_out, OP4);
  not not_195 (not_195_out, OP3);
  not not_196 (not_196_out, OP2);
  not not_197 (not_197_out, OP1);
  not not_198 (not_198_out, OP0);
  not not_199 (not_199_out, F4);
  not not_200 (not_200_out, F3);
  not not_201 (not_201_out, F1);
  not not_202 (not_202_out, F0);
  not not_203 (not_203_out, OP5);
  not not_204 (not_204_out, OP4);
  not not_205 (not_205_out, OP3);
  not not_206 (not_206_out, OP2);
  not not_207 (not_207_out, OP1);
  not not_208 (not_208_out, OP0);
  not not_209 (not_209_out, F4);
  not not_210 (not_210_out, F2);
  not not_211 (not_211_out, OP5);
  not not_212 (not_212_out, OP4);
  not not_213 (not_213_out, OP2);
  not not_214 (not_214_out, OP1);
  not not_215 (not_215_out, OP0);
  not not_216 (not_216_out, OP5);
  not not_217 (not_217_out, OP4);
  not not_218 (not_218_out, OP1);
  not not_219 (not_219_out, OP0);
  not not_220 (not_220_out, OP5);
  not not_221 (not_221_out, OP4);
  not not_222 (not_222_out, OP2);
  not not_223 (not_223_out, OP1);
  not not_224 (not_224_out, OP4);
  not not_225 (not_225_out, OP3);
  not not_226 (not_226_out, OP2);
  not not_227 (not_227_out, OP4);
  not not_228 (not_228_out, OP2);
  not not_229 (not_229_out, OP4);
  not not_230 (not_230_out, OP2);
  not not_231 (not_231_out, OP1);
  not not_232 (not_232_out, OP0);
  not not_233 (not_233_out, OP5);
  not not_234 (not_234_out, OP4);
  not not_235 (not_235_out, OP3);
  not not_236 (not_236_out, OP2);
  not not_237 (not_237_out, OP1);
  not not_238 (not_238_out, OP0);
  not not_239 (not_239_out, F4);
  not not_240 (not_240_out, F3);
  not not_241 (not_241_out, F1);
  not not_242 (not_242_out, OP5);
  not not_243 (not_243_out, OP4);
  not not_244 (not_244_out, OP3);
  not not_245 (not_245_out, OP2);
  not not_246 (not_246_out, OP1);
  not not_247 (not_247_out, OP0);
  not not_248 (not_248_out, F4);
  not not_249 (not_249_out, F3);
  not not_250 (not_250_out, OP5);
  not not_251 (not_251_out, OP4);
  not not_252 (not_252_out, OP3);
  not not_253 (not_253_out, OP2);
  not not_254 (not_254_out, OP1);
  not not_255 (not_255_out, OP0);
  not not_256 (not_256_out, F4);
  not not_257 (not_257_out, F2);
  not not_258 (not_258_out, F0);
  not not_259 (not_259_out, OP5);
  not not_260 (not_260_out, OP4);
  not not_261 (not_261_out, OP3);
  not not_262 (not_262_out, OP2);
  not not_263 (not_263_out, OP1);
  not not_264 (not_264_out, OP0);
  not not_265 (not_265_out, F4);
  not not_266 (not_266_out, F2);
  not not_267 (not_267_out, OP5);
  not not_268 (not_268_out, OP4);
  not not_269 (not_269_out, OP2);
  not not_270 (not_270_out, OP0);
  not not_271 (not_271_out, OP5);
  not not_272 (not_272_out, OP4);
  not not_273 (not_273_out, OP1);
  not not_274 (not_274_out, OP5);
  not not_275 (not_275_out, OP4);
  not not_276 (not_276_out, OP3);
  not not_277 (not_277_out, OP2);
  not not_278 (not_278_out, OP1);
  and and_1 (and_1_out, not_1_out, not_2_out, not_3_out, not_4_out, not_5_out, not_6_out, not_7_out, not_8_out, not_9_out, not_10_out, F1, F0);
  and and_2 (and_2_out, not_11_out, not_12_out, not_13_out, not_14_out, not_15_out, not_16_out, F5, not_17_out, not_18_out, not_19_out, not_20_out, not_21_out);
  and and_3 (and_3_out, not_22_out, not_23_out, not_24_out, not_25_out, not_26_out, not_27_out, F5, not_28_out, not_29_out, not_30_out, not_31_out, F0);
  and and_4 (and_4_out, not_32_out, not_33_out, not_34_out, not_35_out, not_36_out, not_37_out, F5, not_38_out, not_39_out, F2, not_40_out, not_41_out);
  and and_5 (and_5_out, not_42_out, not_43_out, not_44_out, not_45_out, not_46_out, not_47_out, F5, not_48_out, F3, not_49_out, F1, not_50_out);
  and and_6 (and_6_out, not_51_out, not_52_out, OP3, not_53_out, not_54_out, not_55_out);
  and and_7 (and_7_out, not_56_out, not_57_out, OP3, OP2, not_58_out, not_59_out);
  and and_8 (and_8_out, not_60_out, not_61_out, OP3, not_62_out, not_63_out, OP0);
  and and_9 (and_9_out, not_64_out, not_65_out, OP3, not_66_out, OP1, not_67_out);
  and and_10 (and_10_out, OP5, not_68_out, not_69_out, not_70_out, OP1, OP0);
  and and_11 (and_11_out, OP5, not_71_out, OP3, not_72_out, OP1, OP0);
  and and_12 (and_12_out, not_73_out, not_74_out, not_75_out, not_76_out, not_77_out, not_78_out, not_79_out, not_80_out, not_81_out, F2, F1, F0);
  and and_13 (and_13_out, OP5, not_82_out, OP3, not_83_out, not_84_out, not_85_out);
  and and_14 (and_14_out, not_86_out, not_87_out, not_88_out, not_89_out, not_90_out, OP0);
  and and_15 (and_15_out, not_91_out, not_92_out, not_93_out, not_94_out, not_95_out, not_96_out, not_97_out, not_98_out, not_99_out, not_100_out, F1, not_101_out);
  and and_16 (and_16_out, not_102_out, not_103_out, not_104_out, not_105_out, not_106_out, not_107_out, F5, not_108_out, not_109_out, not_110_out, F1, not_111_out);
  and and_17 (and_17_out, not_112_out, not_113_out, not_114_out, not_115_out, not_116_out, not_117_out, F5, not_118_out, not_119_out, F2, not_120_out, not_121_out);
  and and_18 (and_18_out, not_122_out, not_123_out, not_124_out, not_125_out, not_126_out, not_127_out, F5, not_128_out, not_129_out, F2, F1, F0);
  and and_19 (and_19_out, not_130_out, not_131_out, not_132_out, not_133_out, not_134_out, not_135_out, F5, not_136_out, F3, not_137_out, F1, not_138_out);
  and and_20 (and_20_out, not_139_out, not_140_out, OP3, OP2, not_141_out, not_142_out);
  and and_21 (and_21_out, not_143_out, not_144_out, OP3, not_145_out, OP1, not_146_out);
  and and_22 (and_22_out, not_147_out, not_148_out, not_149_out, not_150_out, not_151_out, not_152_out, not_153_out, not_154_out, not_155_out, F2, F1, not_156_out);
  and and_23 (and_23_out, not_157_out, not_158_out, not_159_out, not_160_out, not_161_out, OP0);
  and and_24 (and_24_out, not_162_out, not_163_out, not_164_out, not_165_out, not_166_out, not_167_out, F5, not_168_out, not_169_out, not_170_out, not_171_out, not_172_out);
  and and_25 (and_25_out, not_173_out, not_174_out, not_175_out, not_176_out, not_177_out, not_178_out, F5, not_179_out, not_180_out, not_181_out, not_182_out, F0);
  and and_26 (and_26_out, not_183_out, not_184_out, not_185_out, not_186_out, not_187_out, not_188_out, F5, not_189_out, not_190_out, not_191_out, F1, not_192_out);
  and and_27 (and_27_out, not_193_out, not_194_out, not_195_out, not_196_out, not_197_out, not_198_out, F5, not_199_out, not_200_out, F2, not_201_out, not_202_out);
  and and_28 (and_28_out, not_203_out, not_204_out, not_205_out, not_206_out, not_207_out, not_208_out, F5, not_209_out, F3, not_210_out, F1, F0);
  and and_29 (and_29_out, not_211_out, not_212_out, OP3, not_213_out, not_214_out, not_215_out);
  and and_30 (and_30_out, not_216_out, not_217_out, OP3, OP2, not_218_out, not_219_out);
  and and_31 (and_31_out, not_220_out, not_221_out, OP3, not_222_out, not_223_out, OP0);
  and and_32 (and_32_out, OP5, not_224_out, not_225_out, not_226_out, OP1, OP0);
  and and_33 (and_33_out, OP5, not_227_out, OP3, not_228_out, OP1, OP0);
  and and_34 (and_34_out, OP5, not_229_out, OP3, not_230_out, not_231_out, not_232_out);
  and and_35 (and_35_out, not_233_out, not_234_out, not_235_out, not_236_out, not_237_out, not_238_out, F5, not_239_out, not_240_out, F2, not_241_out, F0);
  and and_36 (and_36_out, not_242_out, not_243_out, not_244_out, not_245_out, not_246_out, not_247_out, F5, not_248_out, not_249_out, F2, F1, F0);
  and and_37 (and_37_out, not_250_out, not_251_out, not_252_out, not_253_out, not_254_out, not_255_out, F5, not_256_out, F3, not_257_out, F1, not_258_out);
  and and_38 (and_38_out, not_259_out, not_260_out, not_261_out, not_262_out, not_263_out, not_264_out, F5, not_265_out, F3, not_266_out, F1, F0);
  and and_39 (and_39_out, not_267_out, not_268_out, OP3, not_269_out, OP1, not_270_out);
  and and_40 (and_40_out, not_271_out, not_272_out, OP3, OP2, not_273_out, OP0);
  and and_41 (and_41_out, not_274_out, not_275_out, not_276_out, not_277_out, not_278_out, OP0);
  or or_1 (S1, and_15_out, and_16_out, and_17_out, and_18_out, and_19_out, and_20_out, and_21_out, and_22_out, and_23_out);
  or or_2 (S2, and_24_out, and_25_out, and_26_out, and_27_out, and_28_out, and_29_out, and_30_out, and_31_out, and_32_out, and_33_out, and_34_out);
  or or_3 (S3, and_35_out, and_36_out, and_37_out, and_38_out, and_39_out, and_40_out, and_41_out);
  or or_4 (S0, and_1_out, and_2_out, and_3_out, and_4_out, and_5_out, and_6_out, and_7_out, and_8_out, and_9_out, and_10_out, and_11_out, and_12_out, and_13_out, and_14_out);
endmodule

// 控制信号生成
module \控制信号生成  (
  input  OP0,
  input  OP1,
  input  OP2,
  input  OP3,
  input  OP4,
  input  OP5,
  input  F0,
  input  F1,
  input  F2,
  input  F3,
  input  F4,
  input  F5,
  output MemToReg,
  output MemWrite,
  output ALU_SRC,
  output RegWrite,
  output SysCALL,
  output SignedExt,
  output RegDst,
  output BEQ,
  output BNE,
  output JR,
  output JMP,
  output JAL
);

  wire and_2_out, and_3_out, and_4_out, and_5_out, and_6_out, and_7_out, and_8_out, and_9_out, and_10_out,
       and_11_out, and_12_out, and_13_out, and_14_out, and_15_out, and_16_out, and_17_out, and_18_out,
       and_19_out, and_20_out, and_21_out, and_22_out, and_23_out, and_24_out, and_25_out, and_26_out,
       and_27_out, and_28_out, and_29_out, and_30_out, and_31_out, and_33_out, and_34_out, and_35_out,
       and_36_out, and_37_out, and_38_out, and_39_out, and_40_out, and_41_out, and_42_out, and_43_out,
       and_44_out, and_45_out, and_46_out, and_47_out, and_48_out, and_49_out, and_50_out, and_51_out,
       and_52_out, and_56_out, and_57_out, and_58_out, not_1_out, not_2_out, not_3_out, not_4_out, not_5_out,
       not_6_out, not_7_out, not_8_out, not_9_out, not_10_out, not_11_out, not_12_out, not_13_out,
       not_14_out, not_15_out, not_16_out, not_17_out, not_18_out, not_19_out, not_20_out, not_21_out,
       not_22_out, not_23_out, not_24_out, not_25_out, not_26_out, not_27_out, not_28_out, not_29_out,
       not_30_out, not_31_out, not_32_out, not_33_out, not_34_out, not_35_out, not_36_out, not_37_out,
       not_38_out, not_39_out, not_40_out, not_41_out, not_42_out, not_43_out, not_44_out, not_45_out,
       not_46_out, not_47_out, not_48_out, not_49_out, not_50_out, not_51_out, not_52_out, not_53_out,
       not_54_out, not_55_out, not_56_out, not_57_out, not_58_out, not_59_out, not_60_out, not_61_out,
       not_62_out, not_63_out, not_64_out, not_65_out, not_66_out, not_67_out, not_68_out, not_69_out,
       not_70_out, not_71_out, not_72_out, not_73_out, not_74_out, not_75_out, not_76_out, not_77_out,
       not_78_out, not_79_out, not_80_out, not_81_out, not_82_out, not_83_out, not_84_out, not_85_out,
       not_86_out, not_87_out, not_88_out, not_89_out, not_90_out, not_91_out, not_92_out, not_93_out,
       not_94_out, not_95_out, not_96_out, not_97_out, not_98_out, not_99_out, not_100_out, not_101_out,
       not_102_out, not_103_out, not_104_out, not_105_out, not_106_out, not_107_out, not_108_out,
       not_109_out, not_110_out, not_111_out, not_112_out, not_113_out, not_114_out, not_115_out,
       not_116_out, not_117_out, not_118_out, not_119_out, not_120_out, not_121_out, not_122_out,
       not_123_out, not_124_out, not_125_out, not_126_out, not_127_out, not_128_out, not_129_out,
       not_130_out, not_131_out, not_132_out, not_133_out, not_134_out, not_135_out, not_136_out,
       not_137_out, not_138_out, not_139_out, not_140_out, not_141_out, not_142_out, not_143_out,
       not_144_out, not_145_out, not_146_out, not_147_out, not_148_out, not_149_out, not_150_out,
       not_151_out, not_152_out, not_153_out, not_154_out, not_155_out, not_156_out, not_157_out,
       not_158_out, not_159_out, not_160_out, not_161_out, not_162_out, not_163_out, not_164_out,
       not_165_out, not_166_out, not_167_out, not_168_out, not_169_out, not_170_out, not_171_out,
       not_172_out, not_173_out, not_174_out, not_175_out, not_176_out, not_177_out, not_178_out,
       not_179_out, not_180_out, not_181_out, not_182_out, not_183_out, not_184_out, not_185_out,
       not_186_out, not_187_out, not_188_out, not_189_out, not_190_out, not_191_out, not_192_out,
       not_193_out, not_194_out, not_195_out, not_196_out, not_197_out, not_198_out, not_199_out,
       not_200_out, not_201_out, not_202_out, not_203_out, not_204_out, not_205_out, not_206_out,
       not_207_out, not_208_out, not_209_out, not_210_out, not_211_out, not_212_out, not_213_out,
       not_214_out, not_215_out, not_216_out, not_217_out, not_218_out, not_219_out, not_220_out,
       not_221_out, not_222_out, not_223_out, not_224_out, not_225_out, not_226_out, not_227_out,
       not_228_out, not_229_out, not_230_out, not_231_out, not_232_out, not_233_out, not_234_out,
       not_235_out, not_236_out, not_237_out, not_238_out, not_239_out, not_240_out, not_241_out,
       not_242_out, not_243_out, not_244_out, not_245_out, not_246_out, not_247_out, not_248_out,
       not_249_out, not_250_out, not_251_out, not_252_out, not_253_out, not_254_out, not_255_out,
       not_256_out, not_257_out, not_258_out, not_259_out, not_260_out, not_261_out, not_262_out,
       not_263_out, not_264_out, not_265_out, not_266_out, not_267_out, not_268_out, not_269_out,
       not_270_out, not_271_out, not_272_out, not_273_out, not_274_out, not_275_out, not_276_out,
       not_277_out, not_278_out, not_279_out, not_280_out, not_281_out, not_282_out, not_283_out,
       not_284_out, not_285_out, not_286_out, not_287_out, not_288_out, not_289_out, not_290_out,
       not_291_out, not_292_out, not_293_out, not_294_out, not_295_out, not_296_out, not_297_out,
       not_298_out, not_299_out, not_300_out, not_301_out, not_302_out, not_303_out, not_304_out,
       not_305_out, not_306_out, not_307_out, not_308_out, not_309_out, not_310_out, not_311_out,
       not_312_out, not_313_out, not_314_out, not_315_out, not_316_out, not_317_out, not_318_out,
       not_319_out, not_320_out, not_321_out, not_322_out, not_323_out, not_324_out, not_325_out,
       not_326_out, not_327_out, not_328_out, not_329_out, not_330_out, not_331_out, not_332_out,
       not_333_out, not_334_out, not_335_out, not_336_out, not_337_out, not_338_out, not_339_out,
       not_340_out, not_341_out, not_342_out, not_343_out, not_344_out, not_345_out, not_346_out,
       not_347_out, not_348_out, not_349_out, not_350_out, not_351_out, not_352_out, not_353_out,
       not_354_out, not_355_out, not_356_out, not_357_out, not_358_out, not_359_out, not_360_out,
       not_361_out, not_362_out, not_363_out, not_364_out, not_365_out, not_366_out, not_367_out,
       not_368_out, not_369_out, not_370_out, not_371_out, not_372_out, not_373_out, not_374_out,
       not_375_out, not_376_out, not_377_out, not_378_out, not_379_out, not_380_out, not_381_out,
       not_382_out, not_383_out, not_384_out, not_385_out, not_386_out, not_387_out, not_388_out,
       not_389_out, not_390_out, not_391_out, not_392_out, not_393_out, not_394_out, not_395_out,
       not_396_out, not_397_out, not_398_out, not_399_out, not_400_out;

  not not_1 (not_1_out, OP4);
  not not_2 (not_2_out, OP3);
  not not_3 (not_3_out, OP2);
  not not_4 (not_4_out, OP4);
  not not_5 (not_5_out, OP2);
  not not_6 (not_6_out, OP4);
  not not_7 (not_7_out, OP2);
  not not_8 (not_8_out, OP1);
  not not_9 (not_9_out, OP0);
  not not_10 (not_10_out, OP5);
  not not_11 (not_11_out, OP4);
  not not_12 (not_12_out, OP2);
  not not_13 (not_13_out, OP1);
  not not_14 (not_14_out, OP0);
  not not_15 (not_15_out, OP5);
  not not_16 (not_16_out, OP4);
  not not_17 (not_17_out, OP1);
  not not_18 (not_18_out, OP0);
  not not_19 (not_19_out, OP5);
  not not_20 (not_20_out, OP4);
  not not_21 (not_21_out, OP2);
  not not_22 (not_22_out, OP1);
  not not_23 (not_23_out, OP5);
  not not_24 (not_24_out, OP4);
  not not_25 (not_25_out, OP2);
  not not_26 (not_26_out, OP0);
  not not_27 (not_27_out, OP5);
  not not_28 (not_28_out, OP4);
  not not_29 (not_29_out, OP1);
  not not_30 (not_30_out, OP4);
  not not_31 (not_31_out, OP3);
  not not_32 (not_32_out, OP2);
  not not_33 (not_33_out, OP4);
  not not_34 (not_34_out, OP2);
  not not_35 (not_35_out, OP4);
  not not_36 (not_36_out, OP2);
  not not_37 (not_37_out, OP1);
  not not_38 (not_38_out, OP0);
  not not_39 (not_39_out, OP5);
  not not_40 (not_40_out, OP4);
  not not_41 (not_41_out, OP3);
  not not_42 (not_42_out, OP2);
  not not_43 (not_43_out, OP1);
  not not_44 (not_44_out, OP0);
  not not_45 (not_45_out, F5);
  not not_46 (not_46_out, F4);
  not not_47 (not_47_out, F3);
  not not_48 (not_48_out, F2);
  not not_49 (not_49_out, F1);
  not not_50 (not_50_out, F0);
  not not_51 (not_51_out, OP5);
  not not_52 (not_52_out, OP4);
  not not_53 (not_53_out, OP3);
  not not_54 (not_54_out, OP2);
  not not_55 (not_55_out, OP1);
  not not_56 (not_56_out, OP0);
  not not_57 (not_57_out, F5);
  not not_58 (not_58_out, F4);
  not not_59 (not_59_out, F3);
  not not_60 (not_60_out, F2);
  not not_61 (not_61_out, OP5);
  not not_62 (not_62_out, OP4);
  not not_63 (not_63_out, OP3);
  not not_64 (not_64_out, OP2);
  not not_65 (not_65_out, OP1);
  not not_66 (not_66_out, OP0);
  not not_67 (not_67_out, F5);
  not not_68 (not_68_out, F4);
  not not_69 (not_69_out, F3);
  not not_70 (not_70_out, F2);
  not not_71 (not_71_out, F0);
  not not_72 (not_72_out, OP5);
  not not_73 (not_73_out, OP4);
  not not_74 (not_74_out, OP3);
  not not_75 (not_75_out, OP2);
  not not_76 (not_76_out, OP1);
  not not_77 (not_77_out, OP0);
  not not_78 (not_78_out, F4);
  not not_79 (not_79_out, F3);
  not not_80 (not_80_out, F2);
  not not_81 (not_81_out, F1);
  not not_82 (not_82_out, F0);
  not not_83 (not_83_out, OP5);
  not not_84 (not_84_out, OP4);
  not not_85 (not_85_out, OP3);
  not not_86 (not_86_out, OP2);
  not not_87 (not_87_out, OP1);
  not not_88 (not_88_out, OP0);
  not not_89 (not_89_out, F4);
  not not_90 (not_90_out, F3);
  not not_91 (not_91_out, F2);
  not not_92 (not_92_out, F1);
  not not_93 (not_93_out, OP5);
  not not_94 (not_94_out, OP4);
  not not_95 (not_95_out, OP3);
  not not_96 (not_96_out, OP2);
  not not_97 (not_97_out, OP1);
  not not_98 (not_98_out, OP0);
  not not_99 (not_99_out, F4);
  not not_100 (not_100_out, F3);
  not not_101 (not_101_out, F2);
  not not_102 (not_102_out, F0);
  not not_103 (not_103_out, OP5);
  not not_104 (not_104_out, OP4);
  not not_105 (not_105_out, OP3);
  not not_106 (not_106_out, OP2);
  not not_107 (not_107_out, OP1);
  not not_108 (not_108_out, OP0);
  not not_109 (not_109_out, F4);
  not not_110 (not_110_out, F3);
  not not_111 (not_111_out, F1);
  not not_112 (not_112_out, F0);
  not not_113 (not_113_out, OP5);
  not not_114 (not_114_out, OP4);
  not not_115 (not_115_out, OP3);
  not not_116 (not_116_out, OP2);
  not not_117 (not_117_out, OP1);
  not not_118 (not_118_out, OP0);
  not not_119 (not_119_out, F4);
  not not_120 (not_120_out, F3);
  not not_121 (not_121_out, F1);
  not not_122 (not_122_out, OP5);
  not not_123 (not_123_out, OP4);
  not not_124 (not_124_out, OP3);
  not not_125 (not_125_out, OP2);
  not not_126 (not_126_out, OP1);
  not not_127 (not_127_out, OP0);
  not not_128 (not_128_out, F4);
  not not_129 (not_129_out, F3);
  not not_130 (not_130_out, OP5);
  not not_131 (not_131_out, OP4);
  not not_132 (not_132_out, OP3);
  not not_133 (not_133_out, OP2);
  not not_134 (not_134_out, OP1);
  not not_135 (not_135_out, OP0);
  not not_136 (not_136_out, F4);
  not not_137 (not_137_out, F2);
  not not_138 (not_138_out, F0);
  not not_139 (not_139_out, OP5);
  not not_140 (not_140_out, OP4);
  not not_141 (not_141_out, OP3);
  not not_142 (not_142_out, OP2);
  not not_143 (not_143_out, OP1);
  not not_144 (not_144_out, OP0);
  not not_145 (not_145_out, F4);
  not not_146 (not_146_out, F2);
  not not_147 (not_147_out, OP5);
  not not_148 (not_148_out, OP4);
  not not_149 (not_149_out, OP3);
  not not_150 (not_150_out, OP2);
  not not_151 (not_151_out, OP5);
  not not_152 (not_152_out, OP4);
  not not_153 (not_153_out, OP2);
  not not_154 (not_154_out, OP1);
  not not_155 (not_155_out, OP0);
  not not_156 (not_156_out, OP5);
  not not_157 (not_157_out, OP4);
  not not_158 (not_158_out, OP1);
  not not_159 (not_159_out, OP0);
  not not_160 (not_160_out, OP5);
  not not_161 (not_161_out, OP4);
  not not_162 (not_162_out, OP2);
  not not_163 (not_163_out, OP1);
  not not_164 (not_164_out, OP5);
  not not_165 (not_165_out, OP4);
  not not_166 (not_166_out, OP2);
  not not_167 (not_167_out, OP0);
  not not_168 (not_168_out, OP5);
  not not_169 (not_169_out, OP4);
  not not_170 (not_170_out, OP1);
  not not_171 (not_171_out, OP4);
  not not_172 (not_172_out, OP3);
  not not_173 (not_173_out, OP2);
  not not_174 (not_174_out, OP5);
  not not_175 (not_175_out, OP4);
  not not_176 (not_176_out, OP3);
  not not_177 (not_177_out, OP2);
  not not_178 (not_178_out, OP1);
  not not_179 (not_179_out, OP0);
  not not_180 (not_180_out, F5);
  not not_181 (not_181_out, F4);
  not not_182 (not_182_out, F3);
  not not_183 (not_183_out, F0);
  not not_184 (not_184_out, OP5);
  not not_185 (not_185_out, OP4);
  not not_186 (not_186_out, OP3);
  not not_187 (not_187_out, OP2);
  not not_188 (not_188_out, OP1);
  not not_189 (not_189_out, OP0);
  not not_190 (not_190_out, F5);
  not not_191 (not_191_out, F4);
  not not_192 (not_192_out, F3);
  not not_193 (not_193_out, OP5);
  not not_194 (not_194_out, OP4);
  not not_195 (not_195_out, OP3);
  not not_196 (not_196_out, OP2);
  not not_197 (not_197_out, OP1);
  not not_198 (not_198_out, OP0);
  not not_199 (not_199_out, F5);
  not not_200 (not_200_out, F4);
  not not_201 (not_201_out, F1);
  not not_202 (not_202_out, F0);
  not not_203 (not_203_out, OP5);
  not not_204 (not_204_out, OP4);
  not not_205 (not_205_out, OP3);
  not not_206 (not_206_out, OP1);
  not not_207 (not_207_out, OP0);
  not not_208 (not_208_out, OP5);
  not not_209 (not_209_out, OP4);
  not not_210 (not_210_out, OP3);
  not not_211 (not_211_out, OP1);
  not not_212 (not_212_out, OP5);
  not not_213 (not_213_out, OP4);
  not not_214 (not_214_out, OP2);
  not not_215 (not_215_out, OP1);
  not not_216 (not_216_out, OP0);
  not not_217 (not_217_out, OP5);
  not not_218 (not_218_out, OP4);
  not not_219 (not_219_out, OP2);
  not not_220 (not_220_out, OP0);
  not not_221 (not_221_out, OP4);
  not not_222 (not_222_out, OP3);
  not not_223 (not_223_out, OP2);
  not not_224 (not_224_out, OP4);
  not not_225 (not_225_out, OP2);
  not not_226 (not_226_out, OP4);
  not not_227 (not_227_out, OP2);
  not not_228 (not_228_out, OP1);
  not not_229 (not_229_out, OP0);
  not not_230 (not_230_out, OP5);
  not not_231 (not_231_out, OP4);
  not not_232 (not_232_out, OP3);
  not not_233 (not_233_out, OP2);
  not not_234 (not_234_out, OP1);
  not not_235 (not_235_out, OP0);
  not not_236 (not_236_out, F5);
  not not_237 (not_237_out, F4);
  not not_238 (not_238_out, F3);
  not not_239 (not_239_out, F2);
  not not_240 (not_240_out, F1);
  not not_241 (not_241_out, F0);
  not not_242 (not_242_out, OP5);
  not not_243 (not_243_out, OP4);
  not not_244 (not_244_out, OP3);
  not not_245 (not_245_out, OP2);
  not not_246 (not_246_out, OP1);
  not not_247 (not_247_out, OP0);
  not not_248 (not_248_out, F5);
  not not_249 (not_249_out, F4);
  not not_250 (not_250_out, F3);
  not not_251 (not_251_out, F2);
  not not_252 (not_252_out, OP5);
  not not_253 (not_253_out, OP4);
  not not_254 (not_254_out, OP3);
  not not_255 (not_255_out, OP2);
  not not_256 (not_256_out, OP1);
  not not_257 (not_257_out, OP0);
  not not_258 (not_258_out, F5);
  not not_259 (not_259_out, F4);
  not not_260 (not_260_out, F3);
  not not_261 (not_261_out, F2);
  not not_262 (not_262_out, F0);
  not not_263 (not_263_out, OP5);
  not not_264 (not_264_out, OP4);
  not not_265 (not_265_out, OP3);
  not not_266 (not_266_out, OP2);
  not not_267 (not_267_out, OP1);
  not not_268 (not_268_out, OP0);
  not not_269 (not_269_out, F4);
  not not_270 (not_270_out, F3);
  not not_271 (not_271_out, F2);
  not not_272 (not_272_out, F1);
  not not_273 (not_273_out, F0);
  not not_274 (not_274_out, OP5);
  not not_275 (not_275_out, OP4);
  not not_276 (not_276_out, OP3);
  not not_277 (not_277_out, OP2);
  not not_278 (not_278_out, OP1);
  not not_279 (not_279_out, OP0);
  not not_280 (not_280_out, F4);
  not not_281 (not_281_out, F3);
  not not_282 (not_282_out, F2);
  not not_283 (not_283_out, F1);
  not not_284 (not_284_out, OP5);
  not not_285 (not_285_out, OP4);
  not not_286 (not_286_out, OP3);
  not not_287 (not_287_out, OP2);
  not not_288 (not_288_out, OP1);
  not not_289 (not_289_out, OP0);
  not not_290 (not_290_out, F4);
  not not_291 (not_291_out, F3);
  not not_292 (not_292_out, F2);
  not not_293 (not_293_out, F0);
  not not_294 (not_294_out, OP5);
  not not_295 (not_295_out, OP4);
  not not_296 (not_296_out, OP3);
  not not_297 (not_297_out, OP2);
  not not_298 (not_298_out, OP1);
  not not_299 (not_299_out, OP0);
  not not_300 (not_300_out, F4);
  not not_301 (not_301_out, F3);
  not not_302 (not_302_out, F1);
  not not_303 (not_303_out, F0);
  not not_304 (not_304_out, OP5);
  not not_305 (not_305_out, OP4);
  not not_306 (not_306_out, OP3);
  not not_307 (not_307_out, OP2);
  not not_308 (not_308_out, OP1);
  not not_309 (not_309_out, OP0);
  not not_310 (not_310_out, F4);
  not not_311 (not_311_out, F3);
  not not_312 (not_312_out, F1);
  not not_313 (not_313_out, OP5);
  not not_314 (not_314_out, OP4);
  not not_315 (not_315_out, OP3);
  not not_316 (not_316_out, OP2);
  not not_317 (not_317_out, OP1);
  not not_318 (not_318_out, OP0);
  not not_319 (not_319_out, F4);
  not not_320 (not_320_out, F3);
  not not_321 (not_321_out, OP5);
  not not_322 (not_322_out, OP4);
  not not_323 (not_323_out, OP3);
  not not_324 (not_324_out, OP2);
  not not_325 (not_325_out, OP1);
  not not_326 (not_326_out, OP0);
  not not_327 (not_327_out, F4);
  not not_328 (not_328_out, F2);
  not not_329 (not_329_out, F0);
  not not_330 (not_330_out, OP5);
  not not_331 (not_331_out, OP4);
  not not_332 (not_332_out, OP3);
  not not_333 (not_333_out, OP2);
  not not_334 (not_334_out, OP1);
  not not_335 (not_335_out, OP0);
  not not_336 (not_336_out, F4);
  not not_337 (not_337_out, F2);
  not not_338 (not_338_out, OP5);
  not not_339 (not_339_out, OP4);
  not not_340 (not_340_out, OP3);
  not not_341 (not_341_out, OP2);
  not not_342 (not_342_out, OP1);
  not not_343 (not_343_out, OP0);
  not not_344 (not_344_out, F5);
  not not_345 (not_345_out, F4);
  not not_346 (not_346_out, F3);
  not not_347 (not_347_out, F0);
  not not_348 (not_348_out, OP5);
  not not_349 (not_349_out, OP4);
  not not_350 (not_350_out, OP3);
  not not_351 (not_351_out, OP2);
  not not_352 (not_352_out, OP1);
  not not_353 (not_353_out, OP0);
  not not_354 (not_354_out, F5);
  not not_355 (not_355_out, F4);
  not not_356 (not_356_out, F3);
  not not_357 (not_357_out, OP5);
  not not_358 (not_358_out, OP4);
  not not_359 (not_359_out, OP3);
  not not_360 (not_360_out, OP1);
  not not_361 (not_361_out, OP0);
  not not_362 (not_362_out, OP5);
  not not_363 (not_363_out, OP4);
  not not_364 (not_364_out, OP3);
  not not_365 (not_365_out, OP1);
  not not_366 (not_366_out, OP5);
  not not_367 (not_367_out, OP4);
  not not_368 (not_368_out, OP3);
  not not_369 (not_369_out, OP2);
  not not_370 (not_370_out, OP1);
  not not_371 (not_371_out, OP0);
  not not_372 (not_372_out, F5);
  not not_373 (not_373_out, F4);
  not not_374 (not_374_out, F2);
  not not_375 (not_375_out, F1);
  not not_376 (not_376_out, F0);
  not not_377 (not_377_out, OP5);
  not not_378 (not_378_out, OP4);
  not not_379 (not_379_out, OP3);
  not not_380 (not_380_out, OP2);
  not not_381 (not_381_out, OP1);
  not not_382 (not_382_out, OP0);
  not not_383 (not_383_out, F5);
  not not_384 (not_384_out, F4);
  not not_385 (not_385_out, F2);
  not not_386 (not_386_out, F1);
  not not_387 (not_387_out, F0);
  not not_388 (not_388_out, OP5);
  not not_389 (not_389_out, OP4);
  not not_390 (not_390_out, OP3);
  not not_391 (not_391_out, OP2);
  not not_392 (not_392_out, OP0);
  not not_393 (not_393_out, OP5);
  not not_394 (not_394_out, OP4);
  not not_395 (not_395_out, OP3);
  not not_396 (not_396_out, OP2);
  not not_397 (not_397_out, OP5);
  not not_398 (not_398_out, OP4);
  not not_399 (not_399_out, OP3);
  not not_400 (not_400_out, OP2);
  and and_1 (MemToReg, OP5, not_1_out, not_2_out, not_3_out, OP1, OP0);
  and and_2 (and_2_out, OP5, not_4_out, OP3, not_5_out, OP1, OP0);
  and and_3 (and_3_out, OP5, not_6_out, OP3, not_7_out, not_8_out, not_9_out);
  and and_4 (and_4_out, not_10_out, not_11_out, OP3, not_12_out, not_13_out, not_14_out);
  and and_5 (and_5_out, not_15_out, not_16_out, OP3, OP2, not_17_out, not_18_out);
  and and_6 (and_6_out, not_19_out, not_20_out, OP3, not_21_out, not_22_out, OP0);
  and and_7 (and_7_out, not_23_out, not_24_out, OP3, not_25_out, OP1, not_26_out);
  and and_8 (and_8_out, not_27_out, not_28_out, OP3, OP2, not_29_out, OP0);
  and and_9 (and_9_out, OP5, not_30_out, not_31_out, not_32_out, OP1, OP0);
  and and_10 (and_10_out, OP5, not_33_out, OP3, not_34_out, OP1, OP0);
  and and_11 (and_11_out, OP5, not_35_out, OP3, not_36_out, not_37_out, not_38_out);
  and and_12 (and_12_out, not_39_out, not_40_out, not_41_out, not_42_out, not_43_out, not_44_out, not_45_out, not_46_out, not_47_out, not_48_out, not_49_out, not_50_out);
  and and_13 (and_13_out, not_51_out, not_52_out, not_53_out, not_54_out, not_55_out, not_56_out, not_57_out, not_58_out, not_59_out, not_60_out, F1, F0);
  and and_14 (and_14_out, not_61_out, not_62_out, not_63_out, not_64_out, not_65_out, not_66_out, not_67_out, not_68_out, not_69_out, not_70_out, F1, not_71_out);
  and and_15 (and_15_out, not_72_out, not_73_out, not_74_out, not_75_out, not_76_out, not_77_out, F5, not_78_out, not_79_out, not_80_out, not_81_out, not_82_out);
  and and_16 (and_16_out, not_83_out, not_84_out, not_85_out, not_86_out, not_87_out, not_88_out, F5, not_89_out, not_90_out, not_91_out, not_92_out, F0);
  and and_17 (and_17_out, not_93_out, not_94_out, not_95_out, not_96_out, not_97_out, not_98_out, F5, not_99_out, not_100_out, not_101_out, F1, not_102_out);
  and and_18 (and_18_out, not_103_out, not_104_out, not_105_out, not_106_out, not_107_out, not_108_out, F5, not_109_out, not_110_out, F2, not_111_out, not_112_out);
  and and_19 (and_19_out, not_113_out, not_114_out, not_115_out, not_116_out, not_117_out, not_118_out, F5, not_119_out, not_120_out, F2, not_121_out, F0);
  and and_20 (and_20_out, not_122_out, not_123_out, not_124_out, not_125_out, not_126_out, not_127_out, F5, not_128_out, not_129_out, F2, F1, F0);
  and and_21 (and_21_out, not_130_out, not_131_out, not_132_out, not_133_out, not_134_out, not_135_out, F5, not_136_out, F3, not_137_out, F1, not_138_out);
  and and_22 (and_22_out, not_139_out, not_140_out, not_141_out, not_142_out, not_143_out, not_144_out, F5, not_145_out, F3, not_146_out, F1, F0);
  and and_23 (and_23_out, not_147_out, not_148_out, not_149_out, not_150_out, OP1, OP0);
  and and_24 (and_24_out, not_151_out, not_152_out, OP3, not_153_out, not_154_out, not_155_out);
  and and_25 (and_25_out, not_156_out, not_157_out, OP3, OP2, not_158_out, not_159_out);
  and and_26 (and_26_out, not_160_out, not_161_out, OP3, not_162_out, not_163_out, OP0);
  and and_27 (and_27_out, not_164_out, not_165_out, OP3, not_166_out, OP1, not_167_out);
  and and_28 (and_28_out, not_168_out, not_169_out, OP3, OP2, not_170_out, OP0);
  and and_29 (and_29_out, OP5, not_171_out, not_172_out, not_173_out, OP1, OP0);
  and and_30 (and_30_out, not_174_out, not_175_out, not_176_out, not_177_out, not_178_out, not_179_out, not_180_out, not_181_out, not_182_out, F2, F1, not_183_out);
  and and_31 (and_31_out, not_184_out, not_185_out, not_186_out, not_187_out, not_188_out, not_189_out, not_190_out, not_191_out, not_192_out, F2, F1, F0);
  and and_32 (SysCALL, not_193_out, not_194_out, not_195_out, not_196_out, not_197_out, not_198_out, not_199_out, not_200_out, F3, F2, not_201_out, not_202_out);
  and and_33 (and_33_out, not_203_out, not_204_out, not_205_out, OP2, not_206_out, not_207_out);
  and and_34 (and_34_out, not_208_out, not_209_out, not_210_out, OP2, not_211_out, OP0);
  and and_35 (and_35_out, not_212_out, not_213_out, OP3, not_214_out, not_215_out, not_216_out);
  and and_36 (and_36_out, not_217_out, not_218_out, OP3, not_219_out, OP1, not_220_out);
  and and_37 (and_37_out, OP5, not_221_out, not_222_out, not_223_out, OP1, OP0);
  and and_38 (and_38_out, OP5, not_224_out, OP3, not_225_out, OP1, OP0);
  and and_39 (and_39_out, OP5, not_226_out, OP3, not_227_out, not_228_out, not_229_out);
  and and_40 (and_40_out, not_230_out, not_231_out, not_232_out, not_233_out, not_234_out, not_235_out, not_236_out, not_237_out, not_238_out, not_239_out, not_240_out, not_241_out);
  and and_41 (and_41_out, not_242_out, not_243_out, not_244_out, not_245_out, not_246_out, not_247_out, not_248_out, not_249_out, not_250_out, not_251_out, F1, F0);
  and and_42 (and_42_out, not_252_out, not_253_out, not_254_out, not_255_out, not_256_out, not_257_out, not_258_out, not_259_out, not_260_out, not_261_out, F1, not_262_out);
  and and_43 (and_43_out, not_263_out, not_264_out, not_265_out, not_266_out, not_267_out, not_268_out, F5, not_269_out, not_270_out, not_271_out, not_272_out, not_273_out);
  and and_44 (and_44_out, not_274_out, not_275_out, not_276_out, not_277_out, not_278_out, not_279_out, F5, not_280_out, not_281_out, not_282_out, not_283_out, F0);
  and and_45 (and_45_out, not_284_out, not_285_out, not_286_out, not_287_out, not_288_out, not_289_out, F5, not_290_out, not_291_out, not_292_out, F1, not_293_out);
  and and_46 (and_46_out, not_294_out, not_295_out, not_296_out, not_297_out, not_298_out, not_299_out, F5, not_300_out, not_301_out, F2, not_302_out, not_303_out);
  and and_47 (and_47_out, not_304_out, not_305_out, not_306_out, not_307_out, not_308_out, not_309_out, F5, not_310_out, not_311_out, F2, not_312_out, F0);
  and and_48 (and_48_out, not_313_out, not_314_out, not_315_out, not_316_out, not_317_out, not_318_out, F5, not_319_out, not_320_out, F2, F1, F0);
  and and_49 (and_49_out, not_321_out, not_322_out, not_323_out, not_324_out, not_325_out, not_326_out, F5, not_327_out, F3, not_328_out, F1, not_329_out);
  and and_50 (and_50_out, not_330_out, not_331_out, not_332_out, not_333_out, not_334_out, not_335_out, F5, not_336_out, F3, not_337_out, F1, F0);
  and and_51 (and_51_out, not_338_out, not_339_out, not_340_out, not_341_out, not_342_out, not_343_out, not_344_out, not_345_out, not_346_out, F2, F1, not_347_out);
  and and_52 (and_52_out, not_348_out, not_349_out, not_350_out, not_351_out, not_352_out, not_353_out, not_354_out, not_355_out, not_356_out, F2, F1, F0);
  and and_53 (BEQ, not_357_out, not_358_out, not_359_out, OP2, not_360_out, not_361_out);
  and and_54 (BNE, not_362_out, not_363_out, not_364_out, OP2, not_365_out, OP0);
  and and_55 (JR, not_366_out, not_367_out, not_368_out, not_369_out, not_370_out, not_371_out, not_372_out, not_373_out, F3, not_374_out, not_375_out, not_376_out);
  and and_56 (and_56_out, not_377_out, not_378_out, not_379_out, not_380_out, not_381_out, not_382_out, not_383_out, not_384_out, F3, not_385_out, not_386_out, not_387_out);
  and and_57 (and_57_out, not_388_out, not_389_out, not_390_out, not_391_out, OP1, not_392_out);
  and and_58 (and_58_out, not_393_out, not_394_out, not_395_out, not_396_out, OP1, OP0);
  and and_59 (JAL, not_397_out, not_398_out, not_399_out, not_400_out, OP1, OP0);
  or or_1 (MemWrite, and_2_out, and_3_out);
  or or_2 (ALU_SRC, and_4_out, and_5_out, and_6_out, and_7_out, and_8_out, and_9_out, and_10_out, and_11_out);
  or or_3 (SignedExt, and_33_out, and_34_out, and_35_out, and_36_out, and_37_out, and_38_out, and_39_out);
  or or_4 (JMP, and_56_out, and_57_out, and_58_out);
  or or_5 (RegWrite, and_12_out, and_13_out, and_14_out, and_15_out, and_16_out, and_17_out, and_18_out, and_19_out, and_20_out, and_21_out, and_22_out, and_23_out, and_24_out, and_25_out, and_26_out, and_27_out, and_28_out, and_29_out, and_30_out, and_31_out);
  or or_6 (RegDst, and_40_out, and_41_out, and_42_out, and_43_out, and_44_out, and_45_out, and_46_out, and_47_out, and_48_out, and_49_out, and_50_out, and_51_out, and_52_out);
endmodule

// ALU
module MIPS_ALU (
  input  [4:0] shamt,
  input  [31:0] X,
  input  [31:0] Y,
  input  [3:0] AluOP,
  output Equal,
  output [31:0] Result,
  output [31:0] Result_2
);

  wire [0:0] comparator_1_lt, comparator_2_lt;
  wire [31:0] adder_1_out, AND_out, divider_1_out, divider_1_rem, multiplier_1_cout, multiplier_1_out,
       NOR_out, OR_out, shifter_1_out, shifter_2_out, shifter_3_out, subtractor_1_out, XOR_out;

  assign AND_out = X & Y;  // AND_Gate AND, 32 bits wide
  assign OR_out = X | Y;  // OR_Gate OR, 32 bits wide
  Shifter #(.width(32)) shifter_1 (.in(Y), .\dist (shamt), .out(shifter_1_out));
  Shifter #(.width(32), .shift("ar")) shifter_2 (.in(Y), .\dist (shamt), .out(shifter_2_out));
  Shifter #(.width(32), .shift("lr")) shifter_3 (.in(Y), .\dist (shamt), .out(shifter_3_out));
  Multiplier #(.width(32)) multiplier_1 (.a(X), .b(Y), .out(multiplier_1_out), .cout(multiplier_1_cout));  // open: cin
  Divider #(.width(32)) divider_1 (.a(X), .b(Y), .out(divider_1_out), .rem(divider_1_rem));  // open: upper
  Adder #(.width(32)) adder_1 (.a(X), .b(Y), .out(adder_1_out));  // open: cin, cout
  Subtractor #(.width(32)) subtractor_1 (.a(X), .b(Y), .out(subtractor_1_out));  // open: bin, bout
  assign XOR_out = X ^ Y;  // XOR_Gate XOR, 32 bits wide
  assign NOR_out = ~(X | Y);  // NOR_Gate NOR, 32 bits wide
  Comparator #(.width(32)) comparator_1 (.a(X), .b(Y), .eq(Equal), .lt(comparator_1_lt[0]));  // open: gt
  Comparator #(.width(32), .mode("unsigned")) comparator_2 (.a(X), .b(Y), .lt(comparator_2_lt[0]));  // open: gt, eq
  Multiplexer #(.select(4), .width(32), .enable("false")) multiplexer_1 (
    .in0(shifter_1_out), .in1(shifter_2_out), .in2(shifter_3_out), .in3(multiplier_1_out),
    .in4(divider_1_out), .in5(adder_1_out), .in6(subtractor_1_out), .in7(AND_out), .in8(OR_out),
    .in9(XOR_out), .in10(NOR_out), .in11({{31{1'b0}}, comparator_1_lt[0]}),
    .in12({{31{1'b0}}, comparator_2_lt[0]}), .in13({32{1'b0}}), .in14({32{1'b0}}), .in15({32{1'b0}}),
    .out(Result), .sel(AluOP));
  Multiplexer #(.select(4), .width(32), .enable("false")) multiplexer_2 (
    .in0({32{1'b0}}), .in1({32{1'b0}}), .in2({32{1'b0}}), .in3(multiplier_1_cout), .in4(divider_1_rem),
    .in5({32{1'b0}}), .in6({32{1'b0}}), .in7({32{1'b0}}), .in8({32{1'b0}}), .in9({32{1'b0}}),
    .in10({32{1'b0}}), .in11({32{1'b0}}), .in12({32{1'b0}}), .in13({32{1'b0}}), .in14({32{1'b0}}),
    .in15({32{1'b0}}), .out(Result_2), .sel(AluOP));

  // Other names for the same wires on the sheet: Result2[31:0] = Result_2; S[3:0] = AluOP

  // Notes on the sheet:
  //   不要改变此引脚区域内容，也不要改变ALU封装形式
  //   输入引脚
  //   输出引脚
endmodule

module MIPS_Regifile (
  input  [31:0] Din,
  input  Clk,
  input  WE,
  input  [4:0] R1_num,
  input  [4:0] W_num,
  input  [4:0] R2_num,
  output [31:0] R1,
  output [31:0] R2
);

  // RegisterFile registerfile_1: pin names not known; wires that end beside it: Din, Clk, WE, W_num, R1_num, R2_num, R1, R2
endmodule

module \理想流水线  (
);

  wire AluSrcB, and_1_out, and_6_out, and_7_out, Beq, beq_suc, Beqout, BLTZ, bltz_suc, BLTZout, Bne, bne_suc,
       Bneout, CLK, clkne, comparator_3_eq, equal, ex_mem_1_jal_2, ex_mem_1_memtoreg_2, ex_mem_1_memwrite_2,
       ex_mem_1_regwrite_2, ex_mem_1_sb_2, ex_mem_1_syscall10_2, ex_mem_1_syscall34_2, ex_mem_1_syscall_2,
       Go, GoCancel__on_fall_q, GoOut, GoUsed_q, id_ex_1_alusrc_2, id_ex_1_memtoreg_2, id_ex_1_memwrite_2,
       id_ex_1_regwrite_2, id_ex_1_sb_2, id_ex_1_sv_2, id_ex_1_syscall10_2, id_ex_1_syscall34_2,
       id_ex_1_syscall_2, IfBranch, ifJAL, IR1, IR2, IR3, is34, JAL, JALout, JMP, JMPout, JR, JRout, less,
       mem_wb_1_memtoreg_2, mem_wb_1_syscall10_2, mem_wb_1_syscall34_2, mem_wb_1_syscall_2, MemToReg,
       MemWrite, or_1_out, or_2_out, or_3_out, RegWrite, RegWriteOut, RST, SB, SignedExt, SV, syscall,
       Syscall10, Syscall34, W1, W2, W3, \硬布线控制器_1_regdst ;
  wire [1:0] PCsel;
  wire [1:1] mips_alu_1_result;
  wire [3:0] AluOP, decoder_1_out0, ex_mem_1_memselsb_2, id_ex_1_aluop_2, multiplexer_12_out;
  wire [4:0] ex_mem_1_regwriteaddr_2, id_ex_1_r1out, id_ex_1_regwriteaddr_2, mem_wb_1_regwriteaddr_2,
       multiplexer_3_out, multiplexer_4_out, multiplexer_5_out, multiplexer_6_out, multiplexer_10_out,
       shifter_3_out;
  wire [11:0] EX_PC, ID_PC, IF_PC, MEM_PC, WB_PC;
  wire [15:0] \LoadUse次数 , \总周期数 , \插入气泡数 , \无条件分支数 , \条件分支成功数 ;
  wire [19:0] ex_mem_1_alures_2_2;
  wire [31:0] adder_1_out, adder_2_out, bit_extender_1_out, ex_mem_1_alures_2, ex_mem_1_irout,
       ex_mem_1_pc_4out, ex_mem_1_pcout, ex_mem_1_r2out, ex_mem_1_sbmemdata_2, id_ex_1_immout, id_ex_1_irout,
       id_ex_1_pc_4out, id_ex_1_pcout, id_ex_1_r2out, if_id_1_irout, if_id_1_pc_4out, if_id_1_pcout, LedData,
       mem_wb_1_alures_2, mem_wb_1_memdata_2, mem_wb_1_pc_4out, mips_ram_1_p7, mips_regifile_1_r1,
       multiplexer_1_out, multiplexer_2_out, multiplexer_7_out, multiplexer_8_out, multiplexer_9_out,
       multiplexer_11_out, multiplexer_13_out, PC_q, R2out, rom_1_data, shifter_1_out, shifter_2_out;
  wire [31:2] mips_alu_1_result_2;
  wire [31:5] id_ex_1_r1out_2;

  Button \u_总复位  (.out(RST));
  Button _1 (.out(IR1));
  Button _2 (.out(IR2));
  Button _3 (.out(IR3));
  Button \u_继续运行  (.out(Go));
  LED led_1 (.in(W1));
  LED led_2 (.in(W2));
  LED led_3 (.in(W3));
  Multiplexer #(.select(2), .width(32), .enable("false")) multiplexer_1 (
    .in0({id_ex_1_r1out_2, id_ex_1_r1out}), .in1(id_ex_1_pc_4out), .in2(adder_2_out),
    .in3({id_ex_1_pcout[31:28], id_ex_1_irout[25:0], 2'b00}), .out(multiplexer_1_out), .sel(PCsel));
  Hex_Digit_Display hex_digit_display_1 (.value(LedData[31:28]));  // open: dp
  Multiplexer #(.width(32), .enable("false")) multiplexer_2 (
    .in0(adder_1_out), .in1(multiplexer_1_out), .out(multiplexer_2_out), .sel(IfBranch));
  Hex_Digit_Display hex_digit_display_2 (.value(LedData[23:20]));  // open: dp
  Hex_Digit_Display hex_digit_display_3 (.value(LedData[27:24]));  // open: dp
  Register #(.width(32)) PC (.D(multiplexer_2_out), .en(clkne), .Q(PC_q), .clk(CLK), .clr(RST));
  Adder #(.width(32)) adder_1 (.a(PC_q), .b(32'h4), .out(adder_1_out));  // open: cin, cout
  Hex_Digit_Display hex_digit_display_4 (.value(LedData[19:16]));  // open: dp
  Hex_Digit_Display hex_digit_display_5 (.value(LedData[15:12]));  // open: dp
  Hex_Digit_Display hex_digit_display_6 (.value(LedData[11:8]));  // open: dp
  Hex_Digit_Display hex_digit_display_7 (.value(LedData[7:4]));  // open: dp
  Clock clock_1 (.out(CLK));
  ROM #(.addrWidth(10), .dataWidth(32)) rom_1 (.addr(PC_q[11:2]), .data(rom_1_data));  // open: sel
  Hex_Digit_Display hex_digit_display_8 (.value(LedData[3:0]));  // open: dp
  IF_ID if_id_1 (
    .IRin(rom_1_data), .IRout(if_id_1_irout), .PCin(PC_q), .PCout(if_id_1_pcout), .PC_4in(adder_1_out),
    .PC_4out(if_id_1_pc_4out), .WE(clkne), .Clk(CLK), .Rst(RST));  // open: BHTData, BHTdata_2
  // Probe on \总周期数 
  // Probe on \无条件分支数 
  // Probe on \条件分支成功数 
  // Probe on \插入气泡数 
  // Probe on \LoadUse次数 
  // Probe on IF_PC
  // Probe on ID_PC
  // Probe on EX_PC
  // Probe on MEM_PC
  \硬布线控制器  \u_硬布线控制器_1  (
    .Func(if_id_1_irout[5:0]), .OP(if_id_1_irout[31:26]), .ALU_OP(AluOP), .MemToReg(MemToReg),
    .MemWrite(MemWrite), .ALU_SRC(AluSrcB), .RegWrite(RegWrite), .SysCALL(syscall), .SignedExt(SignedExt),
    .RegDst(\硬布线控制器_1_regdst ), .JR(JR), .JMP(JMP), .Beq(Beq), .JAL(JAL), .Bne(Bne), .BLTZ(BLTZ), .SB(SB),
    .SV(SV));
  Multiplexer #(.width(5), .enable("false")) multiplexer_3 (
    .in0(if_id_1_irout[20:16]), .in1(if_id_1_irout[15:11]), .out(multiplexer_3_out), .sel(\硬布线控制器_1_regdst ));
  and and_1 (and_1_out, SignedExt, if_id_1_irout[15]);
  assign bit_extender_1_out = {{16{and_1_out}}, if_id_1_irout[15:0]};  // Bit_Extender bit_extender_1
  Comparator #(.width(32), .mode("unsigned")) comparator_1 (.a(32'ha), .b(R2out), .eq(Syscall10));  // open: gt, lt
  Comparator #(.width(32), .mode("unsigned")) comparator_2 (.a(32'h22), .b(R2out), .eq(is34));  // open: gt, lt
  and and_2 (Syscall34, is34, syscall);
  // Probe on WB_PC
  Multiplexer #(.width(5), .enable("false")) multiplexer_4 (
    .in0(if_id_1_irout[25:21]), .in1(5'b00100), .out(multiplexer_4_out), .sel(Syscall34));
  Multiplexer #(.width(5), .enable("false")) multiplexer_5 (
    .in0(if_id_1_irout[20:16]), .in1(5'b00010), .out(multiplexer_5_out), .sel(syscall));
  Multiplexer #(.width(5), .enable("false")) multiplexer_6 (
    .in0(multiplexer_3_out), .in1({5{1'b1}}), .out(multiplexer_6_out), .sel(JAL));
  Multiplexer #(.width(32), .enable("false")) multiplexer_7 (
    .in0(multiplexer_13_out), .in1(mem_wb_1_pc_4out), .out(multiplexer_7_out), .sel(ifJAL));
  MIPS_Regifile mips_regifile_1 (
    .Din(multiplexer_7_out), .Clk(CLK), .R1(mips_regifile_1_r1), .R2(R2out), .WE(RegWriteOut),
    .W_num(mem_wb_1_regwriteaddr_2), .R1_num(multiplexer_4_out), .R2_num(multiplexer_5_out));
  Counter #(.width(16), .max('hffff)) counter_1 (
    .count(clkne), .Q(\总周期数 ), .clk(CLK), .clr(RST));  // open: load, D, carry
  D_Flip_Flop GoPressed (.clk(Go), .D(1'b1), .Q(GoOut), .reset(GoCancel__on_fall_q));  // open: Qn, preset, en
  Counter #(.width(16), .max('hffff)) counter_2 (
    .count(or_1_out), .Q(\条件分支成功数 ), .clk(CLK), .clr(RST));  // open: load, D, carry
  or or_1 (or_1_out, bne_suc, bltz_suc, beq_suc);
  D_Flip_Flop GoUsed (.clk(CLK), .D(GoOut), .Q(GoUsed_q), .reset(GoCancel__on_fall_q));  // open: Qn, preset, en
  or or_2 (or_2_out, JAL, JR, JMP);
  D_Flip_Flop #(.trigger("falling")) GoCancel__on_fall (
    .clk(CLK), .D(GoUsed_q), .Q(GoCancel__on_fall_q), .reset(RST));  // open: Qn, preset, en
  Counter #(.width(16), .max('hffff)) counter_3 (
    .count(or_2_out), .Q(\无条件分支数 ), .clk(CLK), .clr(RST));  // open: load, D, carry
  ID_EX id_ex_1 (
    .IRin(if_id_1_irout), .IRout(id_ex_1_irout), .PCin(if_id_1_pcout), .PCout(id_ex_1_pcout),
    .PC_4in(if_id_1_pc_4out), .PC_4out(id_ex_1_pc_4out), .WE(clkne), .Clk(CLK), .Rst(RST),
    .Immin(bit_extender_1_out), .Immout(id_ex_1_immout), .MemToReg(MemToReg),
    .MemToReg_2(id_ex_1_memtoreg_2), .MemWrite(MemWrite), .MemWrite_2(id_ex_1_memwrite_2), .AluSRC(AluSrcB),
    .AluSRC_2(id_ex_1_alusrc_2), .RegWrite(RegWrite), .RegWrite_2(id_ex_1_regwrite_2), .Syscall(syscall),
    .Syscall_2(id_ex_1_syscall_2), .SignedExt(SignedExt), .RegDst(\硬布线控制器_1_regdst ), .Beq(Beq),
    .Beq_2(Beqout), .Bne(Bne), .Bne_2(Bneout), .JR(JR), .JR_2(JRout), .JMP(JMP), .JMP_2(JMPout), .JAL(JAL),
    .JAL_2(JALout), .BLTZ(BLTZ), .BLTZ_2(BLTZout), .SB(SB), .SB_2(id_ex_1_sb_2), .SV(SV),
    .SV_2(id_ex_1_sv_2), .AluOP(AluOP), .AluOP_2(id_ex_1_aluop_2), .R1in(mips_regifile_1_r1),
    .R1out({id_ex_1_r1out_2, id_ex_1_r1out}), .R2in(R2out), .R2out(id_ex_1_r2out),
    .RegWriteAddr(multiplexer_6_out), .RegWriteAddr_2(id_ex_1_regwriteaddr_2), .Syscall34(is34),
    .Syscall34_2(id_ex_1_syscall34_2), .Syscall10(Syscall10), .Syscall10_2(id_ex_1_syscall10_2));  // open: SignedExt_2, RegDst_2, R1_sel, R1_sel_2, R2_sel, R2_sel_2, BHTData, BHTData_2
  Shifter #(.width(32)) shifter_1 (.in(id_ex_1_immout), .\dist (5'b00010), .out(shifter_1_out));
  Adder #(.width(32)) adder_2 (.a(id_ex_1_pc_4out), .b(shifter_1_out), .out(adder_2_out));  // open: cin, cout
  Multiplexer #(.width(32), .enable("false")) multiplexer_8 (
    .in0(multiplexer_9_out), .in1({32{1'b0}}), .out(multiplexer_8_out), .sel(BLTZout));
  Multiplexer #(.width(32), .enable("false")) multiplexer_9 (
    .in0(id_ex_1_r2out), .in1(id_ex_1_immout), .out(multiplexer_9_out), .sel(id_ex_1_alusrc_2));
  Multiplexer #(.width(5), .enable("false")) multiplexer_10 (
    .in0(id_ex_1_irout[10:6]), .in1(id_ex_1_r1out), .out(multiplexer_10_out), .sel(id_ex_1_sv_2));
  Register #(.width(32)) register_1 (
    .D({id_ex_1_r1out_2, id_ex_1_r1out}), .en(id_ex_1_syscall34_2), .Q(LedData), .clk(CLK), .clr(RST));
  Shifter #(.width(32)) shifter_2 (.in(id_ex_1_r2out), .\dist (shifter_3_out), .out(shifter_2_out));
  temp temp_1 (
    .jmp(JMPout), .jr(JRout), .jal(JALout), .beq(beq_suc), .bne(bne_suc), .bltz(bltz_suc), .sel1(PCsel[1]),
    .sel0(PCsel[0]));
  Comparator #(.width(2)) comparator_3 (.a(PCsel), .b(2'b01), .eq(comparator_3_eq));  // open: gt, lt
  not not_1 (IfBranch, comparator_3_eq);
  MIPS_ALU mips_alu_1 (
    .X({id_ex_1_r1out_2, id_ex_1_r1out}), .Y(multiplexer_8_out), .AluOP(id_ex_1_aluop_2), .Equal(equal),
    .Result({mips_alu_1_result_2, mips_alu_1_result[1], less}), .shamt(multiplexer_10_out));  // open: Result_2
  Shifter #(.width(5)) shifter_3 (.in({3'b000, mips_alu_1_result[1], less}), .\dist (3'b011), .out(shifter_3_out));
  Decoder #(.select(2)) decoder_1 (
    .out0(decoder_1_out0[0]), .out1(decoder_1_out0[1]), .out2(decoder_1_out0[2]), .out3(decoder_1_out0[3]),
    .sel({mips_alu_1_result[1], less}));  // open: en
  and and_3 (beq_suc, Beqout, equal);
  and and_4 (bne_suc, Bneout, ~equal);  // AND_Gate
  and and_5 (bltz_suc, BLTZout, less);
  EX_MEM ex_mem_1 (
    .MemToReg(id_ex_1_memtoreg_2), .MemToReg_2(ex_mem_1_memtoreg_2), .MemWrite(id_ex_1_memwrite_2),
    .MemWrite_2(ex_mem_1_memwrite_2), .IRin(id_ex_1_irout), .IRout(ex_mem_1_irout),
    .RegWrite(id_ex_1_regwrite_2), .RegWrite_2(ex_mem_1_regwrite_2), .PCin(id_ex_1_pcout),
    .PCout(ex_mem_1_pcout), .Syscall(id_ex_1_syscall_2), .Syscall_2(ex_mem_1_syscall_2),
    .PC_4in(id_ex_1_pc_4out), .PC_4out(ex_mem_1_pc_4out), .RegWriteAddr(id_ex_1_regwriteaddr_2),
    .RegWriteAddr_2(ex_mem_1_regwriteaddr_2), .WE(clkne), .Clk(CLK), .Rst(RST),
    .AluRes({mips_alu_1_result_2, mips_alu_1_result[1], less}),
    .AluRes_2({ex_mem_1_alures_2[31:22], ex_mem_1_alures_2_2, ex_mem_1_alures_2[1:0]}), .R2in(id_ex_1_r2out),
    .R2out(ex_mem_1_r2out), .SBMemdata(shifter_2_out), .SBMemdata_2(ex_mem_1_sbmemdata_2), .SB(id_ex_1_sb_2),
    .SB_2(ex_mem_1_sb_2), .MemselSB(decoder_1_out0), .MemselSB_2(ex_mem_1_memselsb_2), .JAL(JALout),
    .JAL_2(ex_mem_1_jal_2), .Syscall34(id_ex_1_syscall34_2), .Syscall34_2(ex_mem_1_syscall34_2),
    .Syscall10(id_ex_1_syscall10_2), .Syscall10_2(ex_mem_1_syscall10_2));  // open: R1in, R1out
  Multiplexer #(.width(32), .enable("false")) multiplexer_11 (
    .in0(ex_mem_1_r2out), .in1(ex_mem_1_sbmemdata_2), .out(multiplexer_11_out), .sel(ex_mem_1_sb_2));
  Multiplexer #(.width(4), .enable("false")) multiplexer_12 (
    .in0(4'b1111), .in1(ex_mem_1_memselsb_2), .out(multiplexer_12_out), .sel(ex_mem_1_sb_2));
  // MIPS_RAM mips_ram_1: pin names not known; wires that end beside it: ex_mem_1_alures_2_2, multiplexer_11_out, ex_mem_1_memwrite_2, multiplexer_12_out, CLK, RST, mips_ram_1_p7
  MEM_WB mem_wb_1 (
    .MemToReg(ex_mem_1_memtoreg_2), .MemToReg_2(mem_wb_1_memtoreg_2), .IRin(ex_mem_1_irout),
    .MemData(mips_ram_1_p7), .MemData_2(mem_wb_1_memdata_2), .RegWrite(ex_mem_1_regwrite_2),
    .RegWrite_2(RegWriteOut), .PCin(ex_mem_1_pcout), .Syscall(ex_mem_1_syscall_2),
    .Syscall_2(mem_wb_1_syscall_2), .PC_4in(ex_mem_1_pc_4out), .PC_4out(mem_wb_1_pc_4out),
    .RegWriteAddr(ex_mem_1_regwriteaddr_2), .RegWriteAddr_2(mem_wb_1_regwriteaddr_2),
    .AluRes({ex_mem_1_alures_2[31:22], ex_mem_1_alures_2_2, ex_mem_1_alures_2[1:0]}),
    .AluRes_2(mem_wb_1_alures_2), .WE(clkne), .Clk(CLK), .Rst(RST), .JAL(ex_mem_1_jal_2), .JAL_2(ifJAL),
    .Syscall34(ex_mem_1_syscall34_2), .Syscall34_2(mem_wb_1_syscall34_2), .Syscall10(ex_mem_1_syscall10_2),
    .Syscall10_2(mem_wb_1_syscall10_2));  // open: IRout, PCout, R1, R1_2
  Multiplexer #(.width(32), .enable("false")) multiplexer_13 (
    .in0(mem_wb_1_alures_2), .in1(mem_wb_1_memdata_2), .out(multiplexer_13_out), .sel(mem_wb_1_memtoreg_2));
  or or_3 (or_3_out, mem_wb_1_syscall10_2, and_7_out);
  not not_2 (clkne, and_6_out);
  and and_6 (and_6_out, or_3_out, mem_wb_1_syscall_2);
  and and_7 (and_7_out, ~mem_wb_1_syscall34_2, ~GoOut);  // AND_Gate

  // Notes on the sheet:
  //   中断源
  //   中断等待指示
  //   数码管输出
  //   指令存储器
  //   contents of rom_1 (hex, n*v repeats v):
  //   20100000 20110001 20120002 20130003 36100000 36310001 36520002 36730003 ae100000 ae110004 ae120008
  //   ae13000c 2002000a 0 0 0 c
  //   指令字
  //   OP
  //   Func
  //   rs
  //   rt
  //   rd
  //   10#10 (exit)
  //   10#34 (print hex)
  //   流水调试日志用
  //   Beq
  //   JMP
  //   JR
  //   Bne
  //   OP
  //   JAL
  //   Func
  //   Syscall
  //   Syscall34
  //   MemToReg
  //   MemWrite
  //   AluOP
  //   AluSrcB
  //   RegWrite
  //   RegDst
endmodule

// 源寄存器使用情况
module \源寄存器使用情况  (
  input  OP0,
  input  OP1,
  input  OP2,
  input  OP3,
  input  OP4,
  input  OP5,
  input  F0,
  input  F1,
  input  F2,
  input  F3,
  input  F4,
  input  F5,
  output R1_Used,
  output R2_Used
);

  wire and_1_out, and_2_out, and_3_out, and_4_out, and_5_out, and_6_out, and_7_out, and_8_out, and_9_out,
       and_10_out, and_11_out, and_12_out, and_13_out, and_14_out, and_15_out, and_16_out, and_17_out,
       and_18_out, and_19_out, and_20_out, and_21_out, and_22_out, and_23_out, and_24_out, and_25_out,
       and_26_out, and_27_out, and_28_out, and_29_out, and_30_out, and_31_out, and_32_out, and_33_out,
       and_34_out, and_35_out, and_36_out, and_37_out, and_38_out, and_39_out, and_40_out, and_41_out,
       not_1_out, not_2_out, not_3_out, not_4_out, not_5_out, not_6_out, not_7_out, not_8_out, not_9_out,
       not_10_out, not_11_out, not_12_out, not_13_out, not_14_out, not_15_out, not_16_out, not_17_out,
       not_18_out, not_19_out, not_20_out, not_21_out, not_22_out, not_23_out, not_24_out, not_25_out,
       not_26_out, not_27_out, not_28_out, not_29_out, not_30_out, not_31_out, not_32_out, not_33_out,
       not_34_out, not_35_out, not_36_out, not_37_out, not_38_out, not_39_out, not_40_out, not_41_out,
       not_42_out, not_43_out, not_44_out, not_45_out, not_46_out, not_47_out, not_48_out, not_49_out,
       not_50_out, not_51_out, not_52_out, not_53_out, not_54_out, not_55_out, not_56_out, not_57_out,
       not_58_out, not_59_out, not_60_out, not_61_out, not_62_out, not_63_out, not_64_out, not_65_out,
       not_66_out, not_67_out, not_68_out, not_69_out, not_70_out, not_71_out, not_72_out, not_73_out,
       not_74_out, not_75_out, not_76_out, not_77_out, not_78_out, not_79_out, not_80_out, not_81_out,
       not_82_out, not_83_out, not_84_out, not_85_out, not_86_out, not_87_out, not_88_out, not_89_out,
       not_90_out, not_91_out, not_92_out, not_93_out, not_94_out, not_95_out, not_96_out, not_97_out,
       not_98_out, not_99_out, not_100_out, not_101_out, not_102_out, not_103_out, not_104_out, not_105_out,
       not_106_out, not_107_out, not_108_out, not_109_out, not_110_out, not_111_out, not_112_out,
       not_113_out, not_114_out, not_115_out, not_116_out, not_117_out, not_118_out, not_119_out,
       not_120_out, not_121_out, not_122_out, not_123_out, not_124_out, not_125_out, not_126_out,
       not_127_out, not_128_out, not_129_out, not_130_out, not_131_out, not_132_out, not_133_out,
       not_134_out, not_135_out, not_136_out, not_137_out, not_138_out, not_139_out, not_140_out,
       not_141_out, not_142_out, not_143_out, not_144_out, not_145_out, not_146_out, not_147_out,
       not_148_out, not_149_out, not_150_out, not_151_out, not_152_out, not_153_out, not_154_out,
       not_155_out, not_156_out, not_157_out, not_158_out, not_159_out, not_160_out, not_161_out,
       not_162_out, not_163_out, not_164_out, not_165_out, not_166_out, not_167_out, not_168_out,
       not_169_out, not_170_out, not_171_out, not_172_out, not_173_out, not_174_out, not_175_out,
       not_176_out, not_177_out, not_178_out, not_179_out, not_180_out, not_181_out, not_182_out,
       not_183_out, not_184_out, not_185_out, not_186_out, not_187_out, not_188_out, not_189_out,
       not_190_out, not_191_out, not_192_out, not_193_out, not_194_out, not_195_out, not_196_out,
       not_197_out, not_198_out, not_199_out, not_200_out, not_201_out, not_202_out, not_203_out,
       not_204_out, not_205_out, not_206_out, not_207_out, not_208_out, not_209_out, not_210_out,
       not_211_out, not_212_out, not_213_out, not_214_out, not_215_out, not_216_out, not_217_out,
       not_218_out, not_219_out, not_220_out, not_221_out, not_222_out, not_223_out, not_224_out,
       not_225_out, not_226_out, not_227_out, not_228_out, not_229_out, not_230_out, not_231_out,
       not_232_out, not_233_out, not_234_out, not_235_out, not_236_out, not_237_out, not_238_out,
       not_239_out, not_240_out, not_241_out, not_242_out, not_243_out, not_244_out, not_245_out,
       not_246_out, not_247_out, not_248_out, not_249_out, not_250_out, not_251_out, not_252_out,
       not_253_out, not_254_out, not_255_out, not_256_out, not_257_out, not_258_out, not_259_out,
       not_260_out, not_261_out, not_262_out, not_263_out, not_264_out, not_265_out, not_266_out,
       not_267_out, not_268_out, not_269_out, not_270_out, not_271_out, not_272_out, not_273_out,
       not_274_out, not_275_out, not_276_out, not_277_out, not_278_out, not_279_out, not_280_out,
       not_281_out, not_282_out, not_283_out, not_284_out, not_285_out, not_286_out, not_287_out,
       not_288_out, not_289_out, not_290_out, not_291_out, not_292_out, not_293_out, not_294_out,
       not_295_out, not_296_out, not_297_out, not_298_out, not_299_out, not_300_out, not_301_out,
       not_302_out, not_303_out, not_304_out, not_305_out, not_306_out, not_307_out, not_308_out,
       not_309_out, not_310_out;

  not not_1 (not_1_out, OP5);
  not not_2 (not_2_out, OP4);
  not not_3 (not_3_out, OP3);
  not not_4 (not_4_out, OP2);
  not not_5 (not_5_out, OP1);
  not not_6 (not_6_out, OP0);
  not not_7 (not_7_out, F4);
  not not_8 (not_8_out, F3);
  not not_9 (not_9_out, F2);
  not not_10 (not_10_out, F1);
  not not_11 (not_11_out, F0);
  not not_12 (not_12_out, OP5);
  not not_13 (not_13_out, OP4);
  not not_14 (not_14_out, OP3);
  not not_15 (not_15_out, OP2);
  not not_16 (not_16_out, OP1);
  not not_17 (not_17_out, OP0);
  not not_18 (not_18_out, F4);
  not not_19 (not_19_out, F3);
  not not_20 (not_20_out, F2);
  not not_21 (not_21_out, F1);
  not not_22 (not_22_out, OP5);
  not not_23 (not_23_out, OP4);
  not not_24 (not_24_out, OP3);
  not not_25 (not_25_out, OP2);
  not not_26 (not_26_out, OP1);
  not not_27 (not_27_out, OP0);
  not not_28 (not_28_out, F4);
  not not_29 (not_29_out, F3);
  not not_30 (not_30_out, F2);
  not not_31 (not_31_out, F0);
  not not_32 (not_32_out, OP5);
  not not_33 (not_33_out, OP4);
  not not_34 (not_34_out, OP3);
  not not_35 (not_35_out, OP2);
  not not_36 (not_36_out, OP1);
  not not_37 (not_37_out, OP0);
  not not_38 (not_38_out, F4);
  not not_39 (not_39_out, F3);
  not not_40 (not_40_out, F1);
  not not_41 (not_41_out, F0);
  not not_42 (not_42_out, OP5);
  not not_43 (not_43_out, OP4);
  not not_44 (not_44_out, OP3);
  not not_45 (not_45_out, OP2);
  not not_46 (not_46_out, OP1);
  not not_47 (not_47_out, OP0);
  not not_48 (not_48_out, F4);
  not not_49 (not_49_out, F3);
  not not_50 (not_50_out, F1);
  not not_51 (not_51_out, OP5);
  not not_52 (not_52_out, OP4);
  not not_53 (not_53_out, OP3);
  not not_54 (not_54_out, OP2);
  not not_55 (not_55_out, OP1);
  not not_56 (not_56_out, OP0);
  not not_57 (not_57_out, F4);
  not not_58 (not_58_out, F3);
  not not_59 (not_59_out, OP5);
  not not_60 (not_60_out, OP4);
  not not_61 (not_61_out, OP3);
  not not_62 (not_62_out, OP2);
  not not_63 (not_63_out, OP1);
  not not_64 (not_64_out, OP0);
  not not_65 (not_65_out, F4);
  not not_66 (not_66_out, F2);
  not not_67 (not_67_out, F0);
  not not_68 (not_68_out, OP5);
  not not_69 (not_69_out, OP4);
  not not_70 (not_70_out, OP3);
  not not_71 (not_71_out, OP2);
  not not_72 (not_72_out, OP1);
  not not_73 (not_73_out, OP0);
  not not_74 (not_74_out, F4);
  not not_75 (not_75_out, F2);
  not not_76 (not_76_out, OP5);
  not not_77 (not_77_out, OP4);
  not not_78 (not_78_out, OP3);
  not not_79 (not_79_out, OP2);
  not not_80 (not_80_out, OP1);
  not not_81 (not_81_out, OP0);
  not not_82 (not_82_out, F5);
  not not_83 (not_83_out, F4);
  not not_84 (not_84_out, F2);
  not not_85 (not_85_out, F1);
  not not_86 (not_86_out, F0);
  not not_87 (not_87_out, OP5);
  not not_88 (not_88_out, OP4);
  not not_89 (not_89_out, OP3);
  not not_90 (not_90_out, OP2);
  not not_91 (not_91_out, OP1);
  not not_92 (not_92_out, OP0);
  not not_93 (not_93_out, F5);
  not not_94 (not_94_out, F4);
  not not_95 (not_95_out, F1);
  not not_96 (not_96_out, F0);
  not not_97 (not_97_out, OP5);
  not not_98 (not_98_out, OP4);
  not not_99 (not_99_out, OP3);
  not not_100 (not_100_out, OP1);
  not not_101 (not_101_out, OP0);
  not not_102 (not_102_out, OP5);
  not not_103 (not_103_out, OP4);
  not not_104 (not_104_out, OP3);
  not not_105 (not_105_out, OP1);
  not not_106 (not_106_out, OP5);
  not not_107 (not_107_out, OP4);
  not not_108 (not_108_out, OP2);
  not not_109 (not_109_out, OP1);
  not not_110 (not_110_out, OP0);
  not not_111 (not_111_out, OP5);
  not not_112 (not_112_out, OP4);
  not not_113 (not_113_out, OP1);
  not not_114 (not_114_out, OP0);
  not not_115 (not_115_out, OP5);
  not not_116 (not_116_out, OP4);
  not not_117 (not_117_out, OP2);
  not not_118 (not_118_out, OP1);
  not not_119 (not_119_out, OP5);
  not not_120 (not_120_out, OP4);
  not not_121 (not_121_out, OP2);
  not not_122 (not_122_out, OP0);
  not not_123 (not_123_out, OP5);
  not not_124 (not_124_out, OP4);
  not not_125 (not_125_out, OP1);
  not not_126 (not_126_out, OP4);
  not not_127 (not_127_out, OP3);
  not not_128 (not_128_out, OP2);
  not not_129 (not_129_out, OP4);
  not not_130 (not_130_out, OP2);
  not not_131 (not_131_out, OP5);
  not not_132 (not_132_out, OP4);
  not not_133 (not_133_out, OP3);
  not not_134 (not_134_out, OP2);
  not not_135 (not_135_out, OP1);
  not not_136 (not_136_out, OP0);
  not not_137 (not_137_out, F5);
  not not_138 (not_138_out, F4);
  not not_139 (not_139_out, F3);
  not not_140 (not_140_out, F0);
  not not_141 (not_141_out, OP5);
  not not_142 (not_142_out, OP4);
  not not_143 (not_143_out, OP3);
  not not_144 (not_144_out, OP2);
  not not_145 (not_145_out, OP1);
  not not_146 (not_146_out, OP0);
  not not_147 (not_147_out, F5);
  not not_148 (not_148_out, F4);
  not not_149 (not_149_out, F3);
  not not_150 (not_150_out, OP4);
  not not_151 (not_151_out, OP2);
  not not_152 (not_152_out, OP1);
  not not_153 (not_153_out, OP0);
  not not_154 (not_154_out, OP5);
  not not_155 (not_155_out, OP4);
  not not_156 (not_156_out, OP3);
  not not_157 (not_157_out, OP2);
  not not_158 (not_158_out, OP1);
  not not_159 (not_159_out, OP5);
  not not_160 (not_160_out, OP4);
  not not_161 (not_161_out, OP3);
  not not_162 (not_162_out, OP2);
  not not_163 (not_163_out, OP1);
  not not_164 (not_164_out, OP0);
  not not_165 (not_165_out, F5);
  not not_166 (not_166_out, F4);
  not not_167 (not_167_out, F3);
  not not_168 (not_168_out, F2);
  not not_169 (not_169_out, F1);
  not not_170 (not_170_out, F0);
  not not_171 (not_171_out, OP5);
  not not_172 (not_172_out, OP4);
  not not_173 (not_173_out, OP3);
  not not_174 (not_174_out, OP2);
  not not_175 (not_175_out, OP1);
  not not_176 (not_176_out, OP0);
  not not_177 (not_177_out, F5);
  not not_178 (not_178_out, F4);
  not not_179 (not_179_out, F3);
  not not_180 (not_180_out, F2);
  not not_181 (not_181_out, OP5);
  not not_182 (not_182_out, OP4);
  not not_183 (not_183_out, OP3);
  not not_184 (not_184_out, OP2);
  not not_185 (not_185_out, OP1);
  not not_186 (not_186_out, OP0);
  not not_187 (not_187_out, F5);
  not not_188 (not_188_out, F4);
  not not_189 (not_189_out, F3);
  not not_190 (not_190_out, F2);
  not not_191 (not_191_out, F0);
  not not_192 (not_192_out, OP5);
  not not_193 (not_193_out, OP4);
  not not_194 (not_194_out, OP3);
  not not_195 (not_195_out, OP2);
  not not_196 (not_196_out, OP1);
  not not_197 (not_197_out, OP0);
  not not_198 (not_198_out, F4);
  not not_199 (not_199_out, F3);
  not not_200 (not_200_out, F2);
  not not_201 (not_201_out, F1);
  not not_202 (not_202_out, F0);
  not not_203 (not_203_out, OP5);
  not not_204 (not_204_out, OP4);
  not not_205 (not_205_out, OP3);
  not not_206 (not_206_out, OP2);
  not not_207 (not_207_out, OP1);
  not not_208 (not_208_out, OP0);
  not not_209 (not_209_out, F4);
  not not_210 (not_210_out, F3);
  not not_211 (not_211_out, F2);
  not not_212 (not_212_out, F1);
  not not_213 (not_213_out, OP5);
  not not_214 (not_214_out, OP4);
  not not_215 (not_215_out, OP3);
  not not_216 (not_216_out, OP2);
  not not_217 (not_217_out, OP1);
  not not_218 (not_218_out, OP0);
  not not_219 (not_219_out, F4);
  not not_220 (not_220_out, F3);
  not not_221 (not_221_out, F2);
  not not_222 (not_222_out, F0);
  not not_223 (not_223_out, OP5);
  not not_224 (not_224_out, OP4);
  not not_225 (not_225_out, OP3);
  not not_226 (not_226_out, OP2);
  not not_227 (not_227_out, OP1);
  not not_228 (not_228_out, OP0);
  not not_229 (not_229_out, F4);
  not not_230 (not_230_out, F3);
  not not_231 (not_231_out, F1);
  not not_232 (not_232_out, F0);
  not not_233 (not_233_out, OP5);
  not not_234 (not_234_out, OP4);
  not not_235 (not_235_out, OP3);
  not not_236 (not_236_out, OP2);
  not not_237 (not_237_out, OP1);
  not not_238 (not_238_out, OP0);
  not not_239 (not_239_out, F4);
  not not_240 (not_240_out, F3);
  not not_241 (not_241_out, F1);
  not not_242 (not_242_out, OP5);
  not not_243 (not_243_out, OP4);
  not not_244 (not_244_out, OP3);
  not not_245 (not_245_out, OP2);
  not not_246 (not_246_out, OP1);
  not not_247 (not_247_out, OP0);
  not not_248 (not_248_out, F4);
  not not_249 (not_249_out, F3);
  not not_250 (not_250_out, OP5);
  not not_251 (not_251_out, OP4);
  not not_252 (not_252_out, OP3);
  not not_253 (not_253_out, OP2);
  not not_254 (not_254_out, OP1);
  not not_255 (not_255_out, OP0);
  not not_256 (not_256_out, F4);
  not not_257 (not_257_out, F2);
  not not_258 (not_258_out, F0);
  not not_259 (not_259_out, OP5);
  not not_260 (not_260_out, OP4);
  not not_261 (not_261_out, OP3);
  not not_262 (not_262_out, OP2);
  not not_263 (not_263_out, OP1);
  not not_264 (not_264_out, OP0);
  not not_265 (not_265_out, F4);
  not not_266 (not_266_out, F2);
  not not_267 (not_267_out, OP5);
  not not_268 (not_268_out, OP4);
  not not_269 (not_269_out, OP3);
  not not_270 (not_270_out, OP2);
  not not_271 (not_271_out, OP1);
  not not_272 (not_272_out, OP0);
  not not_273 (not_273_out, F5);
  not not_274 (not_274_out, F4);
  not not_275 (not_275_out, F1);
  not not_276 (not_276_out, F0);
  not not_277 (not_277_out, OP5);
  not not_278 (not_278_out, OP4);
  not not_279 (not_279_out, OP3);
  not not_280 (not_280_out, OP1);
  not not_281 (not_281_out, OP0);
  not not_282 (not_282_out, OP5);
  not not_283 (not_283_out, OP4);
  not not_284 (not_284_out, OP3);
  not not_285 (not_285_out, OP1);
  not not_286 (not_286_out, OP4);
  not not_287 (not_287_out, OP2);
  not not_288 (not_288_out, OP5);
  not not_289 (not_289_out, OP4);
  not not_290 (not_290_out, OP3);
  not not_291 (not_291_out, OP2);
  not not_292 (not_292_out, OP1);
  not not_293 (not_293_out, OP0);
  not not_294 (not_294_out, F5);
  not not_295 (not_295_out, F4);
  not not_296 (not_296_out, F3);
  not not_297 (not_297_out, F0);
  not not_298 (not_298_out, OP5);
  not not_299 (not_299_out, OP4);
  not not_300 (not_300_out, OP3);
  not not_301 (not_301_out, OP2);
  not not_302 (not_302_out, OP1);
  not not_303 (not_303_out, OP0);
  not not_304 (not_304_out, F5);
  not not_305 (not_305_out, F4);
  not not_306 (not_306_out, F3);
  not not_307 (not_307_out, OP4);
  not not_308 (not_308_out, OP2);
  not not_309 (not_309_out, OP1);
  not not_310 (not_310_out, OP0);
  and and_1 (and_1_out, not_1_out, not_2_out, not_3_out, not_4_out, not_5_out, not_6_out, F5, not_7_out, not_8_out, not_9_out, not_10_out, not_11_out);
  and and_2 (and_2_out, not_12_out, not_13_out, not_14_out, not_15_out, not_16_out, not_17_out, F5, not_18_out, not_19_out, not_20_out, not_21_out, F0);
  and and_3 (and_3_out, not_22_out, not_23_out, not_24_out, not_25_out, not_26_out, not_27_out, F5, not_28_out, not_29_out, not_30_out, F1, not_31_out);
  and and_4 (and_4_out, not_32_out, not_33_out, not_34_out, not_35_out, not_36_out, not_37_out, F5, not_38_out, not_39_out, F2, not_40_out, not_41_out);
  and and_5 (and_5_out, not_42_out, not_43_out, not_44_out, not_45_out, not_46_out, not_47_out, F5, not_48_out, not_49_out, F2, not_50_out, F0);
  and and_6 (and_6_out, not_51_out, not_52_out, not_53_out, not_54_out, not_55_out, not_56_out, F5, not_57_out, not_58_out, F2, F1, F0);
  and and_7 (and_7_out, not_59_out, not_60_out, not_61_out, not_62_out, not_63_out, not_64_out, F5, not_65_out, F3, not_66_out, F1, not_67_out);
  and and_8 (and_8_out, not_68_out, not_69_out, not_70_out, not_71_out, not_72_out, not_73_out, F5, not_74_out, F3, not_75_out, F1, F0);
  and and_9 (and_9_out, not_76_out, not_77_out, not_78_out, not_79_out, not_80_out, not_81_out, not_82_out, not_83_out, F3, not_84_out, not_85_out, not_86_out);
  and and_10 (and_10_out, not_87_out, not_88_out, not_89_out, not_90_out, not_91_out, not_92_out, not_93_out, not_94_out, F3, F2, not_95_out, not_96_out);
  and and_11 (and_11_out, not_97_out, not_98_out, not_99_out, OP2, not_100_out, not_101_out);
  and and_12 (and_12_out, not_102_out, not_103_out, not_104_out, OP2, not_105_out, OP0);
  and and_13 (and_13_out, not_106_out, not_107_out, OP3, not_108_out, not_109_out, not_110_out);
  and and_14 (and_14_out, not_111_out, not_112_out, OP3, OP2, not_113_out, not_114_out);
  and and_15 (and_15_out, not_115_out, not_116_out, OP3, not_117_out, not_118_out, OP0);
  and and_16 (and_16_out, not_119_out, not_120_out, OP3, not_121_out, OP1, not_122_out);
  and and_17 (and_17_out, not_123_out, not_124_out, OP3, OP2, not_125_out, OP0);
  and and_18 (and_18_out, OP5, not_126_out, not_127_out, not_128_out, OP1, OP0);
  and and_19 (and_19_out, OP5, not_129_out, OP3, not_130_out, OP1, OP0);
  and and_20 (and_20_out, not_131_out, not_132_out, not_133_out, not_134_out, not_135_out, not_136_out, not_137_out, not_138_out, not_139_out, F2, F1, not_140_out);
  and and_21 (and_21_out, not_141_out, not_142_out, not_143_out, not_144_out, not_145_out, not_146_out, not_147_out, not_148_out, not_149_out, F2, F1, F0);
  and and_22 (and_22_out, OP5, not_150_out, OP3, not_151_out, not_152_out, not_153_out);
  and and_23 (and_23_out, not_154_out, not_155_out, not_156_out, not_157_out, not_158_out, OP0);
  and and_24 (and_24_out, not_159_out, not_160_out, not_161_out, not_162_out, not_163_out, not_164_out, not_165_out, not_166_out, not_167_out, not_168_out, not_169_out, not_170_out);
  and and_25 (and_25_out, not_171_out, not_172_out, not_173_out, not_174_out, not_175_out, not_176_out, not_177_out, not_178_out, not_179_out, not_180_out, F1, F0);
  and and_26 (and_26_out, not_181_out, not_182_out, not_183_out, not_184_out, not_185_out, not_186_out, not_187_out, not_188_out, not_189_out, not_190_out, F1, not_191_out);
  and and_27 (and_27_out, not_192_out, not_193_out, not_194_out, not_195_out, not_196_out, not_197_out, F5, not_198_out, not_199_out, not_200_out, not_201_out, not_202_out);
  and and_28 (and_28_out, not_203_out, not_204_out, not_205_out, not_206_out, not_207_out, not_208_out, F5, not_209_out, not_210_out, not_211_out, not_212_out, F0);
  and and_29 (and_29_out, not_213_out, not_214_out, not_215_out, not_216_out, not_217_out, not_218_out, F5, not_219_out, not_220_out, not_221_out, F1, not_222_out);
  and and_30 (and_30_out, not_223_out, not_224_out, not_225_out, not_226_out, not_227_out, not_228_out, F5, not_229_out, not_230_out, F2, not_231_out, not_232_out);
  and and_31 (and_31_out, not_233_out, not_234_out, not_235_out, not_236_out, not_237_out, not_238_out, F5, not_239_out, not_240_out, F2, not_241_out, F0);
  and and_32 (and_32_out, not_242_out, not_243_out, not_244_out, not_245_out, not_246_out, not_247_out, F5, not_248_out, not_249_out, F2, F1, F0);
  and and_33 (and_33_out, not_250_out, not_251_out, not_252_out, not_253_out, not_254_out, not_255_out, F5, not_256_out, F3, not_257_out, F1, not_258_out);
  and and_34 (and_34_out, not_259_out, not_260_out, not_261_out, not_262_out, not_263_out, not_264_out, F5, not_265_out, F3, not_266_out, F1, F0);
  and and_35 (and_35_out, not_267_out, not_268_out, not_269_out, not_270_out, not_271_out, not_272_out, not_273_out, not_274_out, F3, F2, not_275_out, not_276_out);
  and and_36 (and_36_out, not_277_out, not_278_out, not_279_out, OP2, not_280_out, not_281_out);
  and and_37 (and_37_out, not_282_out, not_283_out, not_284_out, OP2, not_285_out, OP0);
  and and_38 (and_38_out, OP5, not_286_out, OP3, not_287_out, OP1, OP0);
  and and_39 (and_39_out, not_288_out, not_289_out, not_290_out, not_291_out, not_292_out, not_293_out, not_294_out, not_295_out, not_296_out, F2, F1, not_297_out);
  and and_40 (and_40_out, not_298_out, not_299_out, not_300_out, not_301_out, not_302_out, not_303_out, not_304_out, not_305_out, not_306_out, F2, F1, F0);
  and and_41 (and_41_out, OP5, not_307_out, OP3, not_308_out, not_309_out, not_310_out);
  or or_1 (R1_Used, and_1_out, and_2_out, and_3_out, and_4_out, and_5_out, and_6_out, and_7_out, and_8_out, and_9_out, and_10_out, and_11_out, and_12_out, and_13_out, and_14_out, and_15_out, and_16_out, and_17_out, and_18_out, and_19_out, and_20_out, and_21_out, and_22_out, and_23_out);
  or or_2 (R2_Used, and_24_out, and_25_out, and_26_out, and_27_out, and_28_out, and_29_out, and_30_out, and_31_out, and_32_out, and_33_out, and_34_out, and_35_out, and_36_out, and_37_out, and_38_out, and_39_out, and_40_out, and_41_out);
endmodule
// datahaz
module \数据相关检测  (
  input  [5:0] OP,
  input  [4:0] EX_WriteReg_num,
  input  EX_RegWrite,
  input  [4:0] MEM_WriteReg_num,
  input  MEM_RegWrite,
  input  [5:0] Func,
  input  [4:0] ID_R1_num,
  input  [4:0] ID_R2_num,
  output \数据相关 ,
  output R1_IDEX,
  output R1_IDMEM,
  output R2_IDMEM,
  output R2_IDEX
);

  wire comparator_5_eq, comparator_6_eq, comparator_7_eq, comparator_8_eq, EX_WriteReg_00, ID_R1_00,
       ID_R2_00, IDvsEX, IDvsMEM, MEM_WriteReg_00, nor_1_out, nor_2_out, nor_3_out, nor_4_out, R1_used,
       R2_used;

  \源寄存器使用情况  \u_源寄存器使用情况_1  (
    .OP0(OP[0]), .OP1(OP[1]), .OP2(OP[2]), .OP3(OP[3]), .OP4(OP[4]), .OP5(OP[5]), .F0(Func[0]), .F1(Func[1]),
    .F2(Func[2]), .F3(Func[3]), .F4(Func[4]), .F5(Func[5]), .R1_Used(R1_used), .R2_Used(R2_used));
  Comparator #(.width(5)) comparator_1 (.a(EX_WriteReg_num), .b({5{1'b0}}), .eq(EX_WriteReg_00));  // open: gt, lt
  Comparator #(.width(5)) comparator_2 (.a(ID_R1_num), .b({5{1'b0}}), .eq(ID_R1_00));  // open: gt, lt
  Comparator #(.width(5)) comparator_3 (.a({5{1'b0}}), .b(ID_R2_num), .eq(ID_R2_00));  // open: gt, lt
  Comparator #(.width(5)) comparator_4 (.a({5{1'b0}}), .b(MEM_WriteReg_num), .eq(MEM_WriteReg_00));  // open: gt, lt
  nor nor_1 (nor_1_out, EX_WriteReg_00, ID_R1_00);
  Comparator #(.width(5)) comparator_5 (.a(EX_WriteReg_num), .b(ID_R1_num), .eq(comparator_5_eq));  // open: gt, lt
  Comparator #(.width(5)) comparator_6 (.a(EX_WriteReg_num), .b(ID_R2_num), .eq(comparator_6_eq));  // open: gt, lt
  nor nor_2 (nor_2_out, EX_WriteReg_00, ID_R2_00);
  and and_1 (R1_IDEX, EX_RegWrite, R1_used, nor_1_out, comparator_5_eq);
  and and_2 (R2_IDEX, comparator_6_eq, nor_2_out, R2_used, EX_RegWrite);
  or or_1 (\数据相关 , IDvsEX, IDvsMEM);
  or or_2 (IDvsEX, R1_IDEX, R2_IDEX);
  nor nor_3 (nor_3_out, MEM_WriteReg_00, ID_R1_00);
  Comparator #(.width(5)) comparator_7 (.a(MEM_WriteReg_num), .b(ID_R1_num), .eq(comparator_7_eq));  // open: gt, lt
  Comparator #(.width(5)) comparator_8 (.a(MEM_WriteReg_num), .b(ID_R2_num), .eq(comparator_8_eq));  // open: gt, lt
  nor nor_4 (nor_4_out, MEM_WriteReg_00, ID_R2_00);
  and and_3 (R1_IDMEM, MEM_RegWrite, R1_used, nor_3_out, comparator_7_eq);
  and and_4 (R2_IDMEM, comparator_8_eq, nor_4_out, R2_used, MEM_RegWrite);
  or or_3 (IDvsMEM, R1_IDMEM, R2_IDMEM);

  // Other names for the same wires on the sheet: OP_CODE[5:0] = OP
endmodule

// IF/ID
module IF_ID (
  input  [31:0] IRin,
  input  [31:0] PCin,
  input  [31:0] PC_4in,
  input  [8:0] BHTData,
  input  WE,
  input  Clk,
  input  Rst,
  output [31:0] IRout,
  output [31:0] PCout,
  output [31:0] PC_4out,
  output [8:0] BHTdata_2
);

  wire d_ff_1_q;

  Register #(.width(32)) IR (.D(IRin), .en(WE), .Q(IRout), .clk(Clk), .clr(d_ff_1_q));
  Register #(.width(32)) PC (.D(PCin), .en(WE), .Q(PCout), .clk(Clk), .clr(d_ff_1_q));
  Register #(.width(32)) PC_4 (.D(PC_4in), .en(WE), .Q(PC_4out), .clk(Clk), .clr(d_ff_1_q));
  D_Flip_Flop d_ff_1 (.clk(Clk), .D(Rst), .Q(d_ff_1_q), .en(WE), .reset(d_ff_1_q));  // open: Qn, preset
  Register #(.width(9)) u_BHTData (.D(BHTData), .en(WE), .Q(BHTdata_2), .clk(Clk), .clr(d_ff_1_q));
endmodule

// ID/EX
module ID_EX (
  input  MemToReg,
  input  [3:0] AluOP,
  input  MemWrite,
  input  [31:0] IRin,
  input  AluSRC,
  input  [31:0] R1in,
  input  RegWrite,
  input  [31:0] PCin,
  input  [31:0] R2in,
  input  Syscall,
  input  SignedExt,
  input  [31:0] PC_4in,
  input  [4:0] RegWriteAddr,
  input  RegDst,
  input  Beq,
  input  [31:0] Immin,
  input  Bne,
  input  Syscall34,
  input  JR,
  input  JMP,
  input  Syscall10,
  input  JAL,
  input  [8:0] BHTData,
  input  BLTZ,
  input  WE,
  input  Clk,
  input  SB,
  input  SV,
  input  Rst,
  input  [1:0] R1_sel,
  input  [1:0] R2_sel,
  output MemToReg_2,
  output [3:0] AluOP_2,
  output MemWrite_2,
  output [31:0] IRout,
  output AluSRC_2,
  output [31:0] R1out,
  output RegWrite_2,
  output [31:0] PCout,
  output [31:0] R2out,
  output Syscall_2,
  output SignedExt_2,
  output [31:0] PC_4out,
  output [4:0] RegWriteAddr_2,
  output RegDst_2,
  output Beq_2,
  output [31:0] Immout,
  output Bne_2,
  output Syscall34_2,
  output JR_2,
  output JMP_2,
  output Syscall10_2,
  output JAL_2,
  output [8:0] BHTData_2,
  output BLTZ_2,
  output SB_2,
  output SV_2,
  output [1:0] R1_sel_2,
  output [1:0] R2_sel_2
);

  wire Rst_t;

  Register #(.width(32)) IR (.D(IRin), .en(WE), .Q(IRout), .clk(Clk), .clr(Rst_t));
  Register #(.width(32)) PC (.D(PCin), .en(WE), .Q(PCout), .clk(Clk), .clr(Rst_t));
  Register #(.width(32)) PC_4 (.D(PC_4in), .en(WE), .Q(PC_4out), .clk(Clk), .clr(Rst_t));
  Register #(.width(32)) Imm (.D(Immin), .en(WE), .Q(Immout), .clk(Clk), .clr(Rst_t));
  D_Flip_Flop d_ff_1 (.clk(Clk), .D(Rst), .Q(Rst_t), .en(WE), .reset(Rst_t));  // open: Qn, preset
  Register #(.width(1)) register_1 (.D(MemToReg), .en(WE), .Q(MemToReg_2), .clk(Clk), .clr(Rst_t));
  Register #(.width(1)) register_2 (.D(MemWrite), .en(WE), .Q(MemWrite_2), .clk(Clk), .clr(Rst_t));
  Register #(.width(1)) register_3 (.D(AluSRC), .en(WE), .Q(AluSRC_2), .clk(Clk), .clr(Rst_t));
  Register #(.width(1)) register_4 (.D(RegWrite), .en(WE), .Q(RegWrite_2), .clk(Clk), .clr(Rst_t));
  Register #(.width(1)) register_5 (.D(Syscall), .en(WE), .Q(Syscall_2), .clk(Clk), .clr(Rst_t));
  Register #(.width(1)) register_6 (.D(SignedExt), .en(WE), .Q(SignedExt_2), .clk(Clk), .clr(Rst_t));
  Register #(.width(1)) register_7 (.D(RegDst), .en(WE), .Q(RegDst_2), .clk(Clk), .clr(Rst_t));
  Register #(.width(1)) register_8 (.D(Beq), .en(WE), .Q(Beq_2), .clk(Clk), .clr(Rst_t));
  Register #(.width(1)) register_9 (.D(Bne), .en(WE), .Q(Bne_2), .clk(Clk), .clr(Rst_t));
  Register #(.width(1)) register_10 (.D(JR), .en(WE), .Q(JR_2), .clk(Clk), .clr(Rst_t));
  Register #(.width(1)) register_11 (.D(JMP), .en(WE), .Q(JMP_2), .clk(Clk), .clr(Rst_t));
  Register #(.width(1)) register_12 (.D(JAL), .en(WE), .Q(JAL_2), .clk(Clk), .clr(Rst_t));
  Register #(.width(1)) register_13 (.D(BLTZ), .en(WE), .Q(BLTZ_2), .clk(Clk), .clr(Rst_t));
  Register #(.width(1)) register_14 (.D(SB), .en(WE), .Q(SB_2), .clk(Clk), .clr(Rst_t));
  Register #(.width(1)) register_15 (.D(SV), .en(WE), .Q(SV_2), .clk(Clk), .clr(Rst_t));
  Register #(.width(2)) register_16 (.D(R1_sel), .en(WE), .Q(R1_sel_2), .clk(Clk), .clr(Rst_t));
  Register #(.width(2)) register_17 (.D(R2_sel), .en(WE), .Q(R2_sel_2), .clk(Clk), .clr(Rst_t));
  Register #(.width(4)) u_AluOP (.D(AluOP), .en(WE), .Q(AluOP_2), .clk(Clk), .clr(Rst_t));
  Register #(.width(32)) R1 (.D(R1in), .en(WE), .Q(R1out), .clk(Clk), .clr(Rst_t));
  Register #(.width(32)) R2 (.D(R2in), .en(WE), .Q(R2out), .clk(Clk), .clr(Rst_t));
  Register #(.width(5)) u_RegWriteAddr (.D(RegWriteAddr), .en(WE), .Q(RegWriteAddr_2), .clk(Clk), .clr(Rst_t));
  Register #(.width(1)) register_18 (.D(Syscall34), .en(WE), .Q(Syscall34_2), .clk(Clk), .clr(Rst_t));
  Register #(.width(1)) register_19 (.D(Syscall10), .en(WE), .Q(Syscall10_2), .clk(Clk), .clr(Rst_t));
  Register #(.width(9)) u_BHTData (.D(BHTData), .en(WE), .Q(BHTData_2), .clk(Clk), .clr(Rst_t));
endmodule

// EX/MEM
module EX_MEM (
  input  MemToReg,
  input  MemWrite,
  input  [31:0] IRin,
  input  [31:0] AluRes,
  input  RegWrite,
  input  [31:0] PCin,
  input  Syscall,
  input  [3:0] MemselSB,
  input  [31:0] PC_4in,
  input  [4:0] RegWriteAddr,
  input  SB,
  input  [31:0] R1in,
  input  JAL,
  input  Syscall34,
  input  [31:0] R2in,
  input  [31:0] SBMemdata,
  input  Syscall10,
  input  WE,
  input  Clk,
  input  Rst,
  output MemToReg_2,
  output MemWrite_2,
  output [31:0] IRout,
  output [31:0] AluRes_2,
  output RegWrite_2,
  output [31:0] PCout,
  output Syscall_2,
  output [3:0] MemselSB_2,
  output [31:0] PC_4out,
  output [4:0] RegWriteAddr_2,
  output SB_2,
  output [31:0] R1out,
  output JAL_2,
  output Syscall34_2,
  output [31:0] R2out,
  output [31:0] SBMemdata_2,
  output Syscall10_2
);

  wire d_ff_1_q;

  Register #(.width(32)) IR (.D(IRin), .en(WE), .Q(IRout), .clk(Clk), .clr(d_ff_1_q));
  Register #(.width(32)) PC (.D(PCin), .en(WE), .Q(PCout), .clk(Clk), .clr(d_ff_1_q));
  Register #(.width(32)) PC_4 (.D(PC_4in), .en(WE), .Q(PC_4out), .clk(Clk), .clr(d_ff_1_q));
  D_Flip_Flop d_ff_1 (.clk(Clk), .D(Rst), .Q(d_ff_1_q), .en(WE), .reset(d_ff_1_q));  // open: Qn, preset
  Register #(.width(1)) register_1 (.D(MemToReg), .en(WE), .Q(MemToReg_2), .clk(Clk), .clr(d_ff_1_q));
  Register #(.width(1)) register_2 (.D(MemWrite), .en(WE), .Q(MemWrite_2), .clk(Clk), .clr(d_ff_1_q));
  Register #(.width(1)) register_3 (.D(RegWrite), .en(WE), .Q(RegWrite_2), .clk(Clk), .clr(d_ff_1_q));
  Register #(.width(1)) register_4 (.D(Syscall), .en(WE), .Q(Syscall_2), .clk(Clk), .clr(d_ff_1_q));
  Register #(.width(1)) register_5 (.D(SB), .en(WE), .Q(SB_2), .clk(Clk));  // open: clr
  Register #(.width(1)) register_6 (.D(JAL), .en(WE), .Q(JAL_2), .clk(Clk));  // open: clr
  Register #(.width(1)) register_7 (.D(Syscall34), .en(WE), .Q(Syscall34_2), .clk(Clk), .clr(d_ff_1_q));
  Register #(.width(1)) register_8 (.D(Syscall10), .en(WE), .Q(Syscall10_2), .clk(Clk), .clr(d_ff_1_q));
  Register #(.width(32)) register_9 (.D(AluRes), .en(WE), .Q(AluRes_2), .clk(Clk), .clr(d_ff_1_q));
  Register #(.width(4)) register_10 (.D(MemselSB), .en(WE), .Q(MemselSB_2), .clk(Clk), .clr(d_ff_1_q));
  Register #(.width(5)) u_RegWriteAddr (.D(RegWriteAddr), .en(WE), .Q(RegWriteAddr_2), .clk(Clk), .clr(d_ff_1_q));
  Register #(.width(32)) R1 (.D(R1in), .en(WE), .Q(R1out), .clk(Clk), .clr(d_ff_1_q));
  Register #(.width(32)) R2 (.D(R2in), .en(WE), .Q(R2out), .clk(Clk), .clr(d_ff_1_q));
  Register #(.width(32)) register_11 (.D(SBMemdata), .en(WE), .Q(SBMemdata_2), .clk(Clk), .clr(d_ff_1_q));
endmodule

// MEM/WB
module MEM_WB (
  input  MemToReg,
  input  [31:0] IRin,
  input  [31:0] MemData,
  input  RegWrite,
  input  [31:0] R1,
  input  [31:0] PCin,
  input  Syscall,
  input  [31:0] PC_4in,
  input  [4:0] RegWriteAddr,
  input  JAL,
  input  [31:0] AluRes,
  input  Syscall34,
  input  Syscall10,
  input  WE,
  input  Clk,
  input  Rst,
  output MemToReg_2,
  output [31:0] IRout,
  output [31:0] MemData_2,
  output RegWrite_2,
  output [31:0] R1_2,
  output [31:0] PCout,
  output Syscall_2,
  output [31:0] PC_4out,
  output [4:0] RegWriteAddr_2,
  output JAL_2,
  output [31:0] AluRes_2,
  output Syscall34_2,
  output Syscall10_2
);

  wire d_ff_1_q;

  Register #(.width(32)) IR (.D(IRin), .en(WE), .Q(IRout), .clk(Clk), .clr(d_ff_1_q));
  Register #(.width(32)) PC (.D(PCin), .en(WE), .Q(PCout), .clk(Clk), .clr(d_ff_1_q));
  Register #(.width(32)) PC_4 (.D(PC_4in), .en(WE), .Q(PC_4out), .clk(Clk), .clr(d_ff_1_q));
  D_Flip_Flop d_ff_1 (.clk(Clk), .D(Rst), .Q(d_ff_1_q), .en(WE), .reset(d_ff_1_q));  // open: Qn, preset
  Register #(.width(1)) register_1 (.D(MemToReg), .en(WE), .Q(MemToReg_2), .clk(Clk), .clr(d_ff_1_q));
  Register #(.width(1)) register_2 (.D(RegWrite), .en(WE), .Q(RegWrite_2), .clk(Clk), .clr(d_ff_1_q));
  Register #(.width(1)) register_3 (.D(Syscall), .en(WE), .Q(Syscall_2), .clk(Clk), .clr(d_ff_1_q));
  Register #(.width(1)) register_4 (.D(JAL), .en(WE), .Q(JAL_2), .clk(Clk));  // open: clr
  Register #(.width(1)) register_5 (.D(Syscall34), .en(WE), .Q(Syscall34_2), .clk(Clk), .clr(d_ff_1_q));
  Register #(.width(1)) register_6 (.D(Syscall10), .en(WE), .Q(Syscall10_2), .clk(Clk), .clr(d_ff_1_q));
  Register #(.width(32)) register_7 (.D(MemData), .en(WE), .Q(MemData_2), .clk(Clk), .clr(d_ff_1_q));
  Register #(.width(32)) register_8 (.D(R1), .en(WE), .Q(R1_2), .clk(Clk), .clr(d_ff_1_q));
  Register #(.width(5)) u_RegWriteAddr (.D(RegWriteAddr), .en(WE), .Q(RegWriteAddr_2), .clk(Clk), .clr(d_ff_1_q));
  Register #(.width(32)) register_9 (.D(AluRes), .en(WE), .Q(AluRes_2), .clk(Clk), .clr(d_ff_1_q));
endmodule

module \分支相关流水线  (
);

  wire AluSrcB, and_1_out, and_6_out, and_7_out, Beq, beq_suc, Beqout, BLTZ, bltz_suc, BLTZout, Bne, bne_suc,
       Bneout, CLK, clkne, comparator_3_eq, equal, ex_mem_1_jal_2, ex_mem_1_memtoreg_2, ex_mem_1_memwrite_2,
       ex_mem_1_regwrite_2, ex_mem_1_sb_2, ex_mem_1_syscall10_2, ex_mem_1_syscall34_2, ex_mem_1_syscall_2,
       Go, GoCancel__on_fall_q, GoOut, GoUsed_q, id_ex_1_alusrc_2, id_ex_1_memtoreg_2, id_ex_1_memwrite_2,
       id_ex_1_regwrite_2, id_ex_1_sb_2, id_ex_1_sv_2, id_ex_1_syscall10_2, id_ex_1_syscall34_2,
       id_ex_1_syscall_2, IfBranch, ifJAL, IR1, IR2, IR3, is34, JAL, JALout, JMP, JMPout, JR, JRout, less,
       mem_wb_1_memtoreg_2, mem_wb_1_syscall10_2, mem_wb_1_syscall34_2, mem_wb_1_syscall_2, MemToReg,
       MemWrite, or_1_out, or_2_out, or_3_out, RegWrite, RegWriteOut, RST, SB, SignedExt, SV, syscall,
       Syscall10, Syscall34, W1, W2, W3, \硬布线控制器_1_regdst ;
  wire [1:0] PCsel;
  wire [1:1] mips_alu_1_result;
  wire [3:0] AluOP, decoder_1_out0, ex_mem_1_memselsb_2, id_ex_1_aluop_2, multiplexer_12_out;
  wire [4:0] ex_mem_1_regwriteaddr_2, id_ex_1_regwriteaddr_2, mem_wb_1_regwriteaddr_2, multiplexer_3_out,
       multiplexer_4_out, multiplexer_5_out, multiplexer_6_out, multiplexer_10_out, shifter_3_out;
  wire [11:0] EX_PC, ID_PC, IF_PC, MEM_PC, WB_PC;
  wire [15:0] \LoadUse次数 , \总周期数 , \插入气泡数 , \无条件分支数 , \条件分支成功数 ;
  wire [19:0] ex_mem_1_alures_2_2;
  wire [27:0] id_ex_1_pcout;
  wire [31:0] adder_1_out, adder_2_out, bit_extender_1_out, ex_mem_1_alures_2, ex_mem_1_irout,
       ex_mem_1_pc_4out, ex_mem_1_pcout, ex_mem_1_r2out, ex_mem_1_sbmemdata_2, id_ex_1_immout,
       id_ex_1_pc_4out, id_ex_1_r1out, id_ex_1_r2out, if_id_1_irout, if_id_1_pc_4out, if_id_1_pcout, LedData,
       mem_wb_1_alures_2, mem_wb_1_memdata_2, mem_wb_1_pc_4out, mips_ram_1_p7, mips_regifile_1_r1,
       multiplexer_1_out, multiplexer_2_out, multiplexer_7_out, multiplexer_8_out, multiplexer_9_out,
       multiplexer_11_out, multiplexer_13_out, PC_q, R2out, rom_1_data, shifter_1_out, shifter_2_out;
  wire [31:2] id_ex_1_irout, mips_alu_1_result_2;
  wire [31:26] id_ex_1_irout_2;

  Button \u_总复位  (.out(RST));
  Button _1 (.out(IR1));
  Button _2 (.out(IR2));
  Button _3 (.out(IR3));
  Button \u_继续运行  (.out(Go));
  LED led_1 (.in(W1));
  LED led_2 (.in(W2));
  LED led_3 (.in(W3));
  Hex_Digit_Display hex_digit_display_1 (.value(LedData[31:28]));  // open: dp
  Multiplexer #(.select(2), .width(32), .enable("false")) multiplexer_1 (
    .in0(id_ex_1_r1out), .in1(id_ex_1_pc_4out), .in2(adder_2_out), .in3({id_ex_1_irout, 2'b00}),
    .out(multiplexer_1_out), .sel(PCsel));
  Multiplexer #(.width(32), .enable("false")) multiplexer_2 (
    .in0(adder_1_out), .in1(multiplexer_1_out), .out(multiplexer_2_out), .sel(IfBranch));
  Hex_Digit_Display hex_digit_display_2 (.value(LedData[27:24]));  // open: dp
  Hex_Digit_Display hex_digit_display_3 (.value(LedData[23:20]));  // open: dp
  Register #(.width(32)) PC (.D(multiplexer_2_out), .en(clkne), .Q(PC_q), .clk(CLK), .clr(RST));
  Hex_Digit_Display hex_digit_display_4 (.value(LedData[15:12]));  // open: dp
  Hex_Digit_Display hex_digit_display_5 (.value(LedData[19:16]));  // open: dp
  Adder #(.width(32)) adder_1 (.a(PC_q), .b(32'h4), .out(adder_1_out));  // open: cin, cout
  Hex_Digit_Display hex_digit_display_6 (.value(LedData[7:4]));  // open: dp
  Hex_Digit_Display hex_digit_display_7 (.value(LedData[11:8]));  // open: dp
  Hex_Digit_Display hex_digit_display_8 (.value(LedData[3:0]));  // open: dp
  ROM #(.addrWidth(10), .dataWidth(32)) rom_1 (.addr(PC_q[11:2]), .data(rom_1_data));  // open: sel
  IF_ID if_id_1 (
    .IRin(rom_1_data), .IRout(if_id_1_irout), .PCin(PC_q), .PCout(if_id_1_pcout), .PC_4in(adder_1_out),
    .PC_4out(if_id_1_pc_4out), .WE(clkne), .Clk(CLK), .Rst(IfBranch));  // open: BHTData, BHTdata_2
  // Probe on \总周期数 
  // Probe on \无条件分支数 
  // Probe on \条件分支成功数 
  // Probe on \插入气泡数 
  // Probe on \LoadUse次数 
  // Probe on IF_PC
  // Probe on ID_PC
  // Probe on EX_PC
  // Probe on MEM_PC
  and and_1 (and_1_out, SignedExt, if_id_1_irout[15]);
  Comparator #(.width(32), .mode("unsigned")) comparator_1 (.a(32'ha), .b(R2out), .eq(Syscall10));  // open: gt, lt
  Comparator #(.width(32), .mode("unsigned")) comparator_2 (.a(32'h22), .b(R2out), .eq(is34));  // open: gt, lt
  // Probe on WB_PC
  \硬布线控制器  \u_硬布线控制器_1  (
    .Func(if_id_1_irout[5:0]), .OP(if_id_1_irout[31:26]), .ALU_OP(AluOP), .MemToReg(MemToReg),
    .MemWrite(MemWrite), .ALU_SRC(AluSrcB), .RegWrite(RegWrite), .SysCALL(syscall), .SignedExt(SignedExt),
    .RegDst(\硬布线控制器_1_regdst ), .JR(JR), .JMP(JMP), .Beq(Beq), .JAL(JAL), .Bne(Bne), .BLTZ(BLTZ), .SB(SB),
    .SV(SV));
  Multiplexer #(.width(5), .enable("false")) multiplexer_3 (
    .in0(if_id_1_irout[25:21]), .in1(5'b00100), .out(multiplexer_3_out), .sel(Syscall34));
  Multiplexer #(.width(5), .enable("false")) multiplexer_4 (
    .in0(if_id_1_irout[20:16]), .in1(if_id_1_irout[15:11]), .out(multiplexer_4_out), .sel(\硬布线控制器_1_regdst ));
  assign bit_extender_1_out = {{16{and_1_out}}, if_id_1_irout[15:0]};  // Bit_Extender bit_extender_1
  and and_2 (Syscall34, is34, syscall);
  Multiplexer #(.width(5), .enable("false")) multiplexer_5 (
    .in0(if_id_1_irout[20:16]), .in1(5'b00010), .out(multiplexer_5_out), .sel(syscall));
  Multiplexer #(.width(5), .enable("false")) multiplexer_6 (
    .in0(multiplexer_4_out), .in1({5{1'b1}}), .out(multiplexer_6_out), .sel(JAL));
  Multiplexer #(.width(32), .enable("false")) multiplexer_7 (
    .in0(multiplexer_13_out), .in1(mem_wb_1_pc_4out), .out(multiplexer_7_out), .sel(ifJAL));
  Clock clock_1 (.out(CLK));
  MIPS_Regifile mips_regifile_1 (
    .Din(multiplexer_7_out), .Clk(CLK), .R1(mips_regifile_1_r1), .R2(R2out), .WE(RegWriteOut),
    .W_num(mem_wb_1_regwriteaddr_2), .R1_num(multiplexer_3_out), .R2_num(multiplexer_5_out));
  Counter #(.width(16), .max('hffff)) counter_1 (
    .count(clkne), .Q(\总周期数 ), .clk(CLK), .clr(RST));  // open: load, D, carry
  or or_1 (or_1_out, bne_suc, bltz_suc, beq_suc);
  D_Flip_Flop GoPressed (.clk(Go), .D(1'b1), .Q(GoOut), .reset(GoCancel__on_fall_q));  // open: Qn, preset, en
  Counter #(.width(16), .max('hffff)) counter_2 (
    .count(or_1_out), .Q(\条件分支成功数 ), .clk(CLK), .clr(RST));  // open: load, D, carry
  D_Flip_Flop GoUsed (.clk(CLK), .D(GoOut), .Q(GoUsed_q), .reset(GoCancel__on_fall_q));  // open: Qn, preset, en
  or or_2 (or_2_out, JAL, JR, JMP);
  D_Flip_Flop #(.trigger("falling")) GoCancel__on_fall (
    .clk(CLK), .D(GoUsed_q), .Q(GoCancel__on_fall_q), .reset(RST));  // open: Qn, preset, en
  Counter #(.width(16), .max('hffff)) counter_3 (
    .count(or_2_out), .Q(\无条件分支数 ), .clk(CLK), .clr(RST));  // open: load, D, carry
  ID_EX id_ex_1 (
    .IRin(if_id_1_irout), .IRout({id_ex_1_irout_2, id_ex_1_irout[27:2]}), .PCin(if_id_1_pcout),
    .PCout({id_ex_1_irout[31:28], id_ex_1_pcout}), .PC_4in(if_id_1_pc_4out), .PC_4out(id_ex_1_pc_4out),
    .WE(clkne), .Clk(CLK), .Rst(IfBranch), .Immin(bit_extender_1_out), .Immout(id_ex_1_immout),
    .MemToReg(MemToReg), .MemToReg_2(id_ex_1_memtoreg_2), .MemWrite(MemWrite),
    .MemWrite_2(id_ex_1_memwrite_2), .AluSRC(AluSrcB), .AluSRC_2(id_ex_1_alusrc_2), .RegWrite(RegWrite),
    .RegWrite_2(id_ex_1_regwrite_2), .Syscall(syscall), .Syscall_2(id_ex_1_syscall_2), .SignedExt(SignedExt),
    .RegDst(\硬布线控制器_1_regdst ), .Beq(Beq), .Beq_2(Beqout), .Bne(Bne), .Bne_2(Bneout), .JR(JR), .JR_2(JRout),
    .JMP(JMP), .JMP_2(JMPout), .JAL(JAL), .JAL_2(JALout), .BLTZ(BLTZ), .BLTZ_2(BLTZout), .SB(SB),
    .SB_2(id_ex_1_sb_2), .SV(SV), .SV_2(id_ex_1_sv_2), .AluOP(AluOP), .AluOP_2(id_ex_1_aluop_2),
    .R1in(mips_regifile_1_r1), .R1out(id_ex_1_r1out), .R2in(R2out), .R2out(id_ex_1_r2out),
    .RegWriteAddr(multiplexer_6_out), .RegWriteAddr_2(id_ex_1_regwriteaddr_2), .Syscall34(is34),
    .Syscall34_2(id_ex_1_syscall34_2), .Syscall10(Syscall10), .Syscall10_2(id_ex_1_syscall10_2));  // open: SignedExt_2, RegDst_2, R1_sel, R1_sel_2, R2_sel, R2_sel_2, BHTData, BHTData_2
  Shifter #(.width(32)) shifter_1 (.in(id_ex_1_immout), .\dist (5'b00010), .out(shifter_1_out));
  Adder #(.width(32)) adder_2 (.a(id_ex_1_pc_4out), .b(shifter_1_out), .out(adder_2_out));  // open: cin, cout
  Multiplexer #(.width(32), .enable("false")) multiplexer_8 (
    .in0(id_ex_1_r2out), .in1(id_ex_1_immout), .out(multiplexer_8_out), .sel(id_ex_1_alusrc_2));
  Register #(.width(32)) register_1 (.D(id_ex_1_r1out), .en(id_ex_1_syscall34_2), .Q(LedData), .clk(CLK), .clr(RST));
  Comparator #(.width(2)) comparator_3 (.a(PCsel), .b(2'b01), .eq(comparator_3_eq));  // open: gt, lt
  Multiplexer #(.width(32), .enable("false")) multiplexer_9 (
    .in0(multiplexer_8_out), .in1({32{1'b0}}), .out(multiplexer_9_out), .sel(BLTZout));
  Multiplexer #(.width(5), .enable("false")) multiplexer_10 (
    .in0(id_ex_1_irout[12:8]), .in1(id_ex_1_r1out[4:0]), .out(multiplexer_10_out), .sel(id_ex_1_sv_2));
  Shifter #(.width(32)) shifter_2 (.in(id_ex_1_r2out), .\dist (shifter_3_out), .out(shifter_2_out));
  Shifter #(.width(5)) shifter_3 (.in({3'b000, mips_alu_1_result[1], less}), .\dist (3'b011), .out(shifter_3_out));
  temp temp_1 (
    .jmp(JMPout), .jr(JRout), .jal(JALout), .beq(beq_suc), .bne(bne_suc), .bltz(bltz_suc), .sel1(PCsel[1]),
    .sel0(PCsel[0]));
  not not_1 (IfBranch, comparator_3_eq);
  MIPS_ALU mips_alu_1 (
    .X(id_ex_1_r1out), .Y(multiplexer_9_out), .AluOP(id_ex_1_aluop_2), .Equal(equal),
    .Result({mips_alu_1_result_2, mips_alu_1_result[1], less}), .shamt(multiplexer_10_out));  // open: Result_2
  Decoder #(.select(2)) decoder_1 (
    .out0(decoder_1_out0[0]), .out1(decoder_1_out0[1]), .out2(decoder_1_out0[2]), .out3(decoder_1_out0[3]),
    .sel({mips_alu_1_result[1], less}));  // open: en
  and and_3 (beq_suc, Beqout, equal);
  and and_4 (bne_suc, Bneout, ~equal);  // AND_Gate
  and and_5 (bltz_suc, BLTZout, less);
  EX_MEM ex_mem_1 (
    .MemToReg(id_ex_1_memtoreg_2), .MemToReg_2(ex_mem_1_memtoreg_2), .MemWrite(id_ex_1_memwrite_2),
    .MemWrite_2(ex_mem_1_memwrite_2), .IRin({id_ex_1_irout_2, id_ex_1_irout[27:2]}), .IRout(ex_mem_1_irout),
    .RegWrite(id_ex_1_regwrite_2), .RegWrite_2(ex_mem_1_regwrite_2),
    .PCin({id_ex_1_irout[31:28], id_ex_1_pcout}), .PCout(ex_mem_1_pcout), .Syscall(id_ex_1_syscall_2),
    .Syscall_2(ex_mem_1_syscall_2), .PC_4in(id_ex_1_pc_4out), .PC_4out(ex_mem_1_pc_4out),
    .RegWriteAddr(id_ex_1_regwriteaddr_2), .RegWriteAddr_2(ex_mem_1_regwriteaddr_2), .WE(clkne), .Clk(CLK),
    .Rst(RST), .AluRes({mips_alu_1_result_2, mips_alu_1_result[1], less}),
    .AluRes_2({ex_mem_1_alures_2[31:22], ex_mem_1_alures_2_2, ex_mem_1_alures_2[1:0]}), .R2in(id_ex_1_r2out),
    .R2out(ex_mem_1_r2out), .SBMemdata(shifter_2_out), .SBMemdata_2(ex_mem_1_sbmemdata_2), .SB(id_ex_1_sb_2),
    .SB_2(ex_mem_1_sb_2), .MemselSB(decoder_1_out0), .MemselSB_2(ex_mem_1_memselsb_2), .JAL(JALout),
    .JAL_2(ex_mem_1_jal_2), .Syscall34(id_ex_1_syscall34_2), .Syscall34_2(ex_mem_1_syscall34_2),
    .Syscall10(id_ex_1_syscall10_2), .Syscall10_2(ex_mem_1_syscall10_2));  // open: R1in, R1out
  Multiplexer #(.width(32), .enable("false")) multiplexer_11 (
    .in0(ex_mem_1_r2out), .in1(ex_mem_1_sbmemdata_2), .out(multiplexer_11_out), .sel(ex_mem_1_sb_2));
  Multiplexer #(.width(4), .enable("false")) multiplexer_12 (
    .in0(4'b1111), .in1(ex_mem_1_memselsb_2), .out(multiplexer_12_out), .sel(ex_mem_1_sb_2));
  // MIPS_RAM mips_ram_1: pin names not known; wires that end beside it: ex_mem_1_alures_2_2, multiplexer_11_out, ex_mem_1_memwrite_2, multiplexer_12_out, CLK, RST, mips_ram_1_p7
  MEM_WB mem_wb_1 (
    .MemToReg(ex_mem_1_memtoreg_2), .MemToReg_2(mem_wb_1_memtoreg_2), .IRin(ex_mem_1_irout),
    .MemData(mips_ram_1_p7), .MemData_2(mem_wb_1_memdata_2), .RegWrite(ex_mem_1_regwrite_2),
    .RegWrite_2(RegWriteOut), .PCin(ex_mem_1_pcout), .Syscall(ex_mem_1_syscall_2),
    .Syscall_2(mem_wb_1_syscall_2), .PC_4in(ex_mem_1_pc_4out), .PC_4out(mem_wb_1_pc_4out),
    .RegWriteAddr(ex_mem_1_regwriteaddr_2), .RegWriteAddr_2(mem_wb_1_regwriteaddr_2),
    .AluRes({ex_mem_1_alures_2[31:22], ex_mem_1_alures_2_2, ex_mem_1_alures_2[1:0]}),
    .AluRes_2(mem_wb_1_alures_2), .WE(clkne), .Clk(CLK), .Rst(RST), .JAL(ex_mem_1_jal_2), .JAL_2(ifJAL),
    .Syscall34(ex_mem_1_syscall34_2), .Syscall34_2(mem_wb_1_syscall34_2), .Syscall10(ex_mem_1_syscall10_2),
    .Syscall10_2(mem_wb_1_syscall10_2));  // open: IRout, PCout, R1, R1_2
  Multiplexer #(.width(32), .enable("false")) multiplexer_13 (
    .in0(mem_wb_1_alures_2), .in1(mem_wb_1_memdata_2), .out(multiplexer_13_out), .sel(mem_wb_1_memtoreg_2));
  and and_6 (and_6_out, or_3_out, mem_wb_1_syscall_2);
  or or_3 (or_3_out, mem_wb_1_syscall10_2, and_7_out);
  and and_7 (and_7_out, ~mem_wb_1_syscall34_2, ~GoOut);  // AND_Gate
  not not_2 (clkne, and_6_out);

  // Notes on the sheet:
  //   中断源
  //   中断等待指示
  //   数码管输出
  //   指令存储器
  //   contents of rom_1 (hex, n*v repeats v):
  //   20110020 20020022 8000c06 20110000 20110000 2002000a 10000003 20110000 20110000 2002000a 14110003
  //   20110000 20110000 2002000a c000c14 2002000a 0 0 0 c 2231ffff 0 0 0 112020 0 0 0 c 1620fff6 3e00008
  //   指令字
  //   OP
  //   Func
  //   rs
  //   rt
  //   rd
  //   10#10 (exit)
  //   10#34 (print hex)
  //   流水调试日志用
  //   JMP
  //   JR
  //   OP
  //   Func
  //   Beq
  //   Bne
  //   MemToReg
  //   MemWrite
  //   AluOP
  //   AluSrcB
  //   RegWrite
  //   JAL
  //   RegDst
  //   Syscall
  //   Syscall34
endmodule

module \气泡流水线  (
);

  wire AluSrcB, and_1_out, and_2_out, and_3_out, and_8_out, and_9_out, and_10_out, Beq, beq_suc, Beqout,
       BLTZ, bltz_suc, BLTZout, Bne, bne_suc, Bneout, CLK, clkne, comparator_3_eq, DataHaZ, equal,
       ex_mem_1_jal_2, ex_mem_1_memtoreg_2, ex_mem_1_memwrite_2, ex_mem_1_sb_2, ex_mem_1_syscall10_2,
       ex_mem_1_syscall34_2, ex_mem_1_syscall_2, EX_RegWrite, Go, GoCancel__on_fall_q, GoOut, GoUsed_q,
       id_ex_1_alusrc_2, id_ex_1_memtoreg_2, id_ex_1_memwrite_2, id_ex_1_sb_2, id_ex_1_sv_2,
       id_ex_1_syscall10_2, id_ex_1_syscall34_2, id_ex_1_syscall_2, IfBranch, ifJAL, IR1, IR2, IR3, is34,
       JAL, JALout, JMP, JMPout, JR, JRout, less, MEM_RegWrite, mem_wb_1_memtoreg_2, mem_wb_1_syscall10_2,
       mem_wb_1_syscall34_2, mem_wb_1_syscall_2, MemToReg, MemWrite, not_1_out, not_2_out, or_1_out,
       or_2_out, or_3_out, or_4_out, RegWrite, RegWriteOut, RST, SB, SignedExt, SV, syscall, Syscall10,
       Syscall34, W1, W2, W3, \硬布线控制器_1_regdst ;
  wire [1:0] PCsel;
  wire [1:1] mips_alu_1_result;
  wire [3:0] AluOP, decoder_1_out0, ex_mem_1_memselsb_2, id_ex_1_aluop_2, multiplexer_12_out;
  wire [4:0] EX_RegWrite_num, ID_R1, ID_R2, MEM_RegWrite_num, mem_wb_1_regwriteaddr_2, multiplexer_4_out,
       multiplexer_6_out, multiplexer_10_out, shifter_3_out;
  wire [11:0] EX_PC, ID_PC, IF_PC, MEM_PC, WB_PC;
  wire [15:0] \LoadUse次数 , \总周期数 , \插入气泡数 , \无条件分支数 , \条件分支成功数 ;
  wire [19:0] ex_mem_1_alures_2_2;
  wire [27:0] id_ex_1_pcout;
  wire [31:0] adder_1_out, adder_2_out, bit_extender_1_out, ex_mem_1_alures_2, ex_mem_1_irout,
       ex_mem_1_pc_4out, ex_mem_1_pcout, ex_mem_1_r1out, ex_mem_1_r2out, ex_mem_1_sbmemdata_2,
       id_ex_1_immout, id_ex_1_pc_4out, id_ex_1_r1out, id_ex_1_r2out, if_id_1_irout, if_id_1_pc_4out,
       if_id_1_pcout, LedData, mem_wb_1_alures_2, mem_wb_1_memdata_2, mem_wb_1_pc_4out, mem_wb_1_r1_2,
       mips_ram_1_p7, mips_regifile_1_r1, multiplexer_1_out, multiplexer_2_out, multiplexer_7_out,
       multiplexer_8_out, multiplexer_9_out, multiplexer_11_out, multiplexer_13_out, PC_q, R2out, rom_1_data,
       shifter_1_out, shifter_2_out;
  wire [31:2] id_ex_1_irout, mips_alu_1_result_2;
  wire [31:26] id_ex_1_irout_2;

  Button \u_总复位  (.out(RST));
  Button _1 (.out(IR1));
  Button _2 (.out(IR2));
  Button _3 (.out(IR3));
  Button \u_继续运行  (.out(Go));
  LED led_1 (.in(W1));
  LED led_2 (.in(W2));
  LED led_3 (.in(W3));
  Hex_Digit_Display hex_digit_display_1 (.value(LedData[31:28]));  // open: dp
  Multiplexer #(.select(2), .width(32), .enable("false")) multiplexer_1 (
    .in0(id_ex_1_r1out), .in1(id_ex_1_pc_4out), .in2(adder_2_out), .in3({id_ex_1_irout, 2'b00}),
    .out(multiplexer_1_out), .sel(PCsel));
  Multiplexer #(.width(32), .enable("false")) multiplexer_2 (
    .in0(adder_1_out), .in1(multiplexer_1_out), .out(multiplexer_2_out), .sel(IfBranch));
  Hex_Digit_Display hex_digit_display_2 (.value(LedData[27:24]));  // open: dp
  Hex_Digit_Display hex_digit_display_3 (.value(LedData[23:20]));  // open: dp
  and and_1 (and_1_out, clkne, not_1_out);
  Register #(.width(32)) PC (.D(multiplexer_2_out), .en(and_1_out), .Q(PC_q), .clk(CLK), .clr(RST));
  Hex_Digit_Display hex_digit_display_4 (.value(LedData[19:16]));  // open: dp
  Hex_Digit_Display hex_digit_display_5 (.value(LedData[15:12]));  // open: dp
  not not_1 (not_1_out, DataHaZ);
  Adder #(.width(32)) adder_1 (.a(PC_q), .b(32'h4), .out(adder_1_out));  // open: cin, cout
  Hex_Digit_Display hex_digit_display_6 (.value(LedData[11:8]));  // open: dp
  Hex_Digit_Display hex_digit_display_7 (.value(LedData[7:4]));  // open: dp
  Clock clock_1 (.out(CLK));
  Hex_Digit_Display hex_digit_display_8 (.value(LedData[3:0]));  // open: dp
  and and_2 (and_2_out, clkne, not_2_out);
  not not_2 (not_2_out, DataHaZ);
  ROM #(.addrWidth(10), .dataWidth(32)) rom_1 (.addr(PC_q[11:2]), .data(rom_1_data));  // open: sel
  IF_ID if_id_1 (
    .IRin(rom_1_data), .IRout(if_id_1_irout), .PCin(PC_q), .PCout(if_id_1_pcout), .PC_4in(adder_1_out),
    .PC_4out(if_id_1_pc_4out), .WE(and_2_out), .Clk(CLK), .Rst(IfBranch));  // open: BHTData, BHTdata_2
  // Probe on \总周期数 
  // Probe on \无条件分支数 
  // Probe on \条件分支成功数 
  // Probe on \插入气泡数 
  // Probe on \LoadUse次数 
  // Probe on IF_PC
  // Probe on ID_PC
  // Probe on EX_PC
  // Probe on MEM_PC
  \数据相关检测  \u_数据相关检测_1  (
    .OP(if_id_1_irout[31:26]), .EX_WriteReg_num(EX_RegWrite_num), .EX_RegWrite(EX_RegWrite),
    .MEM_WriteReg_num(MEM_RegWrite_num), .MEM_RegWrite(MEM_RegWrite), .\数据相关 (DataHaZ),
    .Func(if_id_1_irout[5:0]), .ID_R1_num(ID_R1), .ID_R2_num(ID_R2));  // open: R1_IDEX, R2_IDEX, R1_IDMEM, R2_IDMEM
  and and_3 (and_3_out, SignedExt, if_id_1_irout[15]);
  Comparator #(.width(32), .mode("unsigned")) comparator_1 (.a(32'ha), .b(R2out), .eq(Syscall10));  // open: gt, lt
  Comparator #(.width(32), .mode("unsigned")) comparator_2 (.a(32'h22), .b(R2out), .eq(is34));  // open: gt, lt
  // Probe on WB_PC
  \硬布线控制器  \u_硬布线控制器_1  (
    .Func(if_id_1_irout[5:0]), .OP(if_id_1_irout[31:26]), .ALU_OP(AluOP), .MemToReg(MemToReg),
    .MemWrite(MemWrite), .ALU_SRC(AluSrcB), .RegWrite(RegWrite), .SysCALL(syscall), .SignedExt(SignedExt),
    .RegDst(\硬布线控制器_1_regdst ), .JR(JR), .JMP(JMP), .Beq(Beq), .JAL(JAL), .Bne(Bne), .BLTZ(BLTZ), .SB(SB),
    .SV(SV));
  Multiplexer #(.width(5), .enable("false")) multiplexer_3 (
    .in0(if_id_1_irout[25:21]), .in1(5'b00100), .out(ID_R1), .sel(Syscall34));
  Multiplexer #(.width(5), .enable("false")) multiplexer_4 (
    .in0(if_id_1_irout[20:16]), .in1(if_id_1_irout[15:11]), .out(multiplexer_4_out), .sel(\硬布线控制器_1_regdst ));
  assign bit_extender_1_out = {{16{and_3_out}}, if_id_1_irout[15:0]};  // Bit_Extender bit_extender_1
  and and_4 (Syscall34, is34, syscall);
  Multiplexer #(.width(5), .enable("false")) multiplexer_5 (
    .in0(if_id_1_irout[20:16]), .in1(5'b00010), .out(ID_R2), .sel(syscall));
  Multiplexer #(.width(5), .enable("false")) multiplexer_6 (
    .in0(multiplexer_4_out), .in1({5{1'b1}}), .out(multiplexer_6_out), .sel(JAL));
  Multiplexer #(.width(32), .enable("false")) multiplexer_7 (
    .in0(multiplexer_13_out), .in1(mem_wb_1_pc_4out), .out(multiplexer_7_out), .sel(ifJAL));
  MIPS_Regifile mips_regifile_1 (
    .Din(multiplexer_7_out), .Clk(CLK), .R1(mips_regifile_1_r1), .R2(R2out), .WE(RegWriteOut),
    .W_num(mem_wb_1_regwriteaddr_2), .R1_num(ID_R1), .R2_num(ID_R2));
  or or_1 (or_1_out, bne_suc, bltz_suc, beq_suc);
  Counter #(.width(16), .max('hffff)) counter_1 (
    .count(clkne), .Q(\总周期数 ), .clk(CLK), .clr(RST));  // open: load, D, carry
  D_Flip_Flop GoPressed (.clk(Go), .D(1'b1), .Q(GoOut), .reset(GoCancel__on_fall_q));  // open: Qn, preset, en
  Counter #(.width(16), .max('hffff)) counter_2 (
    .count(DataHaZ), .Q(\插入气泡数 ), .clk(CLK), .clr(RST));  // open: load, D, carry
  Counter #(.width(16), .max('hffff)) counter_3 (
    .count(or_1_out), .Q(\条件分支成功数 ), .clk(CLK), .clr(RST));  // open: load, D, carry
  D_Flip_Flop GoUsed (.clk(CLK), .D(GoOut), .Q(GoUsed_q), .reset(GoCancel__on_fall_q));  // open: Qn, preset, en
  or or_2 (or_2_out, JMPout, JRout, JALout);
  D_Flip_Flop #(.trigger("falling")) GoCancel__on_fall (
    .clk(CLK), .D(GoUsed_q), .Q(GoCancel__on_fall_q), .reset(RST));  // open: Qn, preset, en
  Counter #(.width(16), .max('hffff)) counter_4 (
    .count(or_2_out), .Q(\无条件分支数 ), .clk(CLK), .clr(RST));  // open: load, D, carry
  or or_3 (or_3_out, DataHaZ, IfBranch);
  ID_EX id_ex_1 (
    .IRin(if_id_1_irout), .IRout({id_ex_1_irout_2, id_ex_1_irout[27:2]}), .PCin(if_id_1_pcout),
    .PCout({id_ex_1_irout[31:28], id_ex_1_pcout}), .PC_4in(if_id_1_pc_4out), .PC_4out(id_ex_1_pc_4out),
    .WE(clkne), .Clk(CLK), .Rst(or_3_out), .Immin(bit_extender_1_out), .Immout(id_ex_1_immout),
    .MemToReg(MemToReg), .MemToReg_2(id_ex_1_memtoreg_2), .MemWrite(MemWrite),
    .MemWrite_2(id_ex_1_memwrite_2), .AluSRC(AluSrcB), .AluSRC_2(id_ex_1_alusrc_2), .RegWrite(RegWrite),
    .RegWrite_2(EX_RegWrite), .Syscall(syscall), .Syscall_2(id_ex_1_syscall_2), .SignedExt(SignedExt),
    .RegDst(\硬布线控制器_1_regdst ), .Beq(Beq), .Beq_2(Beqout), .Bne(Bne), .Bne_2(Bneout), .JR(JR), .JR_2(JRout),
    .JMP(JMP), .JMP_2(JMPout), .JAL(JAL), .JAL_2(JALout), .BLTZ(BLTZ), .BLTZ_2(BLTZout), .SB(SB),
    .SB_2(id_ex_1_sb_2), .SV(SV), .SV_2(id_ex_1_sv_2), .AluOP(AluOP), .AluOP_2(id_ex_1_aluop_2),
    .R1in(mips_regifile_1_r1), .R1out(id_ex_1_r1out), .R2in(R2out), .R2out(id_ex_1_r2out),
    .RegWriteAddr(multiplexer_6_out), .RegWriteAddr_2(EX_RegWrite_num), .Syscall34(is34),
    .Syscall34_2(id_ex_1_syscall34_2), .Syscall10(Syscall10), .Syscall10_2(id_ex_1_syscall10_2));  // open: SignedExt_2, RegDst_2, R1_sel, R1_sel_2, R2_sel, R2_sel_2, BHTData, BHTData_2
  Shifter #(.width(32)) shifter_1 (.in(id_ex_1_immout), .\dist (5'b00010), .out(shifter_1_out));
  Adder #(.width(32)) adder_2 (.a(id_ex_1_pc_4out), .b(shifter_1_out), .out(adder_2_out));  // open: cin, cout
  Multiplexer #(.width(32), .enable("false")) multiplexer_8 (
    .in0(id_ex_1_r2out), .in1(id_ex_1_immout), .out(multiplexer_8_out), .sel(id_ex_1_alusrc_2));
  Comparator #(.width(2)) comparator_3 (.a(PCsel), .b(2'b01), .eq(comparator_3_eq));  // open: gt, lt
  Multiplexer #(.width(32), .enable("false")) multiplexer_9 (
    .in0(multiplexer_8_out), .in1({32{1'b0}}), .out(multiplexer_9_out), .sel(BLTZout));
  Multiplexer #(.width(5), .enable("false")) multiplexer_10 (
    .in0(id_ex_1_irout[12:8]), .in1(id_ex_1_r1out[4:0]), .out(multiplexer_10_out), .sel(id_ex_1_sv_2));
  Shifter #(.width(32)) shifter_2 (.in(id_ex_1_r2out), .\dist (shifter_3_out), .out(shifter_2_out));
  Shifter #(.width(5)) shifter_3 (.in({3'b000, mips_alu_1_result[1], less}), .\dist (3'b011), .out(shifter_3_out));
  temp temp_1 (
    .jmp(JMPout), .jr(JRout), .jal(JALout), .beq(beq_suc), .bne(bne_suc), .bltz(bltz_suc), .sel1(PCsel[1]),
    .sel0(PCsel[0]));
  not not_3 (IfBranch, comparator_3_eq);
  MIPS_ALU mips_alu_1 (
    .X(id_ex_1_r1out), .Y(multiplexer_9_out), .AluOP(id_ex_1_aluop_2), .Equal(equal),
    .Result({mips_alu_1_result_2, mips_alu_1_result[1], less}), .shamt(multiplexer_10_out));  // open: Result_2
  Decoder #(.select(2)) decoder_1 (
    .out0(decoder_1_out0[0]), .out1(decoder_1_out0[1]), .out2(decoder_1_out0[2]), .out3(decoder_1_out0[3]),
    .sel({mips_alu_1_result[1], less}));  // open: en
  and and_5 (beq_suc, Beqout, equal);
  and and_6 (bne_suc, Bneout, ~equal);  // AND_Gate
  and and_7 (bltz_suc, BLTZout, less);
  EX_MEM ex_mem_1 (
    .MemToReg(id_ex_1_memtoreg_2), .MemToReg_2(ex_mem_1_memtoreg_2), .MemWrite(id_ex_1_memwrite_2),
    .MemWrite_2(ex_mem_1_memwrite_2), .IRin({id_ex_1_irout_2, id_ex_1_irout[27:2]}), .IRout(ex_mem_1_irout),
    .RegWrite(EX_RegWrite), .RegWrite_2(MEM_RegWrite), .PCin({id_ex_1_irout[31:28], id_ex_1_pcout}),
    .PCout(ex_mem_1_pcout), .Syscall(id_ex_1_syscall_2), .Syscall_2(ex_mem_1_syscall_2),
    .PC_4in(id_ex_1_pc_4out), .PC_4out(ex_mem_1_pc_4out), .RegWriteAddr(EX_RegWrite_num),
    .RegWriteAddr_2(MEM_RegWrite_num), .WE(clkne), .Clk(CLK), .Rst(RST),
    .AluRes({mips_alu_1_result_2, mips_alu_1_result[1], less}),
    .AluRes_2({ex_mem_1_alures_2[31:22], ex_mem_1_alures_2_2, ex_mem_1_alures_2[1:0]}), .R2in(id_ex_1_r2out),
    .R2out(ex_mem_1_r2out), .SBMemdata(shifter_2_out), .SBMemdata_2(ex_mem_1_sbmemdata_2), .SB(id_ex_1_sb_2),
    .SB_2(ex_mem_1_sb_2), .MemselSB(decoder_1_out0), .MemselSB_2(ex_mem_1_memselsb_2), .JAL(JALout),
    .JAL_2(ex_mem_1_jal_2), .Syscall34(id_ex_1_syscall34_2), .Syscall34_2(ex_mem_1_syscall34_2),
    .Syscall10(id_ex_1_syscall10_2), .Syscall10_2(ex_mem_1_syscall10_2), .R1in(id_ex_1_r1out),
    .R1out(ex_mem_1_r1out));
  Multiplexer #(.width(32), .enable("false")) multiplexer_11 (
    .in0(ex_mem_1_r2out), .in1(ex_mem_1_sbmemdata_2), .out(multiplexer_11_out), .sel(ex_mem_1_sb_2));
  Multiplexer #(.width(4), .enable("false")) multiplexer_12 (
    .in0(4'b1111), .in1(ex_mem_1_memselsb_2), .out(multiplexer_12_out), .sel(ex_mem_1_sb_2));
  // MIPS_RAM mips_ram_1: pin names not known; wires that end beside it: ex_mem_1_alures_2_2, multiplexer_11_out, ex_mem_1_memwrite_2, multiplexer_12_out, CLK, RST, mips_ram_1_p7
  MEM_WB mem_wb_1 (
    .MemToReg(ex_mem_1_memtoreg_2), .MemToReg_2(mem_wb_1_memtoreg_2), .IRin(ex_mem_1_irout),
    .MemData(mips_ram_1_p7), .MemData_2(mem_wb_1_memdata_2), .RegWrite(MEM_RegWrite),
    .RegWrite_2(RegWriteOut), .PCin(ex_mem_1_pcout), .Syscall(ex_mem_1_syscall_2),
    .Syscall_2(mem_wb_1_syscall_2), .PC_4in(ex_mem_1_pc_4out), .PC_4out(mem_wb_1_pc_4out),
    .RegWriteAddr(MEM_RegWrite_num), .RegWriteAddr_2(mem_wb_1_regwriteaddr_2),
    .AluRes({ex_mem_1_alures_2[31:22], ex_mem_1_alures_2_2, ex_mem_1_alures_2[1:0]}),
    .AluRes_2(mem_wb_1_alures_2), .WE(clkne), .Clk(CLK), .Rst(RST), .JAL(ex_mem_1_jal_2), .JAL_2(ifJAL),
    .Syscall34(ex_mem_1_syscall34_2), .Syscall34_2(mem_wb_1_syscall34_2), .Syscall10(ex_mem_1_syscall10_2),
    .Syscall10_2(mem_wb_1_syscall10_2), .R1(ex_mem_1_r1out), .R1_2(mem_wb_1_r1_2));  // open: IRout, PCout
  Multiplexer #(.width(32), .enable("false")) multiplexer_13 (
    .in0(mem_wb_1_alures_2), .in1(mem_wb_1_memdata_2), .out(multiplexer_13_out), .sel(mem_wb_1_memtoreg_2));
  and and_8 (and_8_out, mem_wb_1_syscall_2, mem_wb_1_syscall34_2);
  and and_9 (and_9_out, or_4_out, mem_wb_1_syscall_2);
  or or_4 (or_4_out, mem_wb_1_syscall10_2, and_10_out);
  and and_10 (and_10_out, ~mem_wb_1_syscall34_2, ~GoOut);  // AND_Gate
  not not_4 (clkne, and_9_out);
  Register #(.width(32)) register_1 (.D(mem_wb_1_r1_2), .en(and_8_out), .Q(LedData), .clk(CLK), .clr(RST));

  // Other names for the same wires on the sheet: ifBubble = DataHaZ

  // Notes on the sheet:
  //   中断源
  //   中断等待指示
  //   数码管输出
  //   指令存储器
  //   contents of rom_1 (hex, n*v repeats v):
  //   20110020 20020022 8000c06 20110000 20110000 2002000a 10000003 20110000 20110000 2002000a 14110003
  //   20110000 20110000 2002000a c000c14 2002000a 0 0 0 c 2231ffff 0 0 0 112020 0 0 0 c 1620fff6 3e00008
  //   指令字
  //   OP
  //   Func
  //   rs
  //   rt
  //   rd
  //   10#10 (exit)
  //   10#34 (print hex)
  //   流水调试日志用
  //   JMP
  //   JR
  //   OP
  //   Func
  //   Beq
  //   Bne
  //   MemToReg
  //   MemWrite
  //   AluOP
  //   AluSrcB
  //   RegWrite
  //   JAL
  //   RegDst
  //   Syscall
  //   Syscall34
endmodule

module \重定向流水线  (
);

  wire AluSrcB, and_3_out, and_4_out, and_6_out, and_7_out, and_12_out, and_13_out, and_14_out, Beq, beq_suc,
       Beqout, BLTZ, bltz_suc, BLTZout, Bne, bne_suc, Bneout, Branch, CLK, clkne, comparator_4_eq, DataHaZ,
       equal, ex_mem_1_jal_2, ex_mem_1_memtoreg_2, ex_mem_1_memwrite_2, ex_mem_1_sb_2, ex_mem_1_syscall10_2,
       ex_mem_1_syscall34_2, ex_mem_1_syscall_2, EX_RegWrite, Go, GoCancel__on_fall_q, GoOut, GoUsed_q,
       HITWrong, HITYes, id_ex_1_alusrc_2, id_ex_1_memtoreg_2, id_ex_1_memwrite_2, id_ex_1_sb_2,
       id_ex_1_sv_2, IfBranch, ifBubble, ifJAL, IR1, IR2, IR3, is34, JAL, JALout, JMP, JMPout, JR, JRout,
       less, MEM_RegWrite, mem_wb_1_memtoreg_2, mem_wb_1_syscall10_2, mem_wb_1_syscall34_2,
       mem_wb_1_syscall_2, MemToReg, MemWrite, NoHitBranch, not_1_out, not_2_out, or_4_out, or_5_out,
       or_6_out, or_7_out, or_8_out, PreRes, RegWrite, RegWriteOut, RST, SB, SignedExt, SV, syscall,
       Syscall10, Syscall34, syscallout, W1, W2, W3, WeLRU, WePredict, \数据相关检测_1_r1_idex ,
       \数据相关检测_1_r1_idmem , \数据相关检测_1_r2_idex , \数据相关检测_1_r2_idmem , \硬布线控制器_1_regdst ;
  wire [0:0] bht_1_hit;
  wire [1:0] bht_1_predict, id_ex_1_r1_sel_2, id_ex_1_r2_sel_2, multiplexer_4_out, multiplexer_5_out,
       multiplexer_6_out, PCsel, R1_sel, R2_sel, write_predict;
  wire [1:1] mips_alu_1_result;
  wire [2:0] bht_1_hitnum, bht_1_insertnum, write_address;
  wire [3:0] AluOP, decoder_1_out0, ex_mem_1_memselsb_2, id_ex_1_aluop_2, multiplexer_20_out;
  wire [4:0] EX_RegWrite_num, ID_R1, ID_R2, if_id_1_irout, MEM_RegWrite_num, mem_wb_1_regwriteaddr_2,
       multiplexer_10_out, multiplexer_12_out, multiplexer_18_out, shifter_3_out;
  wire [8:0] BHTdata, if_id_1_bhtdata_2;
  wire [15:0] \LoadUse次数 , \实际分支数 , \总周期数 , \插入气泡数 , \无条件分支数 , \条件分支成功数 ;
  wire [31:0] adder_1_out, adder_2_out, alures, bht_1_branchaddr, bit_extender_1_out, ex_mem_1_pc_4out,
       ex_mem_1_r1out, ex_mem_1_r2out, ex_mem_1_sbmemdata_2, EX_PC, EXIR, fromalu, frommem, id_ex_1_immout,
       id_ex_1_pc_4out, id_ex_1_r1out, id_ex_1_r2out, ID_PC, if_id_1_irout_2, if_id_1_pc_4out, IF_PC,
       LedData, MEM_PC, mem_wb_1_pc_4out, mem_wb_1_r1_2, MEMIR, mips_ram_1_p7, mips_regifile_1_r1,
       mips_regifile_1_r2, multiplexer_2_out, multiplexer_3_out, multiplexer_7_out, multiplexer_13_out,
       multiplexer_14_out, multiplexer_16_out, multiplexer_17_out, multiplexer_19_out, multiplexer_21_out,
       R2out, rom_1_data, shifter_1_out, shifter_2_out, WB_PC;
  wire [31:2] mips_alu_1_result_2;

  Button \u_总复位  (.out(RST));
  Button _1 (.out(IR1));
  Button _2 (.out(IR2));
  Button _3 (.out(IR3));
  Button \u_继续运行  (.out(Go));
  LED led_1 (.in(W1));
  LED led_2 (.in(W2));
  LED led_3 (.in(W3));
  Hex_Digit_Display hex_digit_display_1 (.value(LedData[31:28]));  // open: dp
  Comparator #(.width(32)) comparator_1 (.a(ID_PC), .b(multiplexer_2_out), .eq(PreRes));  // open: gt, lt
  Multiplexer #(.width(3), .enable("false")) multiplexer_1 (
    .in0(BHTdata[8:6]), .in1(BHTdata[5:3]), .out(write_address), .sel(BHTdata[0]));
  Hex_Digit_Display hex_digit_display_2 (.value(LedData[23:20]));  // open: dp
  Hex_Digit_Display hex_digit_display_3 (.value(LedData[27:24]));  // open: dp
  and and_1 (HITWrong, ~PreRes, BHTdata[0]);  // AND_Gate
  and and_2 (HITYes, PreRes, BHTdata[0]);
  or or_1 (WePredict, NoHitBranch, HITYes, HITWrong);
  Multiplexer #(.select(2), .width(32), .enable("false")) multiplexer_2 (
    .in0(multiplexer_14_out), .in1(id_ex_1_pc_4out), .in2(adder_2_out),
    .in3({EX_PC[31:28], EXIR[25:0], 2'b00}), .out(multiplexer_2_out), .sel(PCsel));
  Hex_Digit_Display hex_digit_display_4 (.value(LedData[19:16]));  // open: dp
  Hex_Digit_Display hex_digit_display_5 (.value(LedData[15:12]));  // open: dp
  or or_2 (WeLRU, HITYes, NoHitBranch);
  and and_3 (and_3_out, clkne, not_1_out);
  Register #(.width(32)) PC (.D(multiplexer_3_out), .en(and_3_out), .Q(IF_PC), .clk(CLK), .clr(RST));
  Multiplexer #(.width(32), .enable("false")) multiplexer_3 (
    .in0(multiplexer_7_out), .in1(multiplexer_2_out), .out(multiplexer_3_out), .sel(Branch));
  and and_4 (and_4_out, bht_1_predict[1], bht_1_hit[0]);
  BHT bht_1 (
    .Clk(CLK), .write_valid(NoHitBranch), .we_valid(NoHitBranch), .we_pc(NoHitBranch), .write_pc(EX_PC),
    .we_branch(NoHitBranch), .cur_pc(IF_PC), .we_predict(WePredict), .write_branch(multiplexer_2_out),
    .we_lru(WeLRU), .write_predict(write_predict), .Hit(bht_1_hit[0]), .HitNum(bht_1_hitnum),
    .BranchAddr(bht_1_branchaddr), .InsertNum(bht_1_insertnum), .predict(bht_1_predict),
    .write_address(write_address));
  Multiplexer #(.select(2), .width(2), .enable("false")) multiplexer_4 (
    .in0(2'b00), .in1(2'b00), .in2(2'b01), .in3(2'b10), .out(multiplexer_4_out), .sel(BHTdata[2:1]));
  Multiplexer #(.select(2), .width(2), .enable("false")) multiplexer_5 (
    .in0(2'b01), .in1(2'b10), .in2(2'b11), .in3(2'b11), .out(multiplexer_5_out), .sel(BHTdata[2:1]));
  Hex_Digit_Display hex_digit_display_6 (.value(LedData[7:4]));  // open: dp
  Hex_Digit_Display hex_digit_display_7 (.value(LedData[11:8]));  // open: dp
  and and_5 (NoHitBranch, ~BHTdata[0], IfBranch);  // AND_Gate
  not not_1 (not_1_out, ifBubble);
  Adder #(.width(32)) adder_1 (.a(IF_PC), .b(32'h4), .out(adder_1_out));  // open: cin, cout
  Multiplexer #(.width(2), .enable("false")) multiplexer_6 (
    .in0(multiplexer_4_out), .in1(multiplexer_5_out), .out(multiplexer_6_out), .sel(PreRes));
  Hex_Digit_Display hex_digit_display_8 (.value(LedData[3:0]));  // open: dp
  Counter #(.width(16), .max('hffff)) counter_1 (
    .count(ifBubble), .Q(\LoadUse次数 ), .clk(CLK), .clr(RST));  // open: load, D, carry
  or or_3 (Branch, NoHitBranch, HITWrong);
  Multiplexer #(.width(32), .enable("false")) multiplexer_7 (
    .in0(adder_1_out), .in1(bht_1_branchaddr), .out(multiplexer_7_out), .sel(and_4_out));
  and and_6 (and_6_out, clkne, not_2_out);
  not not_2 (not_2_out, ifBubble);
  ROM #(.addrWidth(10), .dataWidth(32)) rom_1 (.addr(IF_PC[11:2]), .data(rom_1_data));  // open: sel
  Multiplexer #(.width(2), .enable("false")) multiplexer_8 (
    .in0(2'b10), .in1(multiplexer_6_out), .out(write_predict), .sel(BHTdata[0]));
  // Probe on \总周期数 
  // Probe on \无条件分支数 
  // Probe on \条件分支成功数 
  // Probe on \插入气泡数 
  // Probe on \LoadUse次数 
  // Probe on \实际分支数 
  IF_ID if_id_1 (
    .IRin(rom_1_data), .IRout({if_id_1_irout_2[31:21], if_id_1_irout, if_id_1_irout_2[15:0]}), .PCin(IF_PC),
    .PCout(ID_PC), .PC_4in(adder_1_out), .PC_4out(if_id_1_pc_4out), .WE(and_6_out), .Clk(CLK), .Rst(Branch),
    .BHTData({bht_1_insertnum, bht_1_hitnum, bht_1_predict, bht_1_hit[0]}), .BHTdata_2(if_id_1_bhtdata_2));
  // Probe on IF_PC[11:2]
  // Probe on ID_PC[11:2]
  // Probe on MEM_PC[11:2]
  // Probe on EX_PC[11:2]
  Redirect redirect_1 (
    .R1_IDEX(\数据相关检测_1_r1_idex ), .R1_IDMEM(\数据相关检测_1_r1_idmem ), .R2_IDEX(\数据相关检测_1_r2_idex ),
    .R2_IDMEM(\数据相关检测_1_r2_idmem ), .OP(MEMIR[31:26]), .R1_sel(R1_sel), .Func(MEMIR[5:0]), .R2_sel(R2_sel),
    .IR(EXIR), .load_use(ifBubble));
  // Probe on WB_PC[11:2]
  \数据相关检测  \u_数据相关检测_1  (
    .OP(if_id_1_irout_2[31:26]), .EX_WriteReg_num(EX_RegWrite_num), .EX_RegWrite(EX_RegWrite),
    .MEM_WriteReg_num(MEM_RegWrite_num), .MEM_RegWrite(MEM_RegWrite), .\数据相关 (DataHaZ),
    .Func(if_id_1_irout_2[5:0]), .ID_R1_num(ID_R1), .ID_R2_num(ID_R2), .R1_IDEX(\数据相关检测_1_r1_idex ),
    .R2_IDEX(\数据相关检测_1_r2_idex ), .R1_IDMEM(\数据相关检测_1_r1_idmem ), .R2_IDMEM(\数据相关检测_1_r2_idmem ));
  and and_7 (and_7_out, SignedExt, if_id_1_irout_2[15]);
  Comparator #(.width(32), .mode("unsigned")) comparator_2 (.a(32'ha), .b(R2out), .eq(Syscall10));  // open: gt, lt
  Comparator #(.width(32), .mode("unsigned")) comparator_3 (.a(32'h22), .b(R2out), .eq(is34));  // open: gt, lt
  \硬布线控制器  \u_硬布线控制器_1  (
    .Func(if_id_1_irout_2[5:0]), .OP(if_id_1_irout_2[31:26]), .ALU_OP(AluOP), .MemToReg(MemToReg),
    .MemWrite(MemWrite), .ALU_SRC(AluSrcB), .RegWrite(RegWrite), .SysCALL(syscall), .SignedExt(SignedExt),
    .RegDst(\硬布线控制器_1_regdst ), .JR(JR), .JMP(JMP), .Beq(Beq), .JAL(JAL), .Bne(Bne), .BLTZ(BLTZ), .SB(SB),
    .SV(SV));
  Multiplexer #(.width(5), .enable("false")) multiplexer_9 (
    .in0(if_id_1_irout_2[25:21]), .in1(5'b00100), .out(ID_R1), .sel(syscall));
  Multiplexer #(.width(5), .enable("false")) multiplexer_10 (
    .in0(if_id_1_irout), .in1(if_id_1_irout_2[15:11]), .out(multiplexer_10_out), .sel(\硬布线控制器_1_regdst ));
  assign bit_extender_1_out = {{16{and_7_out}}, if_id_1_irout_2[15:0]};  // Bit_Extender bit_extender_1
  and and_8 (Syscall34, is34, syscallout);
  Multiplexer #(.width(5), .enable("false")) multiplexer_11 (
    .in0(if_id_1_irout), .in1(5'b00010), .out(ID_R2), .sel(syscall));
  Multiplexer #(.width(5), .enable("false")) multiplexer_12 (
    .in0(multiplexer_10_out), .in1({5{1'b1}}), .out(multiplexer_12_out), .sel(JAL));
  Multiplexer #(.width(32), .enable("false")) multiplexer_13 (
    .in0(multiplexer_21_out), .in1(mem_wb_1_pc_4out), .out(multiplexer_13_out), .sel(ifJAL));
  Counter #(.width(16), .max('hffff)) counter_2 (
    .count(Branch), .Q(\实际分支数 ), .clk(CLK), .clr(RST));  // open: load, D, carry
  or or_4 (or_4_out, ifBubble, Branch);
  Clock clock_1 (.out(CLK));
  MIPS_Regifile mips_regifile_1 (
    .Din(multiplexer_13_out), .Clk(CLK), .R1(mips_regifile_1_r1), .R2(mips_regifile_1_r2), .WE(RegWriteOut),
    .W_num(mem_wb_1_regwriteaddr_2), .R1_num(ID_R1), .R2_num(ID_R2));
  or or_5 (or_5_out, bne_suc, bltz_suc, beq_suc);
  Counter #(.width(16), .max('hffff)) counter_3 (
    .count(clkne), .Q(\总周期数 ), .clk(CLK), .clr(RST));  // open: load, D, carry
  // Probe on id_ex_1_r1_sel_2
  // Probe on id_ex_1_r2_sel_2
  D_Flip_Flop GoPressed (.clk(Go), .D(1'b1), .Q(GoOut), .reset(GoCancel__on_fall_q));  // open: Qn, preset, en
  Counter #(.width(16), .max('hffff)) counter_4 (
    .count(or_4_out), .Q(\插入气泡数 ), .clk(CLK), .clr(RST));  // open: load, D, carry
  Counter #(.width(16), .max('hffff)) counter_5 (
    .count(or_5_out), .Q(\条件分支成功数 ), .clk(CLK), .clr(RST));  // open: load, D, carry
  Multiplexer #(.select(2), .width(32), .enable("false")) multiplexer_14 (
    .in0(id_ex_1_r1out), .in1(fromalu), .in2(frommem), .in3(alures), .out(multiplexer_14_out),
    .sel(id_ex_1_r1_sel_2));
  Multiplexer #(.select(2), .width(32), .enable("false")) multiplexer_15 (
    .in0(id_ex_1_r2out), .in1(fromalu), .in2(frommem), .in3(alures), .out(R2out), .sel(id_ex_1_r2_sel_2));
  D_Flip_Flop GoUsed (.clk(CLK), .D(GoOut), .Q(GoUsed_q), .reset(GoCancel__on_fall_q));  // open: Qn, preset, en
  or or_6 (or_6_out, JMPout, JRout, JALout);
  D_Flip_Flop #(.trigger("falling")) GoCancel__on_fall (
    .clk(CLK), .D(GoUsed_q), .Q(GoCancel__on_fall_q), .reset(RST));  // open: Qn, preset, en
  Counter #(.width(16), .max('hffff)) counter_6 (
    .count(or_6_out), .Q(\无条件分支数 ), .clk(CLK), .clr(RST));  // open: load, D, carry
  or or_7 (or_7_out, ifBubble, Branch);
  ID_EX id_ex_1 (
    .IRin({if_id_1_irout_2[31:21], if_id_1_irout, if_id_1_irout_2[15:0]}), .IRout(EXIR), .PCin(ID_PC),
    .PCout(EX_PC), .PC_4in(if_id_1_pc_4out), .PC_4out(id_ex_1_pc_4out), .WE(clkne), .Clk(CLK),
    .Rst(or_7_out), .Immin(bit_extender_1_out), .Immout(id_ex_1_immout), .MemToReg(MemToReg),
    .MemToReg_2(id_ex_1_memtoreg_2), .MemWrite(MemWrite), .MemWrite_2(id_ex_1_memwrite_2), .AluSRC(AluSrcB),
    .AluSRC_2(id_ex_1_alusrc_2), .RegWrite(RegWrite), .RegWrite_2(EX_RegWrite), .Syscall(syscall),
    .Syscall_2(syscallout), .SignedExt(SignedExt), .RegDst(\硬布线控制器_1_regdst ), .Beq(Beq), .Beq_2(Beqout),
    .Bne(Bne), .Bne_2(Bneout), .JR(JR), .JR_2(JRout), .JMP(JMP), .JMP_2(JMPout), .JAL(JAL), .JAL_2(JALout),
    .BLTZ(BLTZ), .BLTZ_2(BLTZout), .SB(SB), .SB_2(id_ex_1_sb_2), .SV(SV), .SV_2(id_ex_1_sv_2), .AluOP(AluOP),
    .AluOP_2(id_ex_1_aluop_2), .R1in(mips_regifile_1_r1), .R1out(id_ex_1_r1out), .R2in(mips_regifile_1_r2),
    .R2out(id_ex_1_r2out), .RegWriteAddr(multiplexer_12_out), .RegWriteAddr_2(EX_RegWrite_num),
    .R1_sel(R1_sel), .R1_sel_2(id_ex_1_r1_sel_2), .R2_sel(R2_sel), .R2_sel_2(id_ex_1_r2_sel_2),
    .BHTData(if_id_1_bhtdata_2), .BHTData_2(BHTdata));  // open: SignedExt_2, RegDst_2, Syscall34, Syscall34_2, Syscall10, Syscall10_2
  Shifter #(.width(32)) shifter_1 (.in(id_ex_1_immout), .\dist (5'b00010), .out(shifter_1_out));
  Adder #(.width(32)) adder_2 (.a(id_ex_1_pc_4out), .b(shifter_1_out), .out(adder_2_out));  // open: cin, cout
  Multiplexer #(.width(32), .enable("false")) multiplexer_16 (
    .in0(R2out), .in1(id_ex_1_immout), .out(multiplexer_16_out), .sel(id_ex_1_alusrc_2));
  Multiplexer #(.width(32), .enable("false")) multiplexer_17 (
    .in0(multiplexer_16_out), .in1({32{1'b0}}), .out(multiplexer_17_out), .sel(BLTZout));
  Multiplexer #(.width(5), .enable("false")) multiplexer_18 (
    .in0(EXIR[10:6]), .in1(multiplexer_14_out[4:0]), .out(multiplexer_18_out), .sel(id_ex_1_sv_2));
  Shifter #(.width(32)) shifter_2 (.in(R2out), .\dist (shifter_3_out), .out(shifter_2_out));
  temp temp_1 (
    .jmp(JMPout), .jr(JRout), .jal(JALout), .beq(beq_suc), .bne(bne_suc), .bltz(bltz_suc), .sel1(PCsel[1]),
    .sel0(PCsel[0]));
  Comparator #(.width(2)) comparator_4 (.a(PCsel), .b(2'b01), .eq(comparator_4_eq));  // open: gt, lt
  not not_3 (IfBranch, comparator_4_eq);
  MIPS_ALU mips_alu_1 (
    .X(multiplexer_14_out), .Y(multiplexer_17_out), .AluOP(id_ex_1_aluop_2), .Equal(equal),
    .Result({mips_alu_1_result_2, mips_alu_1_result[1], less}), .shamt(multiplexer_18_out));  // open: Result_2
  Shifter #(.width(5)) shifter_3 (.in({3'b000, mips_alu_1_result[1], less}), .\dist (3'b011), .out(shifter_3_out));
  Decoder #(.select(2)) decoder_1 (
    .out0(decoder_1_out0[0]), .out1(decoder_1_out0[1]), .out2(decoder_1_out0[2]), .out3(decoder_1_out0[3]),
    .sel({mips_alu_1_result[1], less}));  // open: en
  and and_9 (beq_suc, Beqout, equal);
  and and_10 (bne_suc, Bneout, ~equal);  // AND_Gate
  and and_11 (bltz_suc, BLTZout, less);
  EX_MEM ex_mem_1 (
    .MemToReg(id_ex_1_memtoreg_2), .MemToReg_2(ex_mem_1_memtoreg_2), .MemWrite(id_ex_1_memwrite_2),
    .MemWrite_2(ex_mem_1_memwrite_2), .IRin(EXIR), .IRout(MEMIR), .RegWrite(EX_RegWrite),
    .RegWrite_2(MEM_RegWrite), .PCin(EX_PC), .PCout(MEM_PC), .Syscall(syscallout),
    .Syscall_2(ex_mem_1_syscall_2), .PC_4in(id_ex_1_pc_4out), .PC_4out(ex_mem_1_pc_4out),
    .RegWriteAddr(EX_RegWrite_num), .RegWriteAddr_2(MEM_RegWrite_num), .WE(clkne), .Clk(CLK), .Rst(RST),
    .AluRes({mips_alu_1_result_2, mips_alu_1_result[1], less}), .AluRes_2(alures), .R2in(R2out),
    .R2out(ex_mem_1_r2out), .SBMemdata(shifter_2_out), .SBMemdata_2(ex_mem_1_sbmemdata_2), .SB(id_ex_1_sb_2),
    .SB_2(ex_mem_1_sb_2), .MemselSB(decoder_1_out0), .MemselSB_2(ex_mem_1_memselsb_2), .JAL(JALout),
    .JAL_2(ex_mem_1_jal_2), .Syscall34(is34), .Syscall34_2(ex_mem_1_syscall34_2), .Syscall10(Syscall10),
    .Syscall10_2(ex_mem_1_syscall10_2), .R1in(multiplexer_14_out), .R1out(ex_mem_1_r1out));
  Multiplexer #(.width(32), .enable("false")) multiplexer_19 (
    .in0(ex_mem_1_r2out), .in1(ex_mem_1_sbmemdata_2), .out(multiplexer_19_out), .sel(ex_mem_1_sb_2));
  Multiplexer #(.width(4), .enable("false")) multiplexer_20 (
    .in0(4'b1111), .in1(ex_mem_1_memselsb_2), .out(multiplexer_20_out), .sel(ex_mem_1_sb_2));
  // MIPS_RAM mips_ram_1: pin names not known; wires that end beside it: alures[21:2], multiplexer_19_out, ex_mem_1_memwrite_2, multiplexer_20_out, CLK, RST, mips_ram_1_p7
  MEM_WB mem_wb_1 (
    .MemToReg(ex_mem_1_memtoreg_2), .MemToReg_2(mem_wb_1_memtoreg_2), .IRin(MEMIR), .MemData(mips_ram_1_p7),
    .MemData_2(frommem), .RegWrite(MEM_RegWrite), .RegWrite_2(RegWriteOut), .PCin(MEM_PC), .PCout(WB_PC),
    .Syscall(ex_mem_1_syscall_2), .Syscall_2(mem_wb_1_syscall_2), .PC_4in(ex_mem_1_pc_4out),
    .PC_4out(mem_wb_1_pc_4out), .RegWriteAddr(MEM_RegWrite_num), .RegWriteAddr_2(mem_wb_1_regwriteaddr_2),
    .AluRes(alures), .AluRes_2(fromalu), .WE(clkne), .Clk(CLK), .Rst(RST), .JAL(ex_mem_1_jal_2),
    .JAL_2(ifJAL), .Syscall34(ex_mem_1_syscall34_2), .Syscall34_2(mem_wb_1_syscall34_2),
    .Syscall10(ex_mem_1_syscall10_2), .Syscall10_2(mem_wb_1_syscall10_2), .R1(ex_mem_1_r1out),
    .R1_2(mem_wb_1_r1_2));  // open: IRout
  Multiplexer #(.width(32), .enable("false")) multiplexer_21 (
    .in0(fromalu), .in1(frommem), .out(multiplexer_21_out), .sel(mem_wb_1_memtoreg_2));
  and and_12 (and_12_out, mem_wb_1_syscall_2, mem_wb_1_syscall34_2);
  and and_13 (and_13_out, or_8_out, mem_wb_1_syscall_2);
  or or_8 (or_8_out, mem_wb_1_syscall10_2, and_14_out);
  and and_14 (and_14_out, ~mem_wb_1_syscall34_2, ~GoOut);  // AND_Gate
  not not_4 (clkne, and_13_out);
  Register #(.width(32)) register_1 (.D(mem_wb_1_r1_2), .en(and_12_out), .Q(LedData), .clk(CLK), .clr(RST));

  // Other names for the same wires on the sheet: HIT = BHTdata[0]; Predict[1:0] = BHTdata[2:1];
  //   HitRow[2:0] = BHTdata[5:3]; InsertRow[2:0] = BHTdata[8:6]; load_use = ifBubble

  // Notes on the sheet:
  //   中断源
  //   中断等待指示
  //   数码管输出
  //   指令存储器
  //   contents of rom_1 (hex, n*v repeats v):
  //   20110001 8000c05 20110001 20120002 20130003 8000c09 20110001 20120002 20130003 8000c0d 20110001
  //   20120002 20130003 8000c11 20110001 20120002 20130003 c000cbb 20100001 20110001 118fc0 112020
  //   20020022 c 118882 12200001 8000c15 112020 20020022 c 20110001 118880 112020 20020022 c 12200001
  //   8000c1f 20110001 118fc0 112020 20020022 c 1188c3 112020 20020022 c 118903 112020 20020022 c 118903
  //   112020 20020022 c 118903 112020 20020022 c 118903 112020 20020022 c 118903 112020 20020022 c 118903
  //   112020 20020022 c 118903 112020 20020022 c 20100001 109fc0 139fc3 8021 2012000c 24160003 26100001
  //   3210000f 20080008 20090001 139900 2709825 132020 20020022 c 1094022 1500fff9 22100001 2018000f
  //   2188024 108700 20080008 20090001 139902 2709825 132021 20020022 c 1094022 1500fff9 108702 2c9b022
  //   12c00001 8000c50 4020 1084027 84400 3508ffff 82021 20020022 c 2010ffff 20110000 ae300000 22100001
  //   22310004 ae300000 22100001 22310004 ae300000 22100001 22310004 ae300000 22100001 22310004 ae300000
  //   22100001 22310004 ae300000 22100001 22310004 ae300000 22100001 22310004 ae300000 22100001 22310004
  //   ae300000 22100001 22310004 ae300000 22100001 22310004 ae300000 22100001 22310004 ae300000 22100001
  //   22310004 ae300000 22100001 22310004 ae300000 22100001 22310004 ae300000 22100001 22310004 ae300000
  //   22100001 22310004 22100001 8020 2011003c 8e130000 8e340000 274402a 11000002 ae330000 ae140000
  //   2231fffc 1611fff8 102020 20020022 c 22100004 2011003c 1611fff2 20020032 c 8000c00 2002000a c
  //   20100000 22100001 102020 20020022 c 22100002 102020 20020022 c 22100003 102020 20020022 c 22100004
  //   102020 20020022 c 22100005 102020 20020022 c 22100006 102020 20020022 c 22100007 102020 20020022 c
  //   22100008 102020 20020022 20020022 c 3e00008
  //   指令字
  //   OP
  //   Func
  //   rs
  //   rt
  //   rd
  //   流水调试日志用
  //   10#10 (exit)
  //   10#34 (print hex)
  //   JMP
  //   JR
  //   OP
  //   Func
  //   Beq
  //   Bne
  //   MemToReg
  //   MemWrite
  //   AluOP
  //   AluSrcB
  //   RegWrite
  //   JAL
  //   RegDst
  //   Syscall
  //   Syscall34
endmodule

module temp (
  input  jmp,
  input  jr,
  input  jal,
  input  beq,
  input  bne,
  input  bltz,
  output sel1,
  output sel0
);

  wire and_1_out, and_2_out, and_3_out, and_4_out, and_5_out, and_6_out, and_7_out, and_8_out, and_9_out,
       and_10_out, and_11_out, not_1_out, not_2_out, not_3_out, not_4_out, not_5_out, not_6_out, not_7_out,
       not_8_out, not_9_out, not_10_out, not_11_out, not_12_out, not_13_out, not_14_out, not_15_out,
       not_16_out, not_17_out, not_18_out, not_19_out, not_20_out, not_21_out;

  not not_1 (not_1_out, jmp);
  not not_2 (not_2_out, jr);
  not not_3 (not_3_out, jal);
  not not_4 (not_4_out, beq);
  not not_5 (not_5_out, bne);
  not not_6 (not_6_out, beq);
  not not_7 (not_7_out, bltz);
  not not_8 (not_8_out, bne);
  not not_9 (not_9_out, bltz);
  not not_10 (not_10_out, jr);
  not not_11 (not_11_out, beq);
  not not_12 (not_12_out, bltz);
  not not_13 (not_13_out, jmp);
  not not_14 (not_14_out, beq);
  not not_15 (not_15_out, bne);
  not not_16 (not_16_out, bltz);
  not not_17 (not_17_out, beq);
  not not_18 (not_18_out, bne);
  not not_19 (not_19_out, jr);
  not not_20 (not_20_out, beq);
  not not_21 (not_21_out, bne);
  and and_1 (and_1_out, not_1_out, not_2_out, not_3_out, not_4_out, not_5_out, bltz);
  and and_2 (and_2_out, not_6_out, bne, not_7_out);
  and and_3 (and_3_out, beq, not_8_out, not_9_out);
  and and_4 (and_4_out, jmp, not_10_out, not_11_out, not_12_out);
  and and_5 (and_5_out, not_13_out, not_14_out, not_15_out, not_16_out);
  and and_6 (and_6_out, bne, bltz);
  and and_7 (and_7_out, beq, bltz);
  and and_8 (and_8_out, beq, bne);
  and and_9 (and_9_out, jal, not_17_out, not_18_out);
  and and_10 (and_10_out, jr, bltz);
  and and_11 (and_11_out, jmp, not_19_out, not_20_out, not_21_out);
  or or_1 (sel1, and_1_out, and_2_out, and_3_out, and_4_out);
  or or_2 (sel0, and_5_out, and_6_out, and_7_out, and_8_out, and_9_out, and_10_out, and_11_out);
endmodule

module Redirect (
  input  R1_IDEX,
  input  R1_IDMEM,
  input  R2_IDEX,
  input  R2_IDMEM,
  input  [5:0] OP,
  input  [5:0] Func,
  input  [31:0] IR,
  output load_use,
  output [1:0] R1_sel,
  output [1:0] R2_sel
);

  wire comparator_1_eq, FromAlu, FromMem, or_1_out, R1_src1, R1_src2, R1_src3, R2_src1, R2_src2, R2_src3;

  RegDataFrom regdatafrom_1 (
    .OP0(OP[0]), .OP1(OP[1]), .OP2(OP[2]), .OP3(OP[3]), .OP4(OP[4]), .OP5(OP[5]), .F0(Func[0]), .F1(Func[1]),
    .F2(Func[2]), .F3(Func[3]), .F4(Func[4]), .F5(Func[5]), .FromAlu(FromAlu), .FromMem(FromMem));
  Comparator #(.width(6)) comparator_1 (.a(IR[31:26]), .b(6'b100011), .eq(comparator_1_eq));  // open: gt, lt
  or or_1 (or_1_out, R1_IDEX, R2_IDEX);
  and and_1 (load_use, comparator_1_eq, or_1_out);
  and and_2 (R1_src3, R1_IDEX, ~load_use);  // AND_Gate
  and and_3 (R1_src1, R1_IDMEM, FromAlu);
  and and_4 (R1_src2, R1_IDMEM, FromMem);
  and and_5 (R2_src3, R2_IDEX, ~load_use);  // AND_Gate
  and and_6 (R2_src1, R2_IDMEM, FromAlu);
  and and_7 (R2_src2, R2_IDMEM, FromMem);
  Priority_Encoder #(.select(2)) priority_encoder_1 (
    .in0(1'b1), .in1(R1_src1), .in2(R1_src2), .in3(R1_src3), .out(R1_sel));  // open: gs, en_out, en_in
  Priority_Encoder #(.select(2)) priority_encoder_2 (
    .in0(1'b1), .in1(R2_src1), .in2(R2_src2), .in3(R2_src3), .out(R2_sel));  // open: gs, en_out, en_in

  // Other names for the same wires on the sheet: OP_CODE[5:0] = OP
endmodule

module RegDataFrom (
  input  OP0,
  input  OP1,
  input  OP2,
  input  OP3,
  input  OP4,
  input  OP5,
  input  F0,
  input  F1,
  input  F2,
  input  F3,
  input  F4,
  input  F5,
  output FromAlu,
  output FromMem
);

  wire and_1_out, and_2_out, and_3_out, and_4_out, and_5_out, and_6_out, and_7_out, and_8_out, and_9_out,
       and_10_out, and_11_out, and_12_out, and_13_out, and_14_out, and_15_out, and_16_out, and_17_out,
       and_18_out, not_1_out, not_2_out, not_3_out, not_4_out, not_5_out, not_6_out, not_7_out, not_8_out,
       not_9_out, not_10_out, not_11_out, not_12_out, not_13_out, not_14_out, not_15_out, not_16_out,
       not_17_out, not_18_out, not_19_out, not_20_out, not_21_out, not_22_out, not_23_out, not_24_out,
       not_25_out, not_26_out, not_27_out, not_28_out, not_29_out, not_30_out, not_31_out, not_32_out,
       not_33_out, not_34_out, not_35_out, not_36_out, not_37_out, not_38_out, not_39_out, not_40_out,
       not_41_out, not_42_out, not_43_out, not_44_out, not_45_out, not_46_out, not_47_out, not_48_out,
       not_49_out, not_50_out, not_51_out, not_52_out, not_53_out, not_54_out, not_55_out, not_56_out,
       not_57_out, not_58_out, not_59_out, not_60_out, not_61_out, not_62_out, not_63_out, not_64_out,
       not_65_out, not_66_out, not_67_out, not_68_out, not_69_out, not_70_out, not_71_out, not_72_out,
       not_73_out, not_74_out, not_75_out, not_76_out, not_77_out, not_78_out, not_79_out, not_80_out,
       not_81_out, not_82_out, not_83_out, not_84_out, not_85_out, not_86_out, not_87_out, not_88_out,
       not_89_out, not_90_out, not_91_out, not_92_out, not_93_out, not_94_out, not_95_out, not_96_out,
       not_97_out, not_98_out, not_99_out, not_100_out, not_101_out, not_102_out, not_103_out, not_104_out,
       not_105_out, not_106_out, not_107_out, not_108_out, not_109_out, not_110_out, not_111_out,
       not_112_out, not_113_out, not_114_out, not_115_out, not_116_out, not_117_out, not_118_out,
       not_119_out, not_120_out, not_121_out, not_122_out, not_123_out, not_124_out, not_125_out,
       not_126_out, not_127_out, not_128_out, not_129_out, not_130_out, not_131_out, not_132_out,
       not_133_out, not_134_out, not_135_out, not_136_out, not_137_out, not_138_out, not_139_out,
       not_140_out, not_141_out, not_142_out, not_143_out, not_144_out, not_145_out, not_146_out,
       not_147_out, not_148_out, not_149_out, not_150_out;

  not not_1 (not_1_out, OP5);
  not not_2 (not_2_out, OP4);
  not not_3 (not_3_out, OP3);
  not not_4 (not_4_out, OP2);
  not not_5 (not_5_out, OP1);
  not not_6 (not_6_out, OP0);
  not not_7 (not_7_out, F5);
  not not_8 (not_8_out, F4);
  not not_9 (not_9_out, F3);
  not not_10 (not_10_out, F2);
  not not_11 (not_11_out, F1);
  not not_12 (not_12_out, F0);
  not not_13 (not_13_out, OP5);
  not not_14 (not_14_out, OP4);
  not not_15 (not_15_out, OP3);
  not not_16 (not_16_out, OP2);
  not not_17 (not_17_out, OP1);
  not not_18 (not_18_out, OP0);
  not not_19 (not_19_out, F5);
  not not_20 (not_20_out, F4);
  not not_21 (not_21_out, F3);
  not not_22 (not_22_out, F2);
  not not_23 (not_23_out, OP5);
  not not_24 (not_24_out, OP4);
  not not_25 (not_25_out, OP3);
  not not_26 (not_26_out, OP2);
  not not_27 (not_27_out, OP1);
  not not_28 (not_28_out, OP0);
  not not_29 (not_29_out, F5);
  not not_30 (not_30_out, F4);
  not not_31 (not_31_out, F3);
  not not_32 (not_32_out, F2);
  not not_33 (not_33_out, F0);
  not not_34 (not_34_out, OP5);
  not not_35 (not_35_out, OP4);
  not not_36 (not_36_out, OP3);
  not not_37 (not_37_out, OP2);
  not not_38 (not_38_out, OP1);
  not not_39 (not_39_out, OP0);
  not not_40 (not_40_out, F4);
  not not_41 (not_41_out, F3);
  not not_42 (not_42_out, F2);
  not not_43 (not_43_out, F1);
  not not_44 (not_44_out, F0);
  not not_45 (not_45_out, OP5);
  not not_46 (not_46_out, OP4);
  not not_47 (not_47_out, OP3);
  not not_48 (not_48_out, OP2);
  not not_49 (not_49_out, OP1);
  not not_50 (not_50_out, OP0);
  not not_51 (not_51_out, F4);
  not not_52 (not_52_out, F3);
  not not_53 (not_53_out, F2);
  not not_54 (not_54_out, F1);
  not not_55 (not_55_out, OP5);
  not not_56 (not_56_out, OP4);
  not not_57 (not_57_out, OP3);
  not not_58 (not_58_out, OP2);
  not not_59 (not_59_out, OP1);
  not not_60 (not_60_out, OP0);
  not not_61 (not_61_out, F4);
  not not_62 (not_62_out, F3);
  not not_63 (not_63_out, F2);
  not not_64 (not_64_out, F0);
  not not_65 (not_65_out, OP5);
  not not_66 (not_66_out, OP4);
  not not_67 (not_67_out, OP3);
  not not_68 (not_68_out, OP2);
  not not_69 (not_69_out, OP1);
  not not_70 (not_70_out, OP0);
  not not_71 (not_71_out, F4);
  not not_72 (not_72_out, F3);
  not not_73 (not_73_out, F1);
  not not_74 (not_74_out, F0);
  not not_75 (not_75_out, OP5);
  not not_76 (not_76_out, OP4);
  not not_77 (not_77_out, OP3);
  not not_78 (not_78_out, OP2);
  not not_79 (not_79_out, OP1);
  not not_80 (not_80_out, OP0);
  not not_81 (not_81_out, F4);
  not not_82 (not_82_out, F3);
  not not_83 (not_83_out, F1);
  not not_84 (not_84_out, OP5);
  not not_85 (not_85_out, OP4);
  not not_86 (not_86_out, OP3);
  not not_87 (not_87_out, OP2);
  not not_88 (not_88_out, OP1);
  not not_89 (not_89_out, OP0);
  not not_90 (not_90_out, F4);
  not not_91 (not_91_out, F3);
  not not_92 (not_92_out, OP5);
  not not_93 (not_93_out, OP4);
  not not_94 (not_94_out, OP3);
  not not_95 (not_95_out, OP2);
  not not_96 (not_96_out, OP1);
  not not_97 (not_97_out, OP0);
  not not_98 (not_98_out, F4);
  not not_99 (not_99_out, F2);
  not not_100 (not_100_out, F0);
  not not_101 (not_101_out, OP5);
  not not_102 (not_102_out, OP4);
  not not_103 (not_103_out, OP3);
  not not_104 (not_104_out, OP2);
  not not_105 (not_105_out, OP1);
  not not_106 (not_106_out, OP0);
  not not_107 (not_107_out, F4);
  not not_108 (not_108_out, F2);
  not not_109 (not_109_out, OP5);
  not not_110 (not_110_out, OP4);
  not not_111 (not_111_out, OP2);
  not not_112 (not_112_out, OP1);
  not not_113 (not_113_out, OP0);
  not not_114 (not_114_out, OP5);
  not not_115 (not_115_out, OP4);
  not not_116 (not_116_out, OP1);
  not not_117 (not_117_out, OP0);
  not not_118 (not_118_out, OP5);
  not not_119 (not_119_out, OP4);
  not not_120 (not_120_out, OP2);
  not not_121 (not_121_out, OP1);
  not not_122 (not_122_out, OP5);
  not not_123 (not_123_out, OP4);
  not not_124 (not_124_out, OP2);
  not not_125 (not_125_out, OP0);
  not not_126 (not_126_out, OP5);
  not not_127 (not_127_out, OP4);
  not not_128 (not_128_out, OP1);
  not not_129 (not_129_out, OP5);
  not not_130 (not_130_out, OP4);
  not not_131 (not_131_out, OP3);
  not not_132 (not_132_out, OP2);
  not not_133 (not_133_out, OP1);
  not not_134 (not_134_out, OP0);
  not not_135 (not_135_out, F5);
  not not_136 (not_136_out, F4);
  not not_137 (not_137_out, F3);
  not not_138 (not_138_out, F0);
  not not_139 (not_139_out, OP5);
  not not_140 (not_140_out, OP4);
  not not_141 (not_141_out, OP3);
  not not_142 (not_142_out, OP2);
  not not_143 (not_143_out, OP1);
  not not_144 (not_144_out, OP0);
  not not_145 (not_145_out, F5);
  not not_146 (not_146_out, F4);
  not not_147 (not_147_out, F3);
  not not_148 (not_148_out, OP4);
  not not_149 (not_149_out, OP3);
  not not_150 (not_150_out, OP2);
  and and_1 (and_1_out, not_1_out, not_2_out, not_3_out, not_4_out, not_5_out, not_6_out, not_7_out, not_8_out, not_9_out, not_10_out, not_11_out, not_12_out);
  and and_2 (and_2_out, not_13_out, not_14_out, not_15_out, not_16_out, not_17_out, not_18_out, not_19_out, not_20_out, not_21_out, not_22_out, F1, F0);
  and and_3 (and_3_out, not_23_out, not_24_out, not_25_out, not_26_out, not_27_out, not_28_out, not_29_out, not_30_out, not_31_out, not_32_out, F1, not_33_out);
  and and_4 (and_4_out, not_34_out, not_35_out, not_36_out, not_37_out, not_38_out, not_39_out, F5, not_40_out, not_41_out, not_42_out, not_43_out, not_44_out);
  and and_5 (and_5_out, not_45_out, not_46_out, not_47_out, not_48_out, not_49_out, not_50_out, F5, not_51_out, not_52_out, not_53_out, not_54_out, F0);
  and and_6 (and_6_out, not_55_out, not_56_out, not_57_out, not_58_out, not_59_out, not_60_out, F5, not_61_out, not_62_out, not_63_out, F1, not_64_out);
  and and_7 (and_7_out, not_65_out, not_66_out, not_67_out, not_68_out, not_69_out, not_70_out, F5, not_71_out, not_72_out, F2, not_73_out, not_74_out);
  and and_8 (and_8_out, not_75_out, not_76_out, not_77_out, not_78_out, not_79_out, not_80_out, F5, not_81_out, not_82_out, F2, not_83_out, F0);
  and and_9 (and_9_out, not_84_out, not_85_out, not_86_out, not_87_out, not_88_out, not_89_out, F5, not_90_out, not_91_out, F2, F1, F0);
  and and_10 (and_10_out, not_92_out, not_93_out, not_94_out, not_95_out, not_96_out, not_97_out, F5, not_98_out, F3, not_99_out, F1, not_100_out);
  and and_11 (and_11_out, not_101_out, not_102_out, not_103_out, not_104_out, not_105_out, not_106_out, F5, not_107_out, F3, not_108_out, F1, F0);
  and and_12 (and_12_out, not_109_out, not_110_out, OP3, not_111_out, not_112_out, not_113_out);
  and and_13 (and_13_out, not_114_out, not_115_out, OP3, OP2, not_116_out, not_117_out);
  and and_14 (and_14_out, not_118_out, not_119_out, OP3, not_120_out, not_121_out, OP0);
  and and_15 (and_15_out, not_122_out, not_123_out, OP3, not_124_out, OP1, not_125_out);
  and and_16 (and_16_out, not_126_out, not_127_out, OP3, OP2, not_128_out, OP0);
  and and_17 (and_17_out, not_129_out, not_130_out, not_131_out, not_132_out, not_133_out, not_134_out, not_135_out, not_136_out, not_137_out, F2, F1, not_138_out);
  and and_18 (and_18_out, not_139_out, not_140_out, not_141_out, not_142_out, not_143_out, not_144_out, not_145_out, not_146_out, not_147_out, F2, F1, F0);
  and and_19 (FromMem, OP5, not_148_out, not_149_out, not_150_out, OP1, OP0);
  or or_1 (FromAlu, and_1_out, and_2_out, and_3_out, and_4_out, and_5_out, and_6_out, and_7_out, and_8_out, and_9_out, and_10_out, and_11_out, and_12_out, and_13_out, and_14_out, and_15_out, and_16_out, and_17_out, and_18_out);
endmodule

module BHT (
  input  Clk,
  input  write_valid,
  input  we_valid,
  input  we_pc,
  input  [31:0] write_pc,
  input  we_branch,
  input  [31:0] cur_pc,
  input  we_predict,
  input  [31:0] write_branch,
  input  we_lru,
  input  [1:0] write_predict,
  input  [2:0] write_address,
  output Hit,
  output [2:0] HitNum,
  output [31:0] BranchAddr,
  output [2:0] InsertNum,
  output [1:0] predict
);

  wire and_1_out, and_2_out, and_3_out, and_4_out, and_5_out, and_6_out, and_7_out, and_8_out, and_9_out,
       and_10_out, and_11_out, and_12_out, and_13_out, and_14_out, and_15_out, and_16_out, and_17_out,
       and_18_out, and_19_out, and_20_out, and_21_out, and_22_out, and_23_out, and_24_out, and_25_out,
       and_26_out, and_27_out, and_28_out, and_29_out, and_30_out, and_31_out, and_32_out, and_33_out,
       and_34_out, and_35_out, and_36_out, and_37_out, and_38_out, and_39_out, and_40_out, and_41_out,
       and_42_out, and_43_out, and_44_out, and_45_out, and_46_out, and_47_out, and_48_out, comparator_1_lt,
       comparator_2_lt, comparator_3_lt, comparator_4_lt, comparator_5_lt, comparator_6_lt, comparator_8_eq,
       comparator_9_eq, comparator_10_eq, comparator_11_eq, comparator_12_eq, comparator_13_eq,
       comparator_14_eq, comparator_15_eq, decoder_1_out0, decoder_1_out1, decoder_1_out2, decoder_1_out3,
       decoder_1_out4, decoder_1_out5, decoder_1_out6, decoder_1_out7, multiplexer_6_out, multiplexer_8_out,
       register_1_q, register_2_q, register_3_q, register_4_q, register_5_q, register_6_q, register_7_q,
       register_8_q, we_lru_t;
  wire [1:0] predict0, predict1, predict2, predict3, predict4, predict5, predict6, predict7, undriven_3;
  wire [2:0] priority_encoder_1_out;
  wire [12:0] lru0, lru1, lru2, lru3, lru4, lru5, lru6, lru7, multiplexer_1_out, multiplexer_2_out,
       multiplexer_3_out, multiplexer_4_out, multiplexer_5_out, multiplexer_7_out;
  wire [31:0] register_9_q, register_10_q, register_11_q, register_12_q, register_13_q, register_14_q,
       register_15_q, register_16_q, register_17_q, register_18_q, register_19_q, register_20_q,
       register_21_q, register_22_q, register_23_q, register_24_q, undriven, undriven_2;

  Decoder #(.select(3), .disabled(0), .enable("false")) decoder_1 (
    .out0(decoder_1_out0), .out1(decoder_1_out1), .out2(decoder_1_out2), .out3(decoder_1_out3),
    .out4(decoder_1_out4), .out5(decoder_1_out5), .out6(decoder_1_out6), .out7(decoder_1_out7),
    .sel(write_address));
  and and_1 (and_1_out, we_valid, decoder_1_out0);
  and and_2 (and_2_out, we_valid, decoder_1_out1);
  and and_3 (and_3_out, we_valid, decoder_1_out2);
  and and_4 (and_4_out, we_valid, decoder_1_out3);
  and and_5 (and_5_out, we_valid, decoder_1_out4);
  and and_6 (and_6_out, we_valid, decoder_1_out5);
  and and_7 (and_7_out, we_valid, decoder_1_out6);
  and and_8 (and_8_out, we_valid, decoder_1_out7);
  Comparator #(.width(13), .mode("unsigned")) comparator_1 (.a(lru0), .b(lru1), .lt(comparator_1_lt));  // open: gt, eq
  Comparator #(.width(13), .mode("unsigned")) comparator_2 (.a(lru2), .b(lru3), .lt(comparator_2_lt));  // open: gt, eq
  Comparator #(.width(13), .mode("unsigned")) comparator_3 (.a(lru4), .b(lru5), .lt(comparator_3_lt));  // open: gt, eq
  Comparator #(.width(13), .mode("unsigned")) comparator_4 (.a(lru6), .b(lru7), .lt(comparator_4_lt));  // open: gt, eq
  and and_9 (and_9_out, we_pc, decoder_1_out0);
  and and_10 (and_10_out, we_branch, decoder_1_out0);
  and and_11 (and_11_out, we_pc, decoder_1_out1);
  and and_12 (and_12_out, we_branch, decoder_1_out1);
  and and_13 (and_13_out, we_pc, decoder_1_out2);
  and and_14 (and_14_out, we_branch, decoder_1_out2);
  and and_15 (and_15_out, we_pc, decoder_1_out3);
  and and_16 (and_16_out, we_branch, decoder_1_out3);
  and and_17 (and_17_out, we_pc, decoder_1_out4);
  and and_18 (and_18_out, we_branch, decoder_1_out4);
  and and_19 (and_19_out, we_pc, decoder_1_out5);
  and and_20 (and_20_out, we_branch, decoder_1_out5);
  and and_21 (and_21_out, we_pc, decoder_1_out6);
  and and_22 (and_22_out, we_branch, decoder_1_out6);
  and and_23 (and_23_out, we_pc, decoder_1_out7);
  and and_24 (and_24_out, we_branch, decoder_1_out7);
  Multiplexer #(.width(13), .enable("false")) multiplexer_1 (
    .in0(lru0), .in1(lru1), .out(multiplexer_1_out), .sel(comparator_1_lt));
  Multiplexer #(.width(13), .enable("false")) multiplexer_2 (
    .in0(lru2), .in1(lru3), .out(multiplexer_2_out), .sel(comparator_2_lt));
  Multiplexer #(.width(13), .enable("false")) multiplexer_3 (
    .in0(lru4), .in1(lru5), .out(multiplexer_3_out), .sel(comparator_3_lt));
  Multiplexer #(.width(13), .enable("false")) multiplexer_4 (
    .in0(lru6), .in1(lru7), .out(multiplexer_4_out), .sel(comparator_4_lt));
  and and_25 (and_25_out, we_predict, decoder_1_out0);
  and and_26 (and_26_out, we_predict, decoder_1_out1);
  and and_27 (and_27_out, we_predict, decoder_1_out2);
  and and_28 (and_28_out, we_predict, decoder_1_out3);
  and and_29 (and_29_out, we_predict, decoder_1_out4);
  and and_30 (and_30_out, we_predict, decoder_1_out5);
  and and_31 (and_31_out, we_predict, decoder_1_out6);
  and and_32 (and_32_out, we_predict, decoder_1_out7);
  and and_33 (and_33_out, we_lru_t, decoder_1_out0);
  and and_34 (and_34_out, we_lru_t, decoder_1_out1);
  and and_35 (and_35_out, we_lru_t, decoder_1_out2);
  and and_36 (and_36_out, we_lru_t, decoder_1_out3);
  and and_37 (and_37_out, we_lru_t, decoder_1_out4);
  and and_38 (and_38_out, we_lru_t, decoder_1_out5);
  and and_39 (and_39_out, we_lru_t, decoder_1_out6);
  and and_40 (and_40_out, we_lru_t, decoder_1_out7);
  Comparator #(.width(13), .mode("unsigned")) comparator_5 (
    .a(multiplexer_1_out), .b(multiplexer_2_out), .lt(comparator_5_lt));  // open: gt, eq
  Comparator #(.width(13), .mode("unsigned")) comparator_6 (
    .a(multiplexer_3_out), .b(multiplexer_4_out), .lt(comparator_6_lt));  // open: gt, eq
  D_Flip_Flop d_ff_1 (.clk(Clk), .D(we_lru), .Q(we_lru_t), .reset(we_lru_t));  // open: Qn, preset, en
  Multiplexer #(.width(13), .enable("false")) multiplexer_5 (
    .in0(multiplexer_1_out), .in1(multiplexer_2_out), .out(multiplexer_5_out), .sel(comparator_5_lt));
  Multiplexer #(.enable("false")) multiplexer_6 (
    .in0(comparator_1_lt), .in1(comparator_2_lt), .out(multiplexer_6_out), .sel(comparator_5_lt));
  Multiplexer #(.width(13), .enable("false")) multiplexer_7 (
    .in0(multiplexer_3_out), .in1(multiplexer_4_out), .out(multiplexer_7_out), .sel(comparator_6_lt));
  Multiplexer #(.enable("false")) multiplexer_8 (
    .in0(comparator_3_lt), .in1(comparator_4_lt), .out(multiplexer_8_out), .sel(comparator_6_lt));
  Register #(.width(1)) register_1 (.D(write_valid), .en(and_1_out), .Q(register_1_q), .clk(Clk), .clr(1'b0));
  Register #(.width(1)) register_2 (.D(write_valid), .en(and_2_out), .Q(register_2_q), .clk(Clk), .clr(1'b0));
  Register #(.width(1)) register_3 (.D(write_valid), .en(and_3_out), .Q(register_3_q), .clk(Clk), .clr(1'b0));
  Register #(.width(1)) register_4 (.D(write_valid), .en(and_4_out), .Q(register_4_q), .clk(Clk), .clr(1'b0));
  Register #(.width(1)) register_5 (.D(write_valid), .en(and_5_out), .Q(register_5_q), .clk(Clk), .clr(1'b0));
  Register #(.width(1)) register_6 (.D(write_valid), .en(and_6_out), .Q(register_6_q), .clk(Clk), .clr(1'b0));
  Register #(.width(1)) register_7 (.D(write_valid), .en(and_7_out), .Q(register_7_q), .clk(Clk), .clr(1'b0));
  Register #(.width(1)) register_8 (.D(write_valid), .en(and_8_out), .Q(register_8_q), .clk(Clk), .clr(1'b0));
  Comparator #(.width(13), .mode("unsigned")) comparator_7 (
    .a(multiplexer_5_out), .b(multiplexer_7_out), .lt(InsertNum[2]));  // open: gt, eq
  Register #(.width(32)) register_9 (.D(write_pc), .en(and_9_out), .Q(register_9_q), .clk(Clk), .clr(1'b0));
  Register #(.width(32)) register_10 (.D(write_pc), .en(and_11_out), .Q(register_10_q), .clk(Clk), .clr(1'b0));
  Register #(.width(32)) register_11 (.D(write_pc), .en(and_13_out), .Q(register_11_q), .clk(Clk), .clr(1'b0));
  Register #(.width(32)) register_12 (.D(write_pc), .en(and_15_out), .Q(register_12_q), .clk(Clk), .clr(1'b0));
  Register #(.width(32)) register_13 (.D(write_pc), .en(and_17_out), .Q(register_13_q), .clk(Clk), .clr(1'b0));
  Register #(.width(32)) register_14 (.D(write_pc), .en(and_19_out), .Q(register_14_q), .clk(Clk), .clr(1'b0));
  Register #(.width(32)) register_15 (.D(undriven), .en(and_21_out), .Q(register_15_q), .clk(Clk), .clr(1'b0));
  Register #(.width(32)) register_16 (.D(undriven), .en(and_23_out), .Q(register_16_q), .clk(Clk), .clr(1'b0));
  Multiplexer #(.enable("false")) multiplexer_9 (
    .in0(comparator_5_lt), .in1(comparator_6_lt), .out(InsertNum[1]), .sel(InsertNum[2]));
  Multiplexer #(.enable("false")) multiplexer_10 (
    .in0(multiplexer_6_out), .in1(multiplexer_8_out), .out(InsertNum[0]), .sel(InsertNum[2]));
  Register #(.width(32)) register_17 (.D(write_branch), .en(and_10_out), .Q(register_17_q), .clk(Clk), .clr(1'b0));
  Register #(.width(32)) register_18 (.D(write_branch), .en(and_12_out), .Q(register_18_q), .clk(Clk), .clr(1'b0));
  Register #(.width(32)) register_19 (.D(write_branch), .en(and_14_out), .Q(register_19_q), .clk(Clk), .clr(1'b0));
  Register #(.width(32)) register_20 (.D(write_branch), .en(and_16_out), .Q(register_20_q), .clk(Clk), .clr(1'b0));
  Register #(.width(32)) register_21 (.D(write_branch), .en(and_18_out), .Q(register_21_q), .clk(Clk), .clr(1'b0));
  Register #(.width(32)) register_22 (.D(write_branch), .en(and_20_out), .Q(register_22_q), .clk(Clk), .clr(1'b0));
  Register #(.width(32)) register_23 (.D(undriven_2), .en(and_22_out), .Q(register_23_q), .clk(Clk), .clr(1'b0));
  Register #(.width(32)) register_24 (.D(undriven_2), .en(and_24_out), .Q(register_24_q), .clk(Clk), .clr(1'b0));
  Register #(.width(2)) register_25 (.D(write_predict), .en(and_25_out), .Q(predict0), .clk(Clk), .clr(1'b0));
  Register #(.width(2)) register_26 (.D(write_predict), .en(and_26_out), .Q(predict1), .clk(Clk), .clr(1'b0));
  Register #(.width(2)) register_27 (.D(write_predict), .en(and_27_out), .Q(predict2), .clk(Clk), .clr(1'b0));
  Register #(.width(2)) register_28 (.D(write_predict), .en(and_28_out), .Q(predict3), .clk(Clk), .clr(1'b0));
  Register #(.width(2)) register_29 (.D(write_predict), .en(and_29_out), .Q(predict4), .clk(Clk), .clr(1'b0));
  Register #(.width(2)) register_30 (.D(write_predict), .en(and_30_out), .Q(predict5), .clk(Clk), .clr(1'b0));
  Register #(.width(2)) register_31 (.D(undriven_3), .en(and_31_out), .Q(predict6), .clk(Clk), .clr(1'b0));
  Register #(.width(2)) register_32 (.D(undriven_3), .en(and_32_out), .Q(predict7), .clk(Clk), .clr(1'b0));
  Counter #(.width(13), .max('h1fff)) counter_1 (.Q(lru0), .clk(Clk), .clr(and_33_out));  // open: load, D, count, carry
  Counter #(.width(13), .max('h1fff)) counter_2 (.Q(lru1), .clk(Clk), .clr(and_34_out));  // open: load, D, count, carry
  Counter #(.width(13), .max('h1fff)) counter_3 (.Q(lru2), .clk(Clk), .clr(and_35_out));  // open: load, D, count, carry
  Counter #(.width(13), .max('h1fff)) counter_4 (.Q(lru3), .clk(Clk), .clr(and_36_out));  // open: load, D, count, carry
  Counter #(.width(13), .max('h1fff)) counter_5 (.Q(lru4), .clk(Clk), .clr(and_37_out));  // open: load, D, count, carry
  Counter #(.width(13), .max('h1fff)) counter_6 (.Q(lru5), .clk(Clk), .clr(and_38_out));  // open: load, D, count, carry
  Counter #(.width(13), .max('h1fff)) counter_7 (.Q(lru6), .clk(Clk), .clr(and_39_out));  // open: load, D, count, carry
  Counter #(.width(13), .max('h1fff)) counter_8 (.Q(lru7), .clk(Clk), .clr(and_40_out));  // open: load, D, count, carry
  Comparator #(.width(32), .mode("unsigned")) comparator_8 (
    .a(cur_pc), .b(register_9_q), .eq(comparator_8_eq));  // open: gt, lt
  Comparator #(.width(32), .mode("unsigned")) comparator_9 (
    .a(cur_pc), .b(register_10_q), .eq(comparator_9_eq));  // open: gt, lt
  Comparator #(.width(32), .mode("unsigned")) comparator_10 (
    .a(cur_pc), .b(register_11_q), .eq(comparator_10_eq));  // open: gt, lt
  Comparator #(.width(32), .mode("unsigned")) comparator_11 (
    .a(cur_pc), .b(register_12_q), .eq(comparator_11_eq));  // open: gt, lt
  Comparator #(.width(32), .mode("unsigned")) comparator_12 (
    .a(cur_pc), .b(register_13_q), .eq(comparator_12_eq));  // open: gt, lt
  Comparator #(.width(32), .mode("unsigned")) comparator_13 (
    .a(cur_pc), .b(register_14_q), .eq(comparator_13_eq));  // open: gt, lt
  Comparator #(.width(32), .mode("unsigned")) comparator_14 (
    .a(cur_pc), .b(register_15_q), .eq(comparator_14_eq));  // open: gt, lt
  Comparator #(.width(32), .mode("unsigned")) comparator_15 (
    .a(cur_pc), .b(register_16_q), .eq(comparator_15_eq));  // open: gt, lt
  and and_41 (and_41_out, register_1_q, comparator_8_eq);
  and and_42 (and_42_out, register_2_q, comparator_9_eq);
  and and_43 (and_43_out, register_3_q, comparator_10_eq);
  and and_44 (and_44_out, register_4_q, comparator_11_eq);
  and and_45 (and_45_out, register_5_q, comparator_12_eq);
  and and_46 (and_46_out, register_6_q, comparator_13_eq);
  and and_47 (and_47_out, register_7_q, comparator_14_eq);
  and and_48 (and_48_out, register_8_q, comparator_15_eq);
  Priority_Encoder priority_encoder_1 (
    .in0(and_41_out), .in1(and_42_out), .in2(and_43_out), .in3(and_44_out), .in4(and_45_out),
    .in5(and_46_out), .in6(and_47_out), .in7(and_48_out), .out(priority_encoder_1_out), .gs(Hit));  // open: en_in, en_out
  Multiplexer #(.select(3), .width(2), .disabled(0)) multiplexer_11 (
    .in0(predict0), .in1(predict1), .in2(predict2), .in3(predict3), .in4(predict4), .in5(predict5),
    .in6(predict6), .in7(predict7), .out(predict), .sel(priority_encoder_1_out), .en(Hit));
  Multiplexer #(.width(3), .disabled(0), .enable("false")) multiplexer_12 (
    .in0(3'b000), .in1(priority_encoder_1_out), .out(HitNum), .sel(Hit));
  Multiplexer #(.select(3), .width(32), .disabled(0)) multiplexer_13 (
    .in0(register_17_q), .in1(register_18_q), .in2(register_19_q), .in3(register_20_q), .in4(register_21_q),
    .in5(register_22_q), .in6(register_23_q), .in7(register_24_q), .out(BranchAddr),
    .sel(priority_encoder_1_out), .en(Hit));
endmodule
